// Logisim project control_logic_unit.circ as structural Verilog: 19 circuits, main circuit main
module main (
  input  [7:0] in_1,
  input  in_2,
  input  in_3,
  input  in_4,
  input  in_5,
  input  in_6,
  output out_7
);

  wire any_low_cycle, CLOCK0, fetch_clock, inv_CLOCK, inv_condition_true, inv_enable_wr_addr,
       inv_fetch_clock, inv_fetch_cycle, inv_high_cycle, inv_low_cycle, inv_reset_high_cycle,
       inv_reset_low_cycle, inv_reset_sync, inv_select_opcode_0, inv_select_opcode_1, inv_select_opcode_2,
       inv_select_opcode_3, inv_select_opcode_4, inv_select_opcode_5, inv_select_opcode_6,
       inv_select_opcode_7, inv_select_opcode_int, inv_select_opcode_reset, inv_UC_break,
       inv_UC_clear_cond_reg, inv_UC_clear_interrupt_mask, inv_UC_extended_opcode, inv_UC_halt,
       inv_UC_int_ready, inv_UC_pcia_swap, inv_UC_pclr_swap, inv_UC_read_addr_src_reg, inv_UC_read_mem_const,
       inv_UC_restart_cycle, inv_UC_save_cond_reg, inv_UC_save_src_reg, inv_UC_set_interrupt_mask,
       inv_UC_ula_enable, inv_UC_write_address, inv_UC_write_enable, read_mem_const, RESET, ULA_ENABLE,
       WRITE_ENABLE, write_to_pc;
  wire [4:0] RD_ADDR, WR_ADDR;
  wire [7:0] INS;
  wire [15:0] ADDR;

  Hex_Digit_Display hex_digit_display_1 (.value(INS[7:4]));  // open: dp
  Hex_Digit_Display hex_digit_display_2 (.value(INS[3:0]));  // open: dp
  not not_1 (inv_CLOCK, CLOCK0);
  Pull_Resistor #(.pull(1)) pull_resistor_1 (.node(ADDR[0]));
  Pull_Resistor #(.pull(1)) pull_resistor_2 (.node(ADDR[1]));
  not not_2 (write_to_pc, inv_UC_write_address);
  or or_1 (inv_fetch_clock, inv_CLOCK, inv_fetch_cycle);
  not not_3 (fetch_clock, inv_fetch_clock);
  not not_4 (read_mem_const, inv_UC_read_mem_const);
  Pull_Resistor #(.pull(1)) pull_resistor_3 (.node(ADDR[2]));
  Pull_Resistor #(.pull(1)) pull_resistor_4 (.node(ADDR[3]));
  Pull_Resistor #(.pull(1)) pull_resistor_5 (.node(ADDR[4]));
  Pull_Resistor #(.pull(1)) pull_resistor_6 (.node(ADDR[5]));
  LED #(.active("false")) led_1 (.in(inv_fetch_cycle));
  LED #(.active("false")) led_2 (.in(inv_low_cycle));
  LED #(.active("false")) led_3 (.in(inv_high_cycle));
  Pull_Resistor #(.pull(1)) pull_resistor_7 (.node(ADDR[6]));
  Pull_Resistor #(.pull(1)) pull_resistor_8 (.node(ADDR[7]));
  Pull_Resistor #(.pull(1)) pull_resistor_9 (.node(ADDR[8]));
  Pull_Resistor #(.pull(1)) pull_resistor_10 (.node(ADDR[9]));
  Button button_1 (.out(RESET));
  Clock clock_1 (.out(CLOCK0));
  Pull_Resistor #(.pull(1)) pull_resistor_11 (.node(ADDR[10]));
  Pull_Resistor #(.pull(1)) pull_resistor_12 (.node(ADDR[11]));
  Pull_Resistor #(.pull(1)) pull_resistor_13 (.node(ADDR[12]));
  Pull_Resistor #(.pull(1)) pull_resistor_14 (.node(ADDR[13]));
  sequenciador sequenciador_1 (
    .RESET(RESET), .nUC_halt(inv_UC_halt), .nCLOCK(inv_CLOCK), .nUC_restart_cycle(inv_UC_restart_cycle),
    .any_low_cycle(any_low_cycle), .nreset_sync(inv_reset_sync), .nreset_low_cycle(inv_reset_low_cycle),
    .nreset_high_cycle(inv_reset_high_cycle), .nfetch_cycle(inv_fetch_cycle), .nlow_cycle(inv_low_cycle),
    .nhigh_cycle(inv_high_cycle), .nselect_opcode_reset(inv_select_opcode_reset),
    .out_restart_cycle(inv_UC_restart_cycle));
  avaliador_condicao avaliador_condicao_1 (
    .ZERO_FLAG(in_3), .CARRY_FLAG(in_4), .nclear_cond_reg(inv_UC_clear_cond_reg), .OVERFLOW_FLAG(in_5),
    .nsave_cond_reg(inv_UC_save_cond_reg), .NEGATIVE_FLAG(in_6), .nwrite_enable(inv_UC_write_enable),
    .nula_enable(inv_UC_ula_enable), .INS(INS), .ncondition_true(inv_condition_true),
    .WRITE_ENABLE(WRITE_ENABLE), .ULA_ENABLE(ULA_ENABLE), .nenable_wr_addr(inv_enable_wr_addr));
  Pull_Resistor #(.pull(1)) pull_resistor_15 (.node(ADDR[14]));
  Pull_Resistor #(.pull(1)) pull_resistor_16 (.node(ADDR[15]));
  LED led_4 (.in(WRITE_ENABLE));
  LED led_5 (.in(ULA_ENABLE));
  Hex_Digit_Display hex_digit_display_3 (.value({3'b000, RD_ADDR[4]}));  // open: dp
  Hex_Digit_Display hex_digit_display_4 (.value(RD_ADDR[3:0]));  // open: dp
  Hex_Digit_Display hex_digit_display_5 (.value({3'b000, WR_ADDR[4]}));  // open: dp
  Hex_Digit_Display hex_digit_display_6 (.value(WR_ADDR[3:0]));  // open: dp
  read_from read_from_1 (
    .read_addr_src_reg(inv_UC_read_addr_src_reg), .any_low_cycle(any_low_cycle), .INS(INS),
    .save_src_reg(inv_UC_save_src_reg), .read_mem_const(inv_UC_read_mem_const),
    .nfetch_cycle(inv_fetch_cycle), .RD_ADDR(RD_ADDR));
  write_to write_to_1 (
    .nwrite_pc(inv_UC_write_address), .nenable_wr_addr(inv_enable_wr_addr), .INS(INS),
    .any_low_cycle(any_low_cycle), .nlow_cycle(inv_low_cycle), .WR_ADDR(WR_ADDR));
  address_constant address_constant_1 (
    .nread_mem_const(inv_UC_read_mem_const), .any_low_cycle(any_low_cycle),
    .nselect_opcode_int(inv_select_opcode_int), .ADDR(ADDR));
  Hex_Digit_Display hex_digit_display_7 (.value(ADDR[15:12]));  // open: dp
  Hex_Digit_Display hex_digit_display_8 (.value(ADDR[11:8]));  // open: dp
  Hex_Digit_Display hex_digit_display_9 (.value(ADDR[7:4]));  // open: dp
  Hex_Digit_Display hex_digit_display_10 (.value(ADDR[3:0]));  // open: dp
  extended_code extended_code_1 (
    .extended_opcode(inv_UC_extended_opcode), .INS(INS), .set_interrupt_mask(inv_UC_set_interrupt_mask),
    .clear_interrupt_mask(inv_UC_clear_interrupt_mask), .halt(inv_UC_halt), .\break (inv_UC_break),
    .pclr_swap(inv_UC_pclr_swap));
  decodificador decodificador_1 (
    .clear_interrupt_mask(inv_UC_clear_interrupt_mask), .INT_REQUEST(in_2),
    .set_interrupt_mask(inv_UC_set_interrupt_mask), .DATA(in_1), .restart_cycle(inv_UC_restart_cycle),
    .int_ready(inv_UC_int_ready), .fetch_clock(fetch_clock), .nfetch_cycle(inv_fetch_cycle),
    .nselect_opcode_reset(inv_select_opcode_reset),
    .select_opcode({inv_select_opcode_int, inv_select_opcode_7, inv_select_opcode_6, inv_select_opcode_5, inv_select_opcode_4, inv_select_opcode_3, inv_select_opcode_2, inv_select_opcode_1, inv_select_opcode_0}),
    .INS(INS), .INT_MASK_FLAG(out_7));
  ucode_0 ucode_0_1 (
    .nfetch_cycle(inv_fetch_clock), .nlow_cycle(inv_low_cycle), .mhigh_cycle(inv_high_cycle),
    .nselect_opcode(inv_select_opcode_0), .read_addr_src_reg(inv_UC_read_addr_src_reg),
    .int_ready(inv_UC_int_ready), .write_address(inv_UC_write_address), .restart_cycle(inv_UC_restart_cycle),
    .ula_enable(inv_UC_ula_enable), .write_enable(inv_UC_write_enable), .save_cond_reg(inv_UC_save_cond_reg),
    .clear_cond_reg(inv_UC_clear_cond_reg), .read_mem_const(inv_UC_read_mem_const),
    .pcia_swap(inv_UC_pcia_swap), .save_src_reg(inv_UC_save_src_reg), .extended_opcode(inv_UC_extended_opcode));  // open: UC_B, UC_A
  ucode_1 ucode_1_1 (
    .nfetch_cycle(inv_fetch_clock), .nlow_cycle(inv_low_cycle), .nhigh_cycle(inv_high_cycle),
    .nselect_opcode(inv_select_opcode_1), .read_addr_src_reg(inv_UC_read_addr_src_reg),
    .int_ready(inv_UC_int_ready), .write_address(inv_UC_write_address), .restart_cycle(inv_UC_restart_cycle),
    .ula_enable(inv_UC_ula_enable), .write_enable(inv_UC_write_enable), .save_cond_reg(inv_UC_save_cond_reg),
    .clear_cond_reg(inv_UC_clear_cond_reg), .read_mem_const(inv_UC_read_mem_const),
    .pcia_swap(inv_UC_pcia_swap), .save_src_reg(inv_UC_save_src_reg), .extended_opcode(inv_UC_extended_opcode));  // open: UC_B, UC_A
  ucode_2 ucode_2_1 (
    .nfetch_cycle(inv_fetch_clock), .nlow_cycle(inv_low_cycle), .nhigh_cycle(inv_high_cycle),
    .nselect_opcode(inv_select_opcode_2), .read_addr_src_reg(inv_UC_read_addr_src_reg),
    .int_ready(inv_UC_int_ready), .write_address(inv_UC_write_address), .restart_cycle(inv_UC_restart_cycle),
    .ula_enable(inv_UC_ula_enable), .write_enable(inv_UC_write_enable), .save_cond_reg(inv_UC_save_cond_reg),
    .clear_cond_reg(inv_UC_clear_cond_reg), .read_mem_const(inv_UC_read_mem_const),
    .pcia_swap(inv_UC_pcia_swap), .save_src_reg(inv_UC_save_src_reg), .extended_opcode(inv_UC_extended_opcode));  // open: UC_B, UC_A
  ucode_3 ucode_3_1 (
    .nfetch_cycle(inv_fetch_clock), .nlow_cycle(inv_low_cycle), .nhigh_cycle(inv_high_cycle),
    .nselect_opcode(inv_select_opcode_3), .read_addr_src_reg(inv_UC_read_addr_src_reg),
    .int_ready(inv_UC_int_ready), .write_address(inv_UC_write_address), .restart_cycle(inv_UC_restart_cycle),
    .ula_enable(inv_UC_ula_enable), .write_enable(inv_UC_write_enable), .save_cond_reg(inv_UC_save_cond_reg),
    .clear_cond_reg(inv_UC_clear_cond_reg), .read_mem_const(inv_UC_read_mem_const),
    .pcia_swap(inv_UC_pcia_swap), .save_src_reg(inv_UC_save_src_reg), .extended_opcode(inv_UC_extended_opcode));  // open: UC_B, UC_A
  ucode_4 ucode_4_1 (
    .nfetch_cycle(inv_fetch_clock), .nlow_cycle(inv_low_cycle), .nhigh_cycle(inv_high_cycle),
    .nselect_opcode(inv_select_opcode_4), .read_addr_src_reg(inv_UC_read_addr_src_reg),
    .int_ready(inv_UC_int_ready), .write_address(inv_UC_write_address), .restart_cycle(inv_UC_restart_cycle),
    .ula_enable(inv_UC_ula_enable), .write_enable(inv_UC_write_enable), .save_cond_reg(inv_UC_save_cond_reg),
    .clear_cond_reg(inv_UC_clear_cond_reg), .read_mem_const(inv_UC_read_mem_const),
    .pcia_swap(inv_UC_pcia_swap), .save_src_reg(inv_UC_save_src_reg), .extended_opcode(inv_UC_extended_opcode));  // open: UC_B, UC_A
  ucode_5 ucode_5_1 (
    .nfetch_cycle(inv_fetch_clock), .nlow_cycle(inv_low_cycle), .nhigh_cycle(inv_high_cycle),
    .nselect_opcode(inv_select_opcode_5), .read_addr_src_reg(inv_UC_read_addr_src_reg),
    .int_ready(inv_UC_int_ready), .write_address(inv_UC_write_address), .restart_cycle(inv_UC_restart_cycle),
    .ula_enable(inv_UC_ula_enable), .write_enable(inv_UC_write_enable), .save_cond_reg(inv_UC_save_cond_reg),
    .clear_cond_reg(inv_UC_clear_cond_reg), .read_mem_const(inv_UC_read_mem_const),
    .pcia_swap(inv_UC_pcia_swap), .save_src_reg(inv_UC_save_src_reg), .extended_opcode(inv_UC_extended_opcode));  // open: UC_B, UC_A
  ucode_6 ucode_6_1 (
    .nfetch_cycle(inv_fetch_clock), .nlow_cycle(inv_low_cycle), .nhigh_cycle(inv_high_cycle),
    .nselect_opcode(inv_select_opcode_6), .read_addr_src_reg(inv_UC_read_addr_src_reg),
    .int_ready(inv_UC_int_ready), .write_address(inv_UC_write_address), .restart_cycle(inv_UC_restart_cycle),
    .ula_enable(inv_UC_ula_enable), .write_enable(inv_UC_write_enable), .save_cond_reg(inv_UC_save_cond_reg),
    .clear_cond_reg(inv_UC_clear_cond_reg), .read_mem_const(inv_UC_read_mem_const),
    .pcia_swap(inv_UC_pcia_swap), .save_src_reg(inv_UC_save_src_reg), .extended_opcode(inv_UC_extended_opcode));  // open: UC_B, UC_A
  ucode_7 ucode_7_1 (
    .nfetch_cycle(inv_fetch_clock), .nlow_cycle(inv_low_cycle), .nhigh_cycle(inv_high_cycle),
    .nselect_opcode(inv_select_opcode_7), .read_addr_src_reg(inv_UC_read_addr_src_reg),
    .int_ready(inv_UC_int_ready), .write_address(inv_UC_write_address), .restart_cycle(inv_UC_restart_cycle),
    .ula_enable(inv_UC_ula_enable), .write_enable(inv_UC_write_enable), .save_cond_reg(inv_UC_save_cond_reg),
    .clear_cond_reg(inv_UC_clear_cond_reg), .read_mem_const(inv_UC_read_mem_const),
    .pcia_swap(inv_UC_pcia_swap), .save_src_reg(inv_UC_save_src_reg), .extended_opcode(inv_UC_extended_opcode));  // open: UC_B, UC_A
  ucode_int ucode_int_1 (
    .nfetch_cycle(inv_fetch_clock), .nlow_cycle(inv_low_cycle), .nhigh_cycle(inv_high_cycle),
    .nselect_opcode(inv_select_opcode_int), .read_addr_src_reg(inv_UC_read_addr_src_reg),
    .int_ready(inv_UC_int_ready), .write_address(inv_UC_write_address), .restart_cycle(inv_UC_restart_cycle),
    .ula_enable(inv_UC_ula_enable), .write_enable(inv_UC_write_enable), .save_cond_reg(inv_UC_save_cond_reg),
    .clear_cond_reg(inv_UC_clear_cond_reg), .read_mem_const(inv_UC_read_mem_const),
    .pcia_swap(inv_UC_pcia_swap), .save_src_reg(inv_UC_save_src_reg), .extended_opcode(inv_UC_extended_opcode));  // open: UC_B, UC_A
  ucode_reset ucode_reset_1 (
    .nfetch_cycle(inv_reset_sync), .nlow_cycle(inv_reset_low_cycle), .nhigh_cycle(inv_reset_high_cycle),
    .nselect_opcode(inv_select_opcode_reset), .read_addr_src_reg(inv_UC_read_addr_src_reg),
    .int_ready(inv_UC_int_ready), .write_address(inv_UC_write_address), .restart_cycle(inv_UC_restart_cycle),
    .ula_enable(inv_UC_ula_enable), .write_enable(inv_UC_write_enable), .save_cond_reg(inv_UC_save_cond_reg),
    .clear_cond_reg(inv_UC_clear_cond_reg), .read_mem_const(inv_UC_read_mem_const),
    .pcia_swap(inv_UC_pcia_swap), .save_src_reg(inv_UC_save_src_reg), .extended_opcode(inv_UC_extended_opcode));  // open: UC_B, UC_A
  Pull_Resistor #(.pull(1)) pull_resistor_17 (.node(inv_UC_read_addr_src_reg));
  Pull_Resistor #(.pull(1)) pull_resistor_18 (.node(inv_UC_int_ready));
  Pull_Resistor #(.pull(1)) pull_resistor_19 (.node(inv_UC_write_address));
  Pull_Resistor #(.pull(1)) pull_resistor_20 (.node(inv_UC_restart_cycle));
  Pull_Resistor #(.pull(1)) pull_resistor_21 (.node(inv_UC_ula_enable));
  Pull_Resistor #(.pull(1)) pull_resistor_22 (.node(inv_UC_pcia_swap));
  Pull_Resistor #(.pull(1)) pull_resistor_23 (.node(inv_UC_save_src_reg));
  Pull_Resistor #(.pull(1)) pull_resistor_24 (.node(inv_UC_extended_opcode));
  Pull_Resistor #(.pull(1)) pull_resistor_25 (.node(inv_UC_write_enable));
  Pull_Resistor #(.pull(1)) pull_resistor_26 (.node(inv_UC_save_cond_reg));
  Pull_Resistor #(.pull(1)) pull_resistor_27 (.node(inv_UC_clear_cond_reg));
  Pull_Resistor #(.pull(1)) pull_resistor_28 (.node(inv_UC_read_mem_const));

  // Other names for the same wires on the sheet: CARRY_FLAG = in_4; DATA[7:0] = in_1; INT_MASK_FLAG = out_7;
  //   INT_REQUEST = in_2; NEGATIVE_FLAG = in_6; OVERFLOW_FLAG = in_5; rd_addr8[4:0] = RD_ADDR;
  //   select_opcode[8:0] = {inv_select_opcode_int, inv_select_opcode_7, inv_select_opcode_6, inv_select_opcode_5, inv_select_opcode_4, inv_select_opcode_3, inv_select_opcode_2, inv_select_opcode_1, inv_select_opcode_0};
  //   wr_addr8[4:0] = WR_ADDR; ZERO_FLAG = in_3
endmodule

module sequenciador (
  input  RESET,
  input  nUC_halt,
  input  nCLOCK,
  input  nUC_restart_cycle,
  output any_low_cycle,
  output nreset_sync,
  output nreset_low_cycle,
  output nreset_high_cycle,
  output nfetch_cycle,
  output nlow_cycle,
  output nhigh_cycle,
  output nselect_opcode_reset,
  output out_restart_cycle
);

  wire n74138_1_pin4, n74138_1_pin6, n74138_1_pin7, n74193_1_pin1, n74193_1_pin9, n74193_1_pin10,
       n74193_1_pin15, not_1_out, QA, QB;

  _74193 u_74193_1 (
    .pin1(n74193_1_pin1), .pin2(QB), .pin3(QA), .pin4(nUC_halt), .pin5(nCLOCK), .pin6(nselect_opcode_reset),
    .pin15(n74193_1_pin15), .pin14(RESET), .pin11(nUC_restart_cycle), .pin10(n74193_1_pin10),
    .pin9(n74193_1_pin9));  // open: pin7, pin13, pin12
  _74138 u_74138_1 (
    .pin1(QA), .pin2(QB), .pin3(nselect_opcode_reset), .pin4(n74138_1_pin4), .pin5(n74138_1_pin4),
    .pin6(n74138_1_pin6), .pin7(n74138_1_pin7), .pin14(nreset_sync), .pin13(nreset_low_cycle),
    .pin12(nreset_high_cycle), .pin11(nfetch_cycle), .pin10(nlow_cycle), .pin9(nhigh_cycle));  // open: pin15
  not not_1 (not_1_out, n74138_1_pin7);
  assign out_restart_cycle = not_1_out ? 1'b0 : 1'bz;  // Controlled_Buffer controlled_buffer_1
  and and_1 (any_low_cycle, nreset_low_cycle, nlow_cycle);
  // also tied to GND on the sheet: {n74193_1_pin1, n74193_1_pin15, n74193_1_pin9, n74138_1_pin4}
  // also tied to VCC on the sheet: {n74193_1_pin10, n74138_1_pin6}

  // Other names for the same wires on the sheet: QC = nselect_opcode_reset

  // Notes on the sheet:
  //   nUC_halt: initial=0x1
  //   nCLOCK: initial=0x1
  //   nUC_restart_cycle: initial=0x1
endmodule

module decodificador (
  input  clear_interrupt_mask,
  input  INT_REQUEST,
  input  set_interrupt_mask,
  input  [7:0] DATA,
  input  restart_cycle,
  input  int_ready,
  input  fetch_clock,
  input  nfetch_cycle,
  input  nselect_opcode_reset,
  output [8:0] select_opcode,
  output [7:0] INS,
  output INT_MASK_FLAG
);

  wire and_1_out, and_2_out, int_pending, n7474_1_pin2, n7474_1_pin4, n7474_1_pin11, n7474_1_pin12,
       n7474_2_pin10, n7474_2_pin11, n74138_1_pin4, n74157_1_pin15, n74157_2_pin15, n74377_1_pin1, Q0, Q1,
       Q2, Q3, Q4, Q5, Q6, Q7;

  _74377 u_74377_1 (
    .pin1(n74377_1_pin1), .pin2(Q0), .pin3(DATA[0]), .pin4(DATA[1]), .pin5(Q1), .pin6(Q2), .pin7(DATA[2]),
    .pin8(DATA[3]), .pin9(Q3), .pin19(Q7), .pin18(DATA[7]), .pin17(DATA[6]), .pin16(Q6), .pin15(Q5),
    .pin14(DATA[5]), .pin13(DATA[4]), .pin12(Q4), .pin11(fetch_clock));
  _74157 u_74157_1 (
    .pin1(nfetch_cycle), .pin2(DATA[0]), .pin3(Q0), .pin4(INS[0]), .pin5(DATA[1]), .pin6(Q1), .pin7(INS[1]),
    .pin15(n74157_1_pin15), .pin14(DATA[3]), .pin13(Q3), .pin12(INS[3]), .pin11(DATA[2]), .pin10(Q2),
    .pin9(INS[2]));
  and and_1 (and_1_out, select_opcode[8], nselect_opcode_reset);
  _74157 u_74157_2 (
    .pin1(nfetch_cycle), .pin2(DATA[4]), .pin3(Q4), .pin4(INS[4]), .pin5(DATA[5]), .pin6(Q5), .pin7(INS[5]),
    .pin15(n74157_2_pin15), .pin14(DATA[7]), .pin13(Q7), .pin12(INS[7]), .pin11(DATA[6]), .pin10(Q6),
    .pin9(INS[6]));
  _74138 u_74138_1 (
    .pin1(INS[5]), .pin2(INS[6]), .pin3(INS[7]), .pin4(n74138_1_pin4), .pin5(n74138_1_pin4),
    .pin6(and_1_out), .pin7(select_opcode[7]), .pin15(select_opcode[0]), .pin14(select_opcode[1]),
    .pin13(select_opcode[2]), .pin12(select_opcode[3]), .pin11(select_opcode[4]), .pin10(select_opcode[5]),
    .pin9(select_opcode[6]));
  and and_2 (and_2_out, INT_REQUEST, INT_MASK_FLAG);
  _7474 u_7474_1 (
    .pin1(int_ready), .pin2(n7474_1_pin2), .pin3(and_2_out), .pin4(n7474_1_pin4), .pin5(int_pending),
    .pin13(clear_interrupt_mask), .pin12(n7474_1_pin12), .pin11(n7474_1_pin11), .pin10(set_interrupt_mask),
    .pin9(INT_MASK_FLAG));  // open: pin6, pin8
  _7474 u_7474_2 (
    .pin13(restart_cycle), .pin12(int_pending), .pin11(n7474_2_pin11), .pin10(n7474_2_pin10),
    .pin8(select_opcode[8]));  // open: pin1, pin2, pin3, pin4, pin5, pin6, pin9
  not not_1 (n7474_2_pin11, int_ready);
  // also tied to GND on the sheet: {n74377_1_pin1, n74157_1_pin15, n74138_1_pin4, n74157_2_pin15, n7474_1_pin12, n7474_1_pin11}
  // also tied to VCC on the sheet: {n7474_1_pin2, n7474_1_pin4, n7474_2_pin10}

  // Other names for the same wires on the sheet: inv_fetch_cycle = nfetch_cycle;
  //   inv_select_opcode_reset = nselect_opcode_reset; inv_UC_int_ready = int_ready;
  //   inv_select_opcode_int = select_opcode[8]

  // Notes on the sheet:
  //   restart_cycle: initial=0x1
  //   set_interrupt_mask: initial=0x1
  //   clear_interrupt_mask: initial=0x1
endmodule

module avaliador_condicao (
  input  ZERO_FLAG,
  input  CARRY_FLAG,
  input  nclear_cond_reg,
  input  OVERFLOW_FLAG,
  input  nsave_cond_reg,
  input  NEGATIVE_FLAG,
  input  nwrite_enable,
  input  nula_enable,
  input  [7:0] INS,
  output ncondition_true,
  output WRITE_ENABLE,
  output ULA_ENABLE,
  output nenable_wr_addr
);

  wire and_1_out, n7474_1_pin4, not_1_out, or_1_out, or_2_out, or_3_out, or_4_out, xor_1_out, xor_2_out,
       xor_3_out, xor_4_out;

  xor xor_1 (xor_1_out, ZERO_FLAG, INS[4]);
  xor xor_2 (xor_2_out, CARRY_FLAG, INS[4]);
  xor xor_3 (xor_3_out, OVERFLOW_FLAG, INS[4]);
  xor xor_4 (xor_4_out, NEGATIVE_FLAG, INS[4]);
  or or_1 (or_1_out, xor_1_out, INS[0]);
  or or_2 (or_2_out, xor_2_out, INS[1]);
  or or_3 (or_3_out, xor_3_out, INS[2]);
  or or_4 (or_4_out, xor_4_out, INS[3]);
  and and_1 (and_1_out, or_1_out, or_2_out, or_3_out, or_4_out);
  not not_1 (not_1_out, nsave_cond_reg);
  _7474 u_7474_1 (
    .pin1(nclear_cond_reg), .pin2(and_1_out), .pin3(not_1_out), .pin4(n7474_1_pin4), .pin5(ncondition_true));  // open: pin6, pin13, pin12, pin11, pin10, pin9, pin8
  nor nor_1 (WRITE_ENABLE, ncondition_true, nwrite_enable);
  nor nor_2 (ULA_ENABLE, ncondition_true, nula_enable);
  and and_2 (nenable_wr_addr, nwrite_enable, nula_enable);
  // also tied to VCC on the sheet: n7474_1_pin4
endmodule

module ucode_template (
  input  nfetch_cycle,
  input  nlow_cycle,
  input  nhigh_cycle,
  input  nselect_opcode,
  output inv_UC_read_addr_src_reg,
  output inv_UC_int_ready,
  output inv_UC_B,
  output inv_UC_write_address,
  output inv_UC_restart_cycle,
  output inv_UC_ula_enable,
  output inv_UC_A,
  output inv_UC_pcia_swap,
  output inv_UC_save_src_reg,
  output inv_UC_extended_opcode,
  output inv_UC_write_enable,
  output inv_UC_save_cond_reg,
  output inv_UC_clear_cond_reg,
  output inv_UC_read_mem_const
);

  wire nor_1_out, nor_2_out, nor_3_out;

  assign inv_UC_write_enable = nor_1_out ? 1'b0 : 1'bz;  // Controlled_Buffer controlled_buffer_1
  nor nor_1 (nor_1_out, nfetch_cycle, nselect_opcode);
  assign inv_UC_write_enable = nor_2_out ? 1'b0 : 1'bz;  // Controlled_Buffer controlled_buffer_2
  nor nor_2 (nor_2_out, nlow_cycle, nselect_opcode);
  assign inv_UC_write_enable = nor_3_out ? 1'b0 : 1'bz;  // Controlled_Buffer controlled_buffer_3
  nor nor_3 (nor_3_out, nhigh_cycle, nselect_opcode);
  assign inv_UC_write_address = nor_1_out ? 1'b0 : 1'bz;  // Controlled_Buffer controlled_buffer_4
  assign inv_UC_write_address = nor_2_out ? 1'b0 : 1'bz;  // Controlled_Buffer controlled_buffer_5
  assign inv_UC_write_address = nor_3_out ? 1'b0 : 1'bz;  // Controlled_Buffer controlled_buffer_6
  assign inv_UC_pcia_swap = nor_1_out ? 1'b0 : 1'bz;  // Controlled_Buffer controlled_buffer_7
  assign inv_UC_pcia_swap = nor_2_out ? 1'b0 : 1'bz;  // Controlled_Buffer controlled_buffer_8
  assign inv_UC_pcia_swap = nor_3_out ? 1'b0 : 1'bz;  // Controlled_Buffer controlled_buffer_9
  assign inv_UC_read_addr_src_reg = nor_1_out ? 1'b0 : 1'bz;  // Controlled_Buffer controlled_buffer_10
  assign inv_UC_read_addr_src_reg = nor_2_out ? 1'b0 : 1'bz;  // Controlled_Buffer controlled_buffer_11
  assign inv_UC_read_addr_src_reg = nor_3_out ? 1'b0 : 1'bz;  // Controlled_Buffer controlled_buffer_12
  assign inv_UC_save_cond_reg = nor_1_out ? 1'b0 : 1'bz;  // Controlled_Buffer controlled_buffer_13
  assign inv_UC_save_cond_reg = nor_2_out ? 1'b0 : 1'bz;  // Controlled_Buffer controlled_buffer_14
  assign inv_UC_save_cond_reg = nor_3_out ? 1'b0 : 1'bz;  // Controlled_Buffer controlled_buffer_15
  assign inv_UC_restart_cycle = nor_1_out ? 1'b0 : 1'bz;  // Controlled_Buffer controlled_buffer_16
  assign inv_UC_restart_cycle = nor_2_out ? 1'b0 : 1'bz;  // Controlled_Buffer controlled_buffer_17
  assign inv_UC_restart_cycle = nor_3_out ? 1'b0 : 1'bz;  // Controlled_Buffer controlled_buffer_18
  assign inv_UC_save_src_reg = nor_1_out ? 1'b0 : 1'bz;  // Controlled_Buffer controlled_buffer_19
  assign inv_UC_int_ready = nor_1_out ? 1'b0 : 1'bz;  // Controlled_Buffer controlled_buffer_20
  assign inv_UC_save_src_reg = nor_2_out ? 1'b0 : 1'bz;  // Controlled_Buffer controlled_buffer_21
  assign inv_UC_int_ready = nor_2_out ? 1'b0 : 1'bz;  // Controlled_Buffer controlled_buffer_22
  assign inv_UC_save_src_reg = nor_3_out ? 1'b0 : 1'bz;  // Controlled_Buffer controlled_buffer_23
  assign inv_UC_int_ready = nor_3_out ? 1'b0 : 1'bz;  // Controlled_Buffer controlled_buffer_24
  assign inv_UC_clear_cond_reg = nor_1_out ? 1'b0 : 1'bz;  // Controlled_Buffer controlled_buffer_25
  assign inv_UC_clear_cond_reg = nor_2_out ? 1'b0 : 1'bz;  // Controlled_Buffer controlled_buffer_26
  assign inv_UC_clear_cond_reg = nor_3_out ? 1'b0 : 1'bz;  // Controlled_Buffer controlled_buffer_27
  assign inv_UC_ula_enable = nor_1_out ? 1'b0 : 1'bz;  // Controlled_Buffer controlled_buffer_28
  assign inv_UC_ula_enable = nor_2_out ? 1'b0 : 1'bz;  // Controlled_Buffer controlled_buffer_29
  assign inv_UC_ula_enable = nor_3_out ? 1'b0 : 1'bz;  // Controlled_Buffer controlled_buffer_30
  assign inv_UC_extended_opcode = nor_1_out ? 1'b0 : 1'bz;  // Controlled_Buffer controlled_buffer_31
  assign inv_UC_extended_opcode = nor_2_out ? 1'b0 : 1'bz;  // Controlled_Buffer controlled_buffer_32
  assign inv_UC_extended_opcode = nor_3_out ? 1'b0 : 1'bz;  // Controlled_Buffer controlled_buffer_33
  assign inv_UC_B = nor_1_out ? 1'b0 : 1'bz;  // Controlled_Buffer controlled_buffer_34
  assign inv_UC_B = nor_2_out ? 1'b0 : 1'bz;  // Controlled_Buffer controlled_buffer_35
  assign inv_UC_B = nor_3_out ? 1'b0 : 1'bz;  // Controlled_Buffer controlled_buffer_36
  assign inv_UC_read_mem_const = nor_1_out ? 1'b0 : 1'bz;  // Controlled_Buffer controlled_buffer_37
  assign inv_UC_read_mem_const = nor_2_out ? 1'b0 : 1'bz;  // Controlled_Buffer controlled_buffer_38
  assign inv_UC_read_mem_const = nor_3_out ? 1'b0 : 1'bz;  // Controlled_Buffer controlled_buffer_39
  assign inv_UC_A = nor_1_out ? 1'b0 : 1'bz;  // Controlled_Buffer controlled_buffer_40
  assign inv_UC_A = nor_2_out ? 1'b0 : 1'bz;  // Controlled_Buffer controlled_buffer_41
  assign inv_UC_A = nor_3_out ? 1'b0 : 1'bz;  // Controlled_Buffer controlled_buffer_42
endmodule

module ucode_0 (
  input  nfetch_cycle,
  input  nlow_cycle,
  input  mhigh_cycle,
  input  nselect_opcode,
  output read_addr_src_reg,
  output int_ready,
  output UC_B,
  output write_address,
  output restart_cycle,
  output ula_enable,
  output UC_A,
  output write_enable,
  output save_cond_reg,
  output clear_cond_reg,
  output read_mem_const,
  output pcia_swap,
  output save_src_reg,
  output extended_opcode
);

  wire nor_1_out, nor_2_out, nor_3_out;

  nor nor_1 (nor_1_out, nfetch_cycle, nselect_opcode);
  nor nor_2 (nor_2_out, nlow_cycle, nselect_opcode);
  nor nor_3 (nor_3_out, mhigh_cycle, nselect_opcode);
  assign restart_cycle = nor_2_out ? 1'b0 : 1'bz;  // Controlled_Buffer controlled_buffer_1
  assign int_ready = nor_1_out ? 1'b0 : 1'bz;  // Controlled_Buffer controlled_buffer_2
  assign int_ready = nor_2_out ? 1'b0 : 1'bz;  // Controlled_Buffer controlled_buffer_3
  assign extended_opcode = nor_1_out ? 1'b0 : 1'bz;  // Controlled_Buffer controlled_buffer_4

  // Notes on the sheet:
  //   SHORT CONTROL
endmodule

module ucode_1 (
  input  nfetch_cycle,
  input  nlow_cycle,
  input  nhigh_cycle,
  input  nselect_opcode,
  output read_addr_src_reg,
  output int_ready,
  output UC_B,
  output write_address,
  output restart_cycle,
  output ula_enable,
  output UC_A,
  output write_enable,
  output save_cond_reg,
  output clear_cond_reg,
  output read_mem_const,
  output pcia_swap,
  output save_src_reg,
  output extended_opcode
);

  wire nor_1_out, nor_2_out, nor_3_out;

  nor nor_1 (nor_1_out, nfetch_cycle, nselect_opcode);
  nor nor_2 (nor_2_out, nlow_cycle, nselect_opcode);
  nor nor_3 (nor_3_out, nhigh_cycle, nselect_opcode);
  assign restart_cycle = nor_2_out ? 1'b0 : 1'bz;  // Controlled_Buffer controlled_buffer_1
  assign save_src_reg = nor_1_out ? 1'b0 : 1'bz;  // Controlled_Buffer controlled_buffer_2
  assign int_ready = nor_1_out ? 1'b0 : 1'bz;  // Controlled_Buffer controlled_buffer_3
  assign int_ready = nor_2_out ? 1'b0 : 1'bz;  // Controlled_Buffer controlled_buffer_4
  assign clear_cond_reg = nor_1_out ? 1'b0 : 1'bz;  // Controlled_Buffer controlled_buffer_5

  // Notes on the sheet:
  //   SOURCE + INT
endmodule

module ucode_2 (
  input  nfetch_cycle,
  input  nlow_cycle,
  input  nhigh_cycle,
  input  nselect_opcode,
  output read_addr_src_reg,
  output int_ready,
  output UC_B,
  output write_address,
  output restart_cycle,
  output ula_enable,
  output UC_A,
  output write_enable,
  output save_cond_reg,
  output clear_cond_reg,
  output read_mem_const,
  output pcia_swap,
  output save_src_reg,
  output extended_opcode
);

  wire nor_1_out, nor_2_out, nor_3_out;

  nor nor_1 (nor_1_out, nfetch_cycle, nselect_opcode);
  nor nor_2 (nor_2_out, nlow_cycle, nselect_opcode);
  nor nor_3 (nor_3_out, nhigh_cycle, nselect_opcode);
  assign restart_cycle = nor_2_out ? 1'b0 : 1'bz;  // Controlled_Buffer controlled_buffer_1
  assign save_src_reg = nor_1_out ? 1'b0 : 1'bz;  // Controlled_Buffer controlled_buffer_2

  // Notes on the sheet:
  //   SOURCE
endmodule

module ucode_3 (
  input  nfetch_cycle,
  input  nlow_cycle,
  input  nhigh_cycle,
  input  nselect_opcode,
  output read_addr_src_reg,
  output int_ready,
  output UC_B,
  output write_address,
  output restart_cycle,
  output ula_enable,
  output UC_A,
  output write_enable,
  output save_cond_reg,
  output clear_cond_reg,
  output read_mem_const,
  output pcia_swap,
  output save_src_reg,
  output extended_opcode
);

  wire nor_1_out, nor_2_out, nor_3_out;

  nor nor_1 (nor_1_out, nfetch_cycle, nselect_opcode);
  nor nor_2 (nor_2_out, nlow_cycle, nselect_opcode);
  nor nor_3 (nor_3_out, nhigh_cycle, nselect_opcode);
  assign save_cond_reg = nor_1_out ? 1'b0 : 1'bz;  // Controlled_Buffer controlled_buffer_1
  assign restart_cycle = nor_2_out ? 1'b0 : 1'bz;  // Controlled_Buffer controlled_buffer_2

  // Notes on the sheet:
  //   CONDITION
endmodule

module ucode_4 (
  input  nfetch_cycle,
  input  nlow_cycle,
  input  nhigh_cycle,
  input  nselect_opcode,
  output read_addr_src_reg,
  output int_ready,
  output UC_B,
  output write_address,
  output restart_cycle,
  output ula_enable,
  output UC_A,
  output write_enable,
  output save_cond_reg,
  output clear_cond_reg,
  output read_mem_const,
  output pcia_swap,
  output save_src_reg,
  output extended_opcode
);

  wire nor_1_out, nor_2_out, nor_3_out;

  nor nor_1 (nor_1_out, nfetch_cycle, nselect_opcode);
  nor nor_2 (nor_2_out, nlow_cycle, nselect_opcode);
  nor nor_3 (nor_3_out, nhigh_cycle, nselect_opcode);
  assign restart_cycle = nor_3_out ? 1'b0 : 1'bz;  // Controlled_Buffer controlled_buffer_1
  assign extended_opcode = nor_2_out ? 1'b0 : 1'bz;  // Controlled_Buffer controlled_buffer_2

  // Notes on the sheet:
  //   LONG CONTROL
endmodule

module ucode_5 (
  input  nfetch_cycle,
  input  nlow_cycle,
  input  nhigh_cycle,
  input  nselect_opcode,
  output read_addr_src_reg,
  output int_ready,
  output UC_B,
  output write_address,
  output restart_cycle,
  output ula_enable,
  output UC_A,
  output write_enable,
  output save_cond_reg,
  output clear_cond_reg,
  output read_mem_const,
  output pcia_swap,
  output save_src_reg,
  output extended_opcode
);

  wire nor_1_out, nor_2_out, nor_3_out;

  nor nor_1 (nor_1_out, nfetch_cycle, nselect_opcode);
  assign write_enable = nor_2_out ? 1'b0 : 1'bz;  // Controlled_Buffer controlled_buffer_1
  nor nor_2 (nor_2_out, nlow_cycle, nselect_opcode);
  nor nor_3 (nor_3_out, nhigh_cycle, nselect_opcode);
  assign read_addr_src_reg = nor_2_out ? 1'b0 : 1'bz;  // Controlled_Buffer controlled_buffer_2
  assign restart_cycle = nor_3_out ? 1'b0 : 1'bz;  // Controlled_Buffer controlled_buffer_3

  // Notes on the sheet:
  //   TRANSFER BYTE
endmodule

module ucode_6 (
  input  nfetch_cycle,
  input  nlow_cycle,
  input  nhigh_cycle,
  input  nselect_opcode,
  output read_addr_src_reg,
  output int_ready,
  output UC_B,
  output write_address,
  output restart_cycle,
  output ula_enable,
  output UC_A,
  output write_enable,
  output save_cond_reg,
  output clear_cond_reg,
  output read_mem_const,
  output pcia_swap,
  output save_src_reg,
  output extended_opcode
);

  wire nor_1_out, nor_2_out, nor_3_out;

  nor nor_1 (nor_1_out, nfetch_cycle, nselect_opcode);
  assign write_enable = nor_2_out ? 1'b0 : 1'bz;  // Controlled_Buffer controlled_buffer_1
  nor nor_2 (nor_2_out, nlow_cycle, nselect_opcode);
  assign write_enable = nor_3_out ? 1'b0 : 1'bz;  // Controlled_Buffer controlled_buffer_2
  nor nor_3 (nor_3_out, nhigh_cycle, nselect_opcode);
  assign read_addr_src_reg = nor_2_out ? 1'b0 : 1'bz;  // Controlled_Buffer controlled_buffer_3
  assign read_addr_src_reg = nor_3_out ? 1'b0 : 1'bz;  // Controlled_Buffer controlled_buffer_4

  // Notes on the sheet:
  //   TRANSFER WORD
endmodule

module ucode_7 (
  input  nfetch_cycle,
  input  nlow_cycle,
  input  nhigh_cycle,
  input  nselect_opcode,
  output read_addr_src_reg,
  output int_ready,
  output UC_B,
  output write_address,
  output restart_cycle,
  output ula_enable,
  output UC_A,
  output write_enable,
  output save_cond_reg,
  output clear_cond_reg,
  output read_mem_const,
  output pcia_swap,
  output save_src_reg,
  output extended_opcode
);

  wire nor_1_out, nor_2_out, nor_3_out;

  nor nor_1 (nor_1_out, nfetch_cycle, nselect_opcode);
  nor nor_2 (nor_2_out, nlow_cycle, nselect_opcode);
  nor nor_3 (nor_3_out, nhigh_cycle, nselect_opcode);
  assign read_addr_src_reg = nor_2_out ? 1'b0 : 1'bz;  // Controlled_Buffer controlled_buffer_1
  assign restart_cycle = nor_3_out ? 1'b0 : 1'bz;  // Controlled_Buffer controlled_buffer_2
  assign ula_enable = nor_2_out ? 1'b0 : 1'bz;  // Controlled_Buffer controlled_buffer_3

  // Notes on the sheet:
  //   ARITHMETIC
endmodule

module ucode_int (
  input  nfetch_cycle,
  input  nlow_cycle,
  input  nhigh_cycle,
  input  nselect_opcode,
  output read_addr_src_reg,
  output int_ready,
  output UC_B,
  output write_address,
  output restart_cycle,
  output ula_enable,
  output UC_A,
  output write_enable,
  output save_cond_reg,
  output clear_cond_reg,
  output read_mem_const,
  output pcia_swap,
  output save_src_reg,
  output extended_opcode
);

  wire nor_1_out, nor_2_out, nor_3_out;

  nor nor_1 (nor_1_out, nfetch_cycle, nselect_opcode);
  assign write_enable = nor_2_out ? 1'b0 : 1'bz;  // Controlled_Buffer controlled_buffer_1
  nor nor_2 (nor_2_out, nlow_cycle, nselect_opcode);
  assign write_enable = nor_3_out ? 1'b0 : 1'bz;  // Controlled_Buffer controlled_buffer_2
  nor nor_3 (nor_3_out, nhigh_cycle, nselect_opcode);
  assign write_address = nor_2_out ? 1'b0 : 1'bz;  // Controlled_Buffer controlled_buffer_3
  assign write_address = nor_3_out ? 1'b0 : 1'bz;  // Controlled_Buffer controlled_buffer_4
  assign pcia_swap = nor_1_out ? 1'b0 : 1'bz;  // Controlled_Buffer controlled_buffer_5
  assign read_mem_const = nor_2_out ? 1'b0 : 1'bz;  // Controlled_Buffer controlled_buffer_6
  assign read_mem_const = nor_3_out ? 1'b0 : 1'bz;  // Controlled_Buffer controlled_buffer_7

  // Notes on the sheet:
  //   INTERRUPT
endmodule

module ucode_reset (
  input  nfetch_cycle,
  input  nlow_cycle,
  input  nhigh_cycle,
  input  nselect_opcode,
  output read_addr_src_reg,
  output int_ready,
  output UC_B,
  output write_address,
  output restart_cycle,
  output ula_enable,
  output UC_A,
  output write_enable,
  output save_cond_reg,
  output clear_cond_reg,
  output read_mem_const,
  output pcia_swap,
  output save_src_reg,
  output extended_opcode
);

  wire nor_1_out, nor_2_out, nor_3_out;

  nor nor_1 (nor_1_out, nfetch_cycle, nselect_opcode);
  assign write_enable = nor_2_out ? 1'b0 : 1'bz;  // Controlled_Buffer controlled_buffer_1
  nor nor_2 (nor_2_out, nlow_cycle, nselect_opcode);
  assign write_enable = nor_3_out ? 1'b0 : 1'bz;  // Controlled_Buffer controlled_buffer_2
  nor nor_3 (nor_3_out, nhigh_cycle, nselect_opcode);
  assign write_address = nor_2_out ? 1'b0 : 1'bz;  // Controlled_Buffer controlled_buffer_3
  assign write_address = nor_3_out ? 1'b0 : 1'bz;  // Controlled_Buffer controlled_buffer_4
  assign clear_cond_reg = nor_1_out ? 1'b0 : 1'bz;  // Controlled_Buffer controlled_buffer_5
  assign read_mem_const = nor_2_out ? 1'b0 : 1'bz;  // Controlled_Buffer controlled_buffer_6
  assign read_mem_const = nor_3_out ? 1'b0 : 1'bz;  // Controlled_Buffer controlled_buffer_7

  // Notes on the sheet:
  //   RESET
endmodule

module extended_code (
  input  extended_opcode,
  input  [7:0] INS,
  output set_interrupt_mask,
  output clear_interrupt_mask,
  output halt,
  output \break ,
  output pclr_swap
);

  wire n74138_1_pin6;

  _74138 u_74138_1 (
    .pin1(INS[0]), .pin2(INS[1]), .pin3(INS[2]), .pin4(extended_opcode), .pin5(extended_opcode),
    .pin6(n74138_1_pin6), .pin13(set_interrupt_mask), .pin12(clear_interrupt_mask), .pin11(halt),
    .pin10(\break ), .pin9(pclr_swap));  // open: pin7, pin15, pin14
  // also tied to VCC on the sheet: n74138_1_pin6
endmodule

module read_from (
  input  read_addr_src_reg,
  input  any_low_cycle,
  input  [7:0] INS,
  input  save_src_reg,
  input  read_mem_const,
  input  nfetch_cycle,
  output [4:0] RD_ADDR
);

  wire addr_a_0, addr_a_1, addr_a_2, addr_a_3, addr_a_4, n74125_1_pin2, n74125_1_pin5, n74125_1_pin9,
       n74125_1_pin12, n74125_2_pin2, n74125_2_pin5, n74125_2_pin9, n74125_2_pin12, n74244_1_pin13,
       n74244_1_pin15, n74244_1_pin17, n74377_1_pin1, n74377_1_pin11, n74377_1_pin14, n74377_1_pin17,
       n74377_1_pin18, xor_1_out;

  Pull_Resistor pull_resistor_1 (.node(RD_ADDR[0]));
  Pull_Resistor pull_resistor_2 (.node(RD_ADDR[1]));
  Pull_Resistor pull_resistor_3 (.node(RD_ADDR[2]));
  Pull_Resistor pull_resistor_4 (.node(RD_ADDR[3]));
  Pull_Resistor pull_resistor_5 (.node(RD_ADDR[4]));
  _74377 u_74377_1 (
    .pin1(n74377_1_pin1), .pin2(addr_a_0), .pin3(INS[0]), .pin4(INS[1]), .pin5(addr_a_1), .pin6(addr_a_2),
    .pin7(INS[2]), .pin8(INS[3]), .pin9(addr_a_3), .pin18(n74377_1_pin18), .pin17(n74377_1_pin17),
    .pin14(n74377_1_pin14), .pin13(INS[4]), .pin12(addr_a_4), .pin11(n74377_1_pin11));  // open: pin19, pin16, pin15
  not not_1 (n74377_1_pin11, save_src_reg);
  _74125 u_74125_1 (
    .pin1(read_mem_const), .pin2(n74125_1_pin2), .pin3(RD_ADDR[1]), .pin4(read_mem_const),
    .pin5(n74125_1_pin5), .pin6(RD_ADDR[2]), .pin13(read_mem_const), .pin12(n74125_1_pin12),
    .pin11(RD_ADDR[4]), .pin10(read_mem_const), .pin9(n74125_1_pin9), .pin8(RD_ADDR[3]));
  xor xor_1 (xor_1_out, any_low_cycle, addr_a_0);
  _74244 u_74244_1 (
    .pin1(read_addr_src_reg), .pin2(xor_1_out), .pin4(addr_a_1), .pin6(addr_a_2), .pin8(addr_a_3),
    .pin9(RD_ADDR[4]), .pin19(read_addr_src_reg), .pin18(RD_ADDR[0]), .pin17(n74244_1_pin17),
    .pin16(RD_ADDR[1]), .pin15(n74244_1_pin15), .pin14(RD_ADDR[2]), .pin13(n74244_1_pin13),
    .pin12(RD_ADDR[3]), .pin11(addr_a_4));  // open: pin3, pin5, pin7
  _74125 u_74125_2 (
    .pin1(nfetch_cycle), .pin2(n74125_2_pin2), .pin3(RD_ADDR[1]), .pin4(nfetch_cycle), .pin5(n74125_2_pin5),
    .pin6(RD_ADDR[2]), .pin13(nfetch_cycle), .pin12(n74125_2_pin12), .pin11(RD_ADDR[4]),
    .pin10(nfetch_cycle), .pin9(n74125_2_pin9), .pin8(RD_ADDR[3]));
  // also tied to GND on the sheet: {n74377_1_pin1, n74125_1_pin12, n74377_1_pin18, n74377_1_pin17, n74377_1_pin14, n74125_2_pin2, n74125_2_pin5, n74125_2_pin12, n74244_1_pin17, n74244_1_pin15, n74244_1_pin13}
  // also tied to VCC on the sheet: {n74125_1_pin2, n74125_1_pin5, n74125_1_pin9, n74125_2_pin9}

  // Other names for the same wires on the sheet: addr_out_0 = RD_ADDR[0]; addr_out_1 = RD_ADDR[1];
  //   addr_out_2 = RD_ADDR[2]; addr_out_3 = RD_ADDR[3]; addr_out_4 = RD_ADDR[4]
endmodule

module write_to (
  input  nwrite_pc,
  input  nenable_wr_addr,
  input  [7:0] INS,
  input  any_low_cycle,
  input  nlow_cycle,
  output [4:0] WR_ADDR
);

  wire n74157_1_pin2, n74157_1_pin5, n74157_1_pin11, n74157_1_pin14, xor_1_out;

  xor xor_1 (xor_1_out, nlow_cycle, INS[0]);
  _74157 u_74157_1 (
    .pin1(nwrite_pc), .pin2(n74157_1_pin2), .pin3(INS[1]), .pin4(WR_ADDR[1]), .pin5(n74157_1_pin5),
    .pin6(INS[2]), .pin7(WR_ADDR[2]), .pin15(nenable_wr_addr), .pin14(n74157_1_pin14), .pin13(INS[4]),
    .pin12(WR_ADDR[4]), .pin11(n74157_1_pin11), .pin10(INS[3]), .pin9(WR_ADDR[3]));
  _74157 u_74157_2 (
    .pin1(nwrite_pc), .pin2(any_low_cycle), .pin3(xor_1_out), .pin4(WR_ADDR[0]), .pin15(nenable_wr_addr));  // open: pin5, pin6, pin7, pin14, pin13, pin12, pin11, pin10, pin9
  // also tied to GND on the sheet: {n74157_1_pin2, n74157_1_pin5}
  // also tied to VCC on the sheet: {n74157_1_pin14, n74157_1_pin11}

  // Other names for the same wires on the sheet: addr_out_0 = WR_ADDR[0]; addr_out_1 = WR_ADDR[1];
  //   addr_out_2 = WR_ADDR[2]; addr_out_3 = WR_ADDR[3]; addr_out_4 = WR_ADDR[4]
endmodule

module address_constant (
  input  nread_mem_const,
  input  any_low_cycle,
  input  nselect_opcode_int,
  output [15:0] ADDR
);

  _74125 #(.ShowInternalStructure("true")) u_74125_1 (
    .pin1(nread_mem_const), .pin2(any_low_cycle), .pin3(ADDR[0]), .pin4(nread_mem_const),
    .pin5(nselect_opcode_int), .pin6(ADDR[1]));  // open: pin13, pin12, pin11, pin10, pin9, pin8

  // Other names for the same wires on the sheet: addr_0 = ADDR[0]; addr_1 = ADDR[1]
endmodule
