// Logisim project controle_carry_flag.circ as structural Verilog: 1 circuit, main circuit main
module main (
  input  n_select_cf,
  input  carry_in,
  input  option_value,
  input  option_mode,
  output carry_out
);

  wire n74125_1_pin3, n_carry_in, n_option_mode;

  _7404 #(.ShowInternalStructure("true")) u_7404_1 (
    .pin13(carry_in), .pin12(n_carry_in), .pin11(option_mode), .pin10(n_option_mode));  // open: pin1, pin2, pin3, pin4, pin5, pin6, pin9, pin8
  _74125 #(.ShowInternalStructure("true")) u_74125_1 (
    .pin1(option_mode), .pin2(option_value), .pin3(n74125_1_pin3), .pin4(n_option_mode), .pin5(n_carry_in),
    .pin6(n74125_1_pin3), .pin10(n_select_cf), .pin9(n74125_1_pin3), .pin8(carry_out));  // open: pin13, pin12, pin11
endmodule
