// Logisim project experimento.circ as structural Verilog: 1 circuit, main circuit main
module main (
  input  [7:0] in_1,
  input  in_2
);

  wire and_1_out, clo_ck, n74138_1_pin4, n74138_2_pin6, n74193_1_pin2, n74193_1_pin3, n74193_1_pin4,
       n74193_1_pin6, n_clock, n_cycle2, n_cycle3, n_cycle4, n_cycle5, n_cycle6, n_cycle7, n_fetch_high,
       n_fetch_low, n_script0, n_script1, n_script2, n_script3, n_script4, n_script5, n_script6, n_script7;
  wire [15:0] ins;

  and and_1 (and_1_out, n_fetch_low, n_fetch_high);
  _74377 u_74377_1 (
    .pin1(n_fetch_low), .pin2(ins[8]), .pin3(in_1[0]), .pin4(in_1[1]), .pin5(ins[9]), .pin6(ins[10]),
    .pin7(in_1[2]), .pin8(in_1[3]), .pin9(ins[11]), .pin19(ins[15]), .pin18(in_1[7]), .pin17(in_1[6]),
    .pin16(ins[14]), .pin15(ins[13]), .pin14(in_1[5]), .pin13(in_1[4]), .pin12(ins[12]), .pin11(clo_ck));
  _74377 u_74377_2 (
    .pin1(n_fetch_high), .pin2(ins[0]), .pin3(in_1[0]), .pin4(in_1[1]), .pin5(ins[1]), .pin6(ins[2]),
    .pin7(in_1[2]), .pin8(in_1[3]), .pin9(ins[3]), .pin19(ins[7]), .pin18(in_1[7]), .pin17(in_1[6]),
    .pin16(ins[6]), .pin15(ins[5]), .pin14(in_1[5]), .pin13(in_1[4]), .pin12(ins[4]), .pin11(clo_ck));
  _74138 u_74138_1 (
    .pin1(ins[12]), .pin2(ins[13]), .pin3(ins[14]), .pin4(n74138_1_pin4), .pin5(n74138_1_pin4),
    .pin6(and_1_out), .pin7(n_script7), .pin15(n_script0), .pin14(n_script1), .pin13(n_script2),
    .pin12(n_script3), .pin11(n_script4), .pin10(n_script5), .pin9(n_script6));
  Clock clock_1 (.out(clo_ck));
  not not_1 (n_clock, clo_ck);
  _74193 u_74193_1 (
    .pin2(n74193_1_pin2), .pin3(n74193_1_pin3), .pin4(n74193_1_pin4), .pin5(n_clock), .pin6(n74193_1_pin6));  // open: pin1, pin7, pin15, pin14, pin13, pin12, pin11, pin10, pin9
  _74138 u_74138_2 (
    .pin1(n74193_1_pin3), .pin2(n74193_1_pin2), .pin3(n74193_1_pin6), .pin4(in_2), .pin5(in_2),
    .pin6(n74138_2_pin6), .pin7(n_cycle7), .pin15(n_fetch_low), .pin14(n_fetch_high), .pin13(n_cycle2),
    .pin12(n_cycle3), .pin11(n_cycle4), .pin10(n_cycle5), .pin9(n_cycle6));
  // also tied to GND on the sheet: n74138_1_pin4
  // also tied to VCC on the sheet: {n74193_1_pin4, n74138_2_pin6}

  // Other names for the same wires on the sheet: halt = in_2; ins_p1[4:0] = ins[4:0]; ins_p2[4:0] = ins[9:5];
  //   ins_p3[1:0] = ins[11:10]; ins_script[2:0] = ins[14:12]; ins_finish = ins[15]
endmodule
