// Logisim project overflow.circ as structural Verilog: 1 circuit, main circuit main
module main (
  input  in_1,
  input  [7:0] in_2,
  input  [7:0] in_3,
  output [7:0] out_4
);

  wire adder_1_cout, and_1_out, xnor_1_out, xor_1_out;

  // Probe on in_2
  // Probe on in_2
  // Probe on in_3
  // Probe on in_3
  Adder adder_1 (.a(in_2), .b(in_3), .out(out_4), .cin(in_1), .cout(adder_1_cout));
  xnor xnor_1 (xnor_1_out, in_2[7], in_3[7]);
  // Probe on out_4
  // Probe on out_4
  xor xor_1 (xor_1_out, out_4[7], adder_1_cout);
  LED led_1 (.in(adder_1_cout));
  LED led_2 (.in(and_1_out));
  and and_1 (and_1_out, xor_1_out, xnor_1_out);

  // Notes on the sheet:
  //   CARRY
  //   OVERFLOW
endmodule
