// Logisim project regs.circ as structural Verilog: 17 circuits, main circuit main
module main (
  input  [7:0] PORT_C,
  input  [7:0] PORT_D,
  input  int_request
);

  wire button_1_out, clock_1_out, control_v5_1_debug_fetch, control_v5_1_flag_intmask,
       control_v5_1_pcia_swap, control_v5_1_pclr_swap, control_v5_1_ula_enable, control_v5_1_write_enable,
       reg16_file_1_inc_0, reg16_file_1_inc_1, reg16_file_1_inc_2, reg16_file_1_mar_inc,
       reg16_file_1_memory_read, reg16_file_1_memory_write, reg16_file_1_naddr_0, reg16_file_1_naddr_1,
       reg16_file_1_naddr_2, reg16_file_1_naddr_mar, reg16_file_1_naddr_sp, reg16_file_1_nselread0h,
       reg16_file_1_nselread0l, reg16_file_1_nselread1h, reg16_file_1_nselread1l, reg16_file_1_nselread2h,
       reg16_file_1_nselread2l, reg16_file_1_nselreadmarh, reg16_file_1_nselreadmarl,
       reg16_file_1_nselreadsph, reg16_file_1_nselreadspl, reg16_file_1_nselwrite0h,
       reg16_file_1_nselwrite0l, reg16_file_1_nselwrite1h, reg16_file_1_nselwrite1l,
       reg16_file_1_nselwrite2h, reg16_file_1_nselwrite2l, reg16_file_1_nselwritemarh,
       reg16_file_1_nselwritemarl, reg16_file_1_nselwritesph, reg16_file_1_nselwritespl, reg16_file_1_sp_dec,
       reg16_file_1_sp_inc, ula_8_1_carry_flag, ula_8_1_negative_flag, ula_8_1_overflow_flag,
       ula_8_1_zero_flag;
  wire [3:0] control_v5_1_addr_out, control_v5_1_addr_out_2, control_v5_1_addr_out_3,
       control_v5_1_addr_out_4, in_out_1_port_output_a, in_out_1_port_output_a_2, in_out_1_port_output_b,
       in_out_1_port_output_b_2, regs_bank_1_data_read, regs_bank_1_data_read_2;
  wire [4:0] control_v5_1_read_addr, control_v5_1_write_address;
  wire [7:0] control_v5_1_debug_ins, regs_bank_1_debug, regs_bank_1_debug_2, regs_bank_1_debug_3,
       regs_bank_1_debug_4, regs_bank_1_debug_5, regs_bank_1_debug_6, regs_bank_1_debug_7, ula_8_1_debug_acc;

  Hex_Digit_Display hex_digit_display_1 (.value(regs_bank_1_data_read_2));  // open: dp
  Clock clock_1 (.out(clock_1_out));
  Button button_1 (.out(button_1_out));
  LED led_1 (.in(control_v5_1_ula_enable));
  LED led_2 (.in(control_v5_1_write_enable));
  // Probe on control_v5_1_write_address
  // Probe on control_v5_1_read_addr
  // Probe on {control_v5_1_addr_out_4, control_v5_1_addr_out_3, control_v5_1_addr_out_2, control_v5_1_addr_out}
  LED led_3 (.in(control_v5_1_debug_fetch));
  LED led_4 (.in(reg16_file_1_memory_write));
  LED led_5 (.in(reg16_file_1_memory_read));
  LED #(.active("false")) led_6 (.in(control_v5_1_pclr_swap));
  LED #(.active("false")) led_7 (.in(control_v5_1_pcia_swap));
  LED led_8 (.in(ula_8_1_zero_flag));
  LED led_9 (.in(ula_8_1_negative_flag));
  LED led_10 (.in(ula_8_1_carry_flag));
  LED led_11 (.in(ula_8_1_overflow_flag));
  LED led_12 (.in(control_v5_1_flag_intmask));
  Hex_Digit_Display hex_digit_display_2 (.value(control_v5_1_addr_out_4));  // open: dp
  Hex_Digit_Display hex_digit_display_3 (.value(regs_bank_1_data_read));  // open: dp
  Hex_Digit_Display hex_digit_display_4 (.value(control_v5_1_addr_out_3));  // open: dp
  Hex_Digit_Display hex_digit_display_5 (.value(control_v5_1_addr_out_2));  // open: dp
  Hex_Digit_Display hex_digit_display_6 (.value(control_v5_1_addr_out));  // open: dp
  Hex_Digit_Display hex_digit_display_7 (.value(control_v5_1_debug_ins[7:4]));  // open: dp
  Hex_Digit_Display hex_digit_display_8 (.value(control_v5_1_debug_ins[3:0]));  // open: dp
  regs_bank regs_bank_1 (
    .DATA_WRITE({regs_bank_1_data_read_2, regs_bank_1_data_read}), .CLOCK(clock_1_out),
    .WRITE_ADDR(control_v5_1_write_address), .WR_ENABLE(control_v5_1_write_enable),
    .READ_ADDR(control_v5_1_read_addr), .DATA_READ({regs_bank_1_data_read_2, regs_bank_1_data_read}),
    .DEBUG({regs_bank_1_debug_7, regs_bank_1_debug_6, regs_bank_1_debug_5, regs_bank_1_debug_4, regs_bank_1_debug_3, regs_bank_1_debug_2, regs_bank_1_debug}));
  Hex_Digit_Display hex_digit_display_9 (.value(in_out_1_port_output_a_2));  // open: dp
  Hex_Digit_Display hex_digit_display_10 (.value(in_out_1_port_output_a));  // open: dp
  control_v5 control_v5_1 (
    .FLAG_ZERO(ula_8_1_zero_flag), .FLAG_CARRY(ula_8_1_carry_flag), .FLAG_NEGATIVE(ula_8_1_negative_flag),
    .FLAG_OVERFLOW(ula_8_1_overflow_flag), .IN({regs_bank_1_data_read_2, regs_bank_1_data_read}),
    .INT_REQUEST(int_request), .CLOCK(clock_1_out), .RESET(button_1_out), .PCLR_SWAP(control_v5_1_pclr_swap),
    .ADDR_OUT({control_v5_1_addr_out_4, control_v5_1_addr_out_3, control_v5_1_addr_out_2, control_v5_1_addr_out}),
    .READ_ADDR(control_v5_1_read_addr), .FLAG_INTMASK(control_v5_1_flag_intmask),
    .WRITE_ADDRESS(control_v5_1_write_address), .WRITE_ENABLE(control_v5_1_write_enable),
    .ULA_ENABLE(control_v5_1_ula_enable), .DEBUG_INS(control_v5_1_debug_ins),
    .DEBUG_FETCH(control_v5_1_debug_fetch), .PCIA_SWAP(control_v5_1_pcia_swap));
  Hex_Digit_Display hex_digit_display_11 (.value(in_out_1_port_output_b_2));  // open: dp
  memory memory_1 (
    .MEMORY_READ(reg16_file_1_memory_read), .CLOCK(clock_1_out), .MEMORY_WRITE(reg16_file_1_memory_write),
    .IN({regs_bank_1_data_read_2, regs_bank_1_data_read}),
    .ADDRESS({control_v5_1_addr_out_4, control_v5_1_addr_out_3, control_v5_1_addr_out_2, control_v5_1_addr_out}),
    .OUT({regs_bank_1_data_read_2, regs_bank_1_data_read}));
  Hex_Digit_Display hex_digit_display_12 (.value(in_out_1_port_output_b));  // open: dp
  in_out in_out_1 (
    .PORT_INPUT_D(PORT_D), .DATA_IN({regs_bank_1_data_read_2, regs_bank_1_data_read}), .CLOCK(clock_1_out),
    .RD_ADDR(control_v5_1_read_addr), .WR_ENABLE(control_v5_1_write_enable),
    .WR_ADDR(control_v5_1_write_address), .PORT_INPUT_C(PORT_C),
    .ADDR({control_v5_1_addr_out_4, control_v5_1_addr_out_3, control_v5_1_addr_out_2, control_v5_1_addr_out}),
    .PORT_OUTPUT_B({in_out_1_port_output_b_2, in_out_1_port_output_b}),
    .DATA_OUT({regs_bank_1_data_read_2, regs_bank_1_data_read}),
    .PORT_OUTPUT_A({in_out_1_port_output_a_2, in_out_1_port_output_a}));  // open: PORT_INPUT_B, PORT_INPUT_A, PORT_INPUT, PORT_OUTPUT_D, PORT_WRITE, PORT_READ, PORT_OUTPUT_C, PORT_ADDR, PORT_OUTPUT
  reg16 reg16_1 (
    .nINC(reg16_file_1_sp_inc), .nDEC(reg16_file_1_sp_dec), .nLOAD_HIGH(reg16_file_1_nselwritesph),
    .nADDR_SEL(reg16_file_1_naddr_sp), .nREAD_HIGH(reg16_file_1_nselreadsph),
    .nREAD_LOW(reg16_file_1_nselreadspl), .nLOAD_LOW(reg16_file_1_nselwritespl),
    .DATA_IN({regs_bank_1_data_read_2, regs_bank_1_data_read}),
    .DATA_OUT({regs_bank_1_data_read_2, regs_bank_1_data_read}),
    .ADDR({control_v5_1_addr_out_4, control_v5_1_addr_out_3, control_v5_1_addr_out_2, control_v5_1_addr_out}));
  ula_8 ula_8_1 (
    .INTMASK_FLAG(control_v5_1_flag_intmask), .WRITE_ADDR(control_v5_1_write_address),
    .WR_ENABLE(control_v5_1_write_enable), .DATA_IN({regs_bank_1_data_read_2, regs_bank_1_data_read}),
    .ULA_ENABLE(control_v5_1_ula_enable), .CLOCK(clock_1_out), .READ_ADDR(control_v5_1_read_addr),
    .DATA_OUT({regs_bank_1_data_read_2, regs_bank_1_data_read}), .ZERO_FLAG(ula_8_1_zero_flag),
    .CARRY_FLAG(ula_8_1_carry_flag), .OVERFLOW_FLAG(ula_8_1_overflow_flag),
    .NEGATIVE_FLAG(ula_8_1_negative_flag), .DEBUG_ACC(ula_8_1_debug_acc));
  reg16 reg16_2 (
    .nINC(reg16_file_1_mar_inc), .nDEC(1'b1), .nLOAD_HIGH(reg16_file_1_nselwritemarh),
    .nADDR_SEL(reg16_file_1_naddr_mar), .nREAD_HIGH(reg16_file_1_nselreadmarh),
    .nREAD_LOW(reg16_file_1_nselreadmarl), .nLOAD_LOW(reg16_file_1_nselwritemarl),
    .DATA_IN({regs_bank_1_data_read_2, regs_bank_1_data_read}),
    .DATA_OUT({regs_bank_1_data_read_2, regs_bank_1_data_read}),
    .ADDR({control_v5_1_addr_out_4, control_v5_1_addr_out_3, control_v5_1_addr_out_2, control_v5_1_addr_out}));
  Hex_Digit_Display hex_digit_display_13 (.value(ula_8_1_debug_acc[7:4]));  // open: dp
  Hex_Digit_Display hex_digit_display_14 (.value(ula_8_1_debug_acc[3:0]));  // open: dp
  reg16_file reg16_file_1 (
    .PCIA_SWAP(control_v5_1_pcia_swap), .PCLR_SWAP(control_v5_1_pclr_swap),
    .WR_ENABLE(control_v5_1_write_enable), .CLOCK(clock_1_out), .WRITE_ADDR(control_v5_1_write_address),
    .READ_ADDR(control_v5_1_read_addr), .nSelWrite0L(reg16_file_1_nselwrite0l),
    .nSelWrite0H(reg16_file_1_nselwrite0h), .nSelRead0L(reg16_file_1_nselread0l),
    .nSelRead0H(reg16_file_1_nselread0h), .nADDR_0(reg16_file_1_naddr_0), .INC_0(reg16_file_1_inc_0),
    .nSelWrite1L(reg16_file_1_nselwrite1l), .nSelWrite1H(reg16_file_1_nselwrite1h),
    .nSelRead1L(reg16_file_1_nselread1l), .nSelRead1H(reg16_file_1_nselread1h),
    .nADDR_1(reg16_file_1_naddr_1), .INC_1(reg16_file_1_inc_1), .nSelWrite2L(reg16_file_1_nselwrite2l),
    .nSelWrite2H(reg16_file_1_nselwrite2h), .nSelRead2L(reg16_file_1_nselread2l),
    .nSelRead2H(reg16_file_1_nselread2h), .nADDR_2(reg16_file_1_naddr_2), .INC_2(reg16_file_1_inc_2),
    .SP_DEC(reg16_file_1_sp_dec), .SP_INC(reg16_file_1_sp_inc), .nADDR_SP(reg16_file_1_naddr_sp),
    .MAR_INC(reg16_file_1_mar_inc), .nADDR_MAR(reg16_file_1_naddr_mar),
    .MEMORY_WRITE(reg16_file_1_memory_write), .nSelWriteSPL(reg16_file_1_nselwritespl),
    .nSelWriteSPH(reg16_file_1_nselwritesph), .nSelWriteMARL(reg16_file_1_nselwritemarl),
    .nSelWriteMARH(reg16_file_1_nselwritemarh), .MEMORY_READ(reg16_file_1_memory_read),
    .nSelReadSPL(reg16_file_1_nselreadspl), .nSelReadSPH(reg16_file_1_nselreadsph),
    .nSelReadMARL(reg16_file_1_nselreadmarl), .nSelReadMARH(reg16_file_1_nselreadmarh));
  reg16 reg16_3 (
    .nINC(reg16_file_1_inc_0), .nDEC(1'b1), .nLOAD_HIGH(reg16_file_1_nselwrite0h),
    .nADDR_SEL(reg16_file_1_naddr_0), .nREAD_HIGH(reg16_file_1_nselread0h),
    .nREAD_LOW(reg16_file_1_nselread0l), .nLOAD_LOW(reg16_file_1_nselwrite0l),
    .DATA_IN({regs_bank_1_data_read_2, regs_bank_1_data_read}),
    .DATA_OUT({regs_bank_1_data_read_2, regs_bank_1_data_read}),
    .ADDR({control_v5_1_addr_out_4, control_v5_1_addr_out_3, control_v5_1_addr_out_2, control_v5_1_addr_out}));
  reg16 reg16_4 (
    .nINC(reg16_file_1_inc_1), .nDEC(1'b1), .nLOAD_HIGH(reg16_file_1_nselwrite1h),
    .nADDR_SEL(reg16_file_1_naddr_1), .nREAD_HIGH(reg16_file_1_nselread1h),
    .nREAD_LOW(reg16_file_1_nselread1l), .nLOAD_LOW(reg16_file_1_nselwrite1l),
    .DATA_IN({regs_bank_1_data_read_2, regs_bank_1_data_read}),
    .DATA_OUT({regs_bank_1_data_read_2, regs_bank_1_data_read}),
    .ADDR({control_v5_1_addr_out_4, control_v5_1_addr_out_3, control_v5_1_addr_out_2, control_v5_1_addr_out}));
  Hex_Digit_Display hex_digit_display_15 (.value(regs_bank_1_debug[7:4]));  // open: dp
  Hex_Digit_Display hex_digit_display_16 (.value(regs_bank_1_debug[3:0]));  // open: dp
  Hex_Digit_Display hex_digit_display_17 (.value(regs_bank_1_debug_2[7:4]));  // open: dp
  Hex_Digit_Display hex_digit_display_18 (.value(regs_bank_1_debug_2[3:0]));  // open: dp
  Hex_Digit_Display hex_digit_display_19 (.value(regs_bank_1_debug_3[7:4]));  // open: dp
  Hex_Digit_Display hex_digit_display_20 (.value(regs_bank_1_debug_3[3:0]));  // open: dp
  Hex_Digit_Display hex_digit_display_21 (.value(regs_bank_1_debug_4[7:4]));  // open: dp
  Hex_Digit_Display hex_digit_display_22 (.value(regs_bank_1_debug_4[3:0]));  // open: dp
  Hex_Digit_Display hex_digit_display_23 (.value(regs_bank_1_debug_5[7:4]));  // open: dp
  Hex_Digit_Display hex_digit_display_24 (.value(regs_bank_1_debug_5[3:0]));  // open: dp
  Hex_Digit_Display hex_digit_display_25 (.value(regs_bank_1_debug_6[7:4]));  // open: dp
  Hex_Digit_Display hex_digit_display_26 (.value(regs_bank_1_debug_6[3:0]));  // open: dp
  Hex_Digit_Display hex_digit_display_27 (.value(regs_bank_1_debug_7[7:4]));  // open: dp
  Hex_Digit_Display hex_digit_display_28 (.value(regs_bank_1_debug_7[3:0]));  // open: dp
  reg16 reg16_5 (
    .nINC(reg16_file_1_inc_2), .nDEC(1'b1), .nLOAD_HIGH(reg16_file_1_nselwrite2h),
    .nADDR_SEL(reg16_file_1_naddr_2), .nREAD_HIGH(reg16_file_1_nselread2h),
    .nREAD_LOW(reg16_file_1_nselread2l), .nLOAD_LOW(reg16_file_1_nselwrite2l),
    .DATA_IN({regs_bank_1_data_read_2, regs_bank_1_data_read}),
    .DATA_OUT({regs_bank_1_data_read_2, regs_bank_1_data_read}),
    .ADDR({control_v5_1_addr_out_4, control_v5_1_addr_out_3, control_v5_1_addr_out_2, control_v5_1_addr_out}));

  // Notes on the sheet:
  //   DATA
  //   clock
  //   RESET
  //   ula_enable
  //   wr_enable
  //   wr_addr
  //   rd_addr
  //   addr
  //   fetch
  //   wr_mem
  //   rd_mem
  //   pc/lr swap
  //   pc/ia swap
  //   zero
  //   negative
  //   carry
  //   overflow
  //   intm
  //   ADDRESS
  //   INS
  //   PORT A
  //   PORT B
  //   SP
  //   MAR
  //   ACC
  //   PC/LR/IA
  //   PC/LR/IA
  //   A
  //   B
  //   C
  //   D
  //   E
  //   H
  //   L
  //   PC/LR/IA
endmodule

module regs_bank (
  input  [4:0] WRITE_ADDR,
  input  [4:0] READ_ADDR,
  input  WR_ENABLE,
  input  CLOCK,
  input  [7:0] DATA_WRITE,
  output [55:0] DEBUG,
  output [7:0] DATA_READ
);

  wire n74138_2_pin6, nSelReadA, nSelReadB, nSelReadC, nSelReadD, nSelReadE, nSelReadH, nSelReadL,
       nSelWriteA, nSelWriteB, nSelWriteC, nSelWriteD, nSelWriteE, nSelWriteH, nSelWriteL;

  _74244 u_74244_1 (
    .pin1(nSelReadA), .pin2(DEBUG[0]), .pin3(DATA_READ[7]), .pin4(DEBUG[1]), .pin5(DATA_READ[6]),
    .pin6(DEBUG[2]), .pin7(DATA_READ[5]), .pin8(DEBUG[3]), .pin9(DATA_READ[4]), .pin19(nSelReadA),
    .pin18(DATA_READ[0]), .pin17(DEBUG[7]), .pin16(DATA_READ[1]), .pin15(DEBUG[6]), .pin14(DATA_READ[2]),
    .pin13(DEBUG[5]), .pin12(DATA_READ[3]), .pin11(DEBUG[4]));
  _74377 u_74377_1 (
    .pin1(nSelWriteA), .pin2(DEBUG[0]), .pin3(DATA_WRITE[0]), .pin4(DATA_WRITE[1]), .pin5(DEBUG[1]),
    .pin6(DEBUG[2]), .pin7(DATA_WRITE[2]), .pin8(DATA_WRITE[3]), .pin9(DEBUG[3]), .pin19(DEBUG[7]),
    .pin18(DATA_WRITE[7]), .pin17(DATA_WRITE[6]), .pin16(DEBUG[6]), .pin15(DEBUG[5]), .pin14(DATA_WRITE[5]),
    .pin13(DATA_WRITE[4]), .pin12(DEBUG[4]), .pin11(CLOCK));
  _74138 u_74138_1 (
    .pin1(WRITE_ADDR[0]), .pin2(WRITE_ADDR[1]), .pin3(WRITE_ADDR[2]), .pin4(WRITE_ADDR[3]),
    .pin5(WRITE_ADDR[4]), .pin6(WR_ENABLE), .pin7(nSelWriteL), .pin14(nSelWriteA), .pin13(nSelWriteB),
    .pin12(nSelWriteC), .pin11(nSelWriteD), .pin10(nSelWriteE), .pin9(nSelWriteH));  // open: pin15
  _74377 u_74377_2 (
    .pin1(nSelWriteB), .pin2(DEBUG[8]), .pin3(DATA_WRITE[0]), .pin4(DATA_WRITE[1]), .pin5(DEBUG[9]),
    .pin6(DEBUG[10]), .pin7(DATA_WRITE[2]), .pin8(DATA_WRITE[3]), .pin9(DEBUG[11]), .pin19(DEBUG[15]),
    .pin18(DATA_WRITE[7]), .pin17(DATA_WRITE[6]), .pin16(DEBUG[14]), .pin15(DEBUG[13]),
    .pin14(DATA_WRITE[5]), .pin13(DATA_WRITE[4]), .pin12(DEBUG[12]), .pin11(CLOCK));
  _74244 u_74244_2 (
    .pin1(nSelReadB), .pin2(DEBUG[8]), .pin3(DATA_READ[7]), .pin4(DEBUG[9]), .pin5(DATA_READ[6]),
    .pin6(DEBUG[10]), .pin7(DATA_READ[5]), .pin8(DEBUG[11]), .pin9(DATA_READ[4]), .pin19(nSelReadB),
    .pin18(DATA_READ[0]), .pin17(DEBUG[15]), .pin16(DATA_READ[1]), .pin15(DEBUG[14]), .pin14(DATA_READ[2]),
    .pin13(DEBUG[13]), .pin12(DATA_READ[3]), .pin11(DEBUG[12]));
  _74138 u_74138_2 (
    .pin1(READ_ADDR[0]), .pin2(READ_ADDR[1]), .pin3(READ_ADDR[2]), .pin4(READ_ADDR[3]), .pin5(READ_ADDR[4]),
    .pin6(n74138_2_pin6), .pin7(nSelReadL), .pin14(nSelReadA), .pin13(nSelReadB), .pin12(nSelReadC),
    .pin11(nSelReadD), .pin10(nSelReadE), .pin9(nSelReadH));  // open: pin15
  _74377 u_74377_3 (
    .pin1(nSelWriteC), .pin2(DEBUG[16]), .pin3(DATA_WRITE[0]), .pin4(DATA_WRITE[1]), .pin5(DEBUG[17]),
    .pin6(DEBUG[18]), .pin7(DATA_WRITE[2]), .pin8(DATA_WRITE[3]), .pin9(DEBUG[19]), .pin19(DEBUG[23]),
    .pin18(DATA_WRITE[7]), .pin17(DATA_WRITE[6]), .pin16(DEBUG[22]), .pin15(DEBUG[21]),
    .pin14(DATA_WRITE[5]), .pin13(DATA_WRITE[4]), .pin12(DEBUG[20]), .pin11(CLOCK));
  _74244 u_74244_3 (
    .pin1(nSelReadC), .pin2(DEBUG[16]), .pin3(DATA_READ[7]), .pin4(DEBUG[17]), .pin5(DATA_READ[6]),
    .pin6(DEBUG[18]), .pin7(DATA_READ[5]), .pin8(DEBUG[19]), .pin9(DATA_READ[4]), .pin19(nSelReadC),
    .pin18(DATA_READ[0]), .pin17(DEBUG[23]), .pin16(DATA_READ[1]), .pin15(DEBUG[22]), .pin14(DATA_READ[2]),
    .pin13(DEBUG[21]), .pin12(DATA_READ[3]), .pin11(DEBUG[20]));
  _74377 u_74377_4 (
    .pin1(nSelWriteD), .pin2(DEBUG[24]), .pin3(DATA_WRITE[0]), .pin4(DATA_WRITE[1]), .pin5(DEBUG[25]),
    .pin6(DEBUG[26]), .pin7(DATA_WRITE[2]), .pin8(DATA_WRITE[3]), .pin9(DEBUG[27]), .pin19(DEBUG[31]),
    .pin18(DATA_WRITE[7]), .pin17(DATA_WRITE[6]), .pin16(DEBUG[30]), .pin15(DEBUG[29]),
    .pin14(DATA_WRITE[5]), .pin13(DATA_WRITE[4]), .pin12(DEBUG[28]), .pin11(CLOCK));
  _74244 u_74244_4 (
    .pin1(nSelReadD), .pin2(DEBUG[24]), .pin3(DATA_READ[7]), .pin4(DEBUG[25]), .pin5(DATA_READ[6]),
    .pin6(DEBUG[26]), .pin7(DATA_READ[5]), .pin8(DEBUG[27]), .pin9(DATA_READ[4]), .pin19(nSelReadD),
    .pin18(DATA_READ[0]), .pin17(DEBUG[31]), .pin16(DATA_READ[1]), .pin15(DEBUG[30]), .pin14(DATA_READ[2]),
    .pin13(DEBUG[29]), .pin12(DATA_READ[3]), .pin11(DEBUG[28]));
  _74244 u_74244_5 (
    .pin1(nSelReadE), .pin2(DEBUG[32]), .pin3(DATA_READ[7]), .pin4(DEBUG[33]), .pin5(DATA_READ[6]),
    .pin6(DEBUG[34]), .pin7(DATA_READ[5]), .pin8(DEBUG[35]), .pin9(DATA_READ[4]), .pin19(nSelReadE),
    .pin18(DATA_READ[0]), .pin17(DEBUG[39]), .pin16(DATA_READ[1]), .pin15(DEBUG[38]), .pin14(DATA_READ[2]),
    .pin13(DEBUG[37]), .pin12(DATA_READ[3]), .pin11(DEBUG[36]));
  _74377 u_74377_5 (
    .pin1(nSelWriteE), .pin2(DEBUG[32]), .pin3(DATA_WRITE[0]), .pin4(DATA_WRITE[1]), .pin5(DEBUG[33]),
    .pin6(DEBUG[34]), .pin7(DATA_WRITE[2]), .pin8(DATA_WRITE[3]), .pin9(DEBUG[35]), .pin19(DEBUG[39]),
    .pin18(DATA_WRITE[7]), .pin17(DATA_WRITE[6]), .pin16(DEBUG[38]), .pin15(DEBUG[37]),
    .pin14(DATA_WRITE[5]), .pin13(DATA_WRITE[4]), .pin12(DEBUG[36]), .pin11(CLOCK));
  _74377 u_74377_6 (
    .pin1(nSelWriteH), .pin2(DEBUG[40]), .pin3(DATA_WRITE[0]), .pin4(DATA_WRITE[1]), .pin5(DEBUG[41]),
    .pin6(DEBUG[42]), .pin7(DATA_WRITE[2]), .pin8(DATA_WRITE[3]), .pin9(DEBUG[43]), .pin19(DEBUG[47]),
    .pin18(DATA_WRITE[7]), .pin17(DATA_WRITE[6]), .pin16(DEBUG[46]), .pin15(DEBUG[45]),
    .pin14(DATA_WRITE[5]), .pin13(DATA_WRITE[4]), .pin12(DEBUG[44]), .pin11(CLOCK));
  _74244 u_74244_6 (
    .pin1(nSelReadH), .pin2(DEBUG[40]), .pin3(DATA_READ[7]), .pin4(DEBUG[41]), .pin5(DATA_READ[6]),
    .pin6(DEBUG[42]), .pin7(DATA_READ[5]), .pin8(DEBUG[43]), .pin9(DATA_READ[4]), .pin19(nSelReadH),
    .pin18(DATA_READ[0]), .pin17(DEBUG[47]), .pin16(DATA_READ[1]), .pin15(DEBUG[46]), .pin14(DATA_READ[2]),
    .pin13(DEBUG[45]), .pin12(DATA_READ[3]), .pin11(DEBUG[44]));
  _74377 u_74377_7 (
    .pin1(nSelWriteL), .pin2(DEBUG[48]), .pin3(DATA_WRITE[0]), .pin4(DATA_WRITE[1]), .pin5(DEBUG[49]),
    .pin6(DEBUG[50]), .pin7(DATA_WRITE[2]), .pin8(DATA_WRITE[3]), .pin9(DEBUG[51]), .pin19(DEBUG[55]),
    .pin18(DATA_WRITE[7]), .pin17(DATA_WRITE[6]), .pin16(DEBUG[54]), .pin15(DEBUG[53]),
    .pin14(DATA_WRITE[5]), .pin13(DATA_WRITE[4]), .pin12(DEBUG[52]), .pin11(CLOCK));
  _74244 u_74244_7 (
    .pin1(nSelReadL), .pin2(DEBUG[48]), .pin3(DATA_READ[7]), .pin4(DEBUG[49]), .pin5(DATA_READ[6]),
    .pin6(DEBUG[50]), .pin7(DATA_READ[5]), .pin8(DEBUG[51]), .pin9(DATA_READ[4]), .pin19(nSelReadL),
    .pin18(DATA_READ[0]), .pin17(DEBUG[55]), .pin16(DATA_READ[1]), .pin15(DEBUG[54]), .pin14(DATA_READ[2]),
    .pin13(DEBUG[53]), .pin12(DATA_READ[3]), .pin11(DEBUG[52]));
  // also tied to VCC on the sheet: n74138_2_pin6

  // Other names for the same wires on the sheet: data_out_0 = DATA_READ[0]; data_out_1 = DATA_READ[1];
  //   data_out_2 = DATA_READ[2]; data_out_3 = DATA_READ[3]; data_out_4 = DATA_READ[4]; data_out_5 = DATA_READ[5];
  //   data_out_6 = DATA_READ[6]; data_out_7 = DATA_READ[7]; data_in_0 = DATA_WRITE[0]; data_in_1 = DATA_WRITE[1];
  //   data_in_2 = DATA_WRITE[2]; data_in_3 = DATA_WRITE[3]; data_in_4 = DATA_WRITE[4]; data_in_5 = DATA_WRITE[5];
  //   data_in_6 = DATA_WRITE[6]; data_in_7 = DATA_WRITE[7]; DEBUG_A[7:0] = DEBUG[7:0]; DEBUG_B[7:0] = DEBUG[15:8];
  //   DEBUG_C[7:0] = DEBUG[23:16]; DEBUG_D[7:0] = DEBUG[31:24]; DEBUG_E[7:0] = DEBUG[39:32];
  //   DEBUG_H[7:0] = DEBUG[47:40]; DEBUG_L[7:0] = DEBUG[55:48]

  // Notes on the sheet:
  //   REG A
  //   REG B
  //   REG C
  //   REG D
  //   REG E
  //   REG H
  //   REG L
endmodule

module ula (
  input  ULA_ENABLE,
  input  [3:0] WRITE_ADDR,
  input  [3:0] READ_ADDR,
  input  WR_ENABLE,
  input  CLOCK,
  input  [7:0] DATA_IN,
  output [7:0] DATA_OUT,
  output ZERO_FLAG,
  output CARRY_FLAG,
  output OVERFLOW_FLAG,
  output NEGATIVE_FLAG,
  output INTMASK_FLAG
);

  wire acc_bit_4, acc_bit_7, and_1_out, and_2_out, and_3_out, and_4_out, carry_result, clr_cf, clr_if,
       flags_write, intmask_result, invert_lower_bus, invert_ula_bus, invert_upper_bus, n7400_1_pin11,
       n7400_1_pin12, n7400_1_pin13, n7404_1_pin2, n7404_1_pin4, n7404_1_pin6, n7404_1_pin10, n7404_1_pin12,
       n7404_2_pin2, n7404_2_pin4, n7404_2_pin6, n7404_2_pin8, n7404_2_pin10, n7404_2_pin12, n7408_1_pin3,
       n7408_1_pin6, n7408_1_pin8, n7408_1_pin11, n7432_2_pin3, n7432_2_pin6, n7474_1_pin3, n7474_2_pin13,
       n7474_3_pin1, n7474_5_pin1, n7486_1_pin3, n7486_1_pin6, n7486_1_pin8, n7486_1_pin11, n7486_3_pin3,
       n7486_3_pin6, n7486_3_pin8, n7486_3_pin11, n7486_5_pin3, n7486_5_pin5, n7486_5_pin9, n74125_1_pin2,
       n74125_1_pin5, n74125_1_pin9, n74125_1_pin12, n74125_3_pin4, n74125_3_pin13, n74125_4_pin3,
       n74125_4_pin6, n74125_4_pin8, n74125_4_pin11, n74125_8_pin1, n74125_8_pin4, n74125_8_pin12,
       n74125_9_pin2, n74125_9_pin12, n74138_1_pin7, n74138_3_pin7, n74138_3_pin9, n74138_3_pin11,
       n74138_3_pin12, n74138_3_pin13, n74138_3_pin14, n74138_3_pin15, n74138_4_pin4, n74138_4_pin13,
       n74138_4_pin14, n74138_4_pin15, n74157_1_pin4, n74157_1_pin7, n74157_1_pin9, n74157_1_pin12,
       n74157_1_pin15, n74157_2_pin4, n74157_2_pin7, n74157_2_pin9, n74157_2_pin12, n74157_2_pin15,
       n74157_3_pin4, n74157_3_pin7, n74157_3_pin9, n74157_3_pin12, n74157_3_pin15, n74175_1_pin1,
       n74175_1_pin7, n74175_1_pin10, n74175_2_pin1, n74175_2_pin2, n74175_2_pin7, n74175_2_pin10,
       n74175_2_pin15, n74244_4_pin17, n74283_1_pin1, n74283_1_pin4, n74283_1_pin9, n74283_1_pin10,
       n74283_1_pin13, negative_result, not_1_out, not_3_out, not_4_out, not_5_out, or_3_out, or_6_out,
       or_7_out, or_8_out, or_9_out, or_11_out, overflow_result, read_acc, read_psw, rotate, save_acc,
       save_flags, select_adder, select_left_shifter, select_logic, select_nibble_high, select_nibble_low,
       select_right_shifter, select_sx, select_xor, set_cf, set_if, ula_sync, zero_result;
  wire [2:0] ula_bus;
  wire [3:0] lower_bus, upper_bus;

  LED #(.active("false")) led_1 (.in(select_xor));
  LED #(.active("false")) led_2 (.in(select_right_shifter));
  LED #(.active("false")) led_3 (.in(select_logic));
  LED #(.active("false")) led_4 (.in(select_adder));
  LED #(.active("false")) led_5 (.in(select_left_shifter));
  LED #(.active("false")) led_6 (.in(select_sx));
  LED led_7 (.in(rotate));
  LED led_8 (.in(save_flags));
  _74138 u_74138_1 (
    .pin1(WRITE_ADDR[0]), .pin2(WRITE_ADDR[1]), .pin3(WRITE_ADDR[2]), .pin4(WRITE_ADDR[3]),
    .pin5(WRITE_ADDR[3]), .pin6(WR_ENABLE), .pin7(n74138_1_pin7), .pin9(flags_write));  // open: pin15, pin14, pin13, pin12, pin11, pin10
  _7486 u_7486_1 (
    .pin1(ula_bus[0]), .pin2(invert_ula_bus), .pin3(n7486_1_pin3), .pin4(ula_bus[1]), .pin5(invert_ula_bus),
    .pin6(n7486_1_pin6), .pin13(negative_result), .pin12(invert_ula_bus), .pin11(n7486_1_pin11),
    .pin10(ula_bus[2]), .pin9(invert_ula_bus), .pin8(n7486_1_pin8));
  _74283 u_74283_1 (
    .pin1(n74283_1_pin1), .pin2(lower_bus[1]), .pin3(upper_bus[1]), .pin4(n74283_1_pin4),
    .pin5(upper_bus[0]), .pin6(lower_bus[0]), .pin7(CARRY_FLAG), .pin15(lower_bus[2]), .pin14(upper_bus[2]),
    .pin13(n74283_1_pin13), .pin12(upper_bus[3]), .pin11(lower_bus[3]), .pin10(n74283_1_pin10),
    .pin9(n74283_1_pin9));
  _74125 u_74125_1 (
    .pin1(select_logic), .pin2(n74125_1_pin2), .pin3(ula_bus[0]), .pin4(select_logic), .pin5(n74125_1_pin5),
    .pin6(ula_bus[1]), .pin13(select_logic), .pin12(n74125_1_pin12), .pin11(negative_result),
    .pin10(select_logic), .pin9(n74125_1_pin9), .pin8(ula_bus[2]));
  _74125 u_74125_2 (
    .pin1(select_left_shifter), .pin2(CARRY_FLAG), .pin3(ula_bus[0]), .pin4(select_left_shifter),
    .pin5(upper_bus[0]), .pin6(ula_bus[1]), .pin13(select_left_shifter), .pin12(upper_bus[2]),
    .pin11(negative_result), .pin10(select_left_shifter), .pin9(upper_bus[1]), .pin8(ula_bus[2]));
  LED led_9 (.in(invert_upper_bus));
  LED led_10 (.in(invert_ula_bus));
  LED led_11 (.in(invert_lower_bus));
  LED #(.active("false")) led_12 (.in(set_cf));
  LED #(.active("false")) led_13 (.in(clr_cf));
  LED #(.active("false")) led_14 (.in(set_if));
  LED #(.active("false")) led_15 (.in(clr_if));
  LED led_16 (.in(save_acc));
  _74157 u_74157_1 (
    .pin1(select_nibble_low), .pin2(DATA_IN[0]), .pin3(DATA_IN[4]), .pin4(n74157_1_pin4), .pin5(DATA_IN[1]),
    .pin6(DATA_IN[5]), .pin7(n74157_1_pin7), .pin15(n74157_1_pin15), .pin14(DATA_IN[3]), .pin13(DATA_IN[7]),
    .pin12(n74157_1_pin12), .pin11(DATA_IN[2]), .pin10(DATA_IN[6]), .pin9(n74157_1_pin9));
  not not_1 (not_1_out, n74138_1_pin7);
  _74157 u_74157_2 (
    .pin1(n74138_1_pin7), .pin2(DATA_IN[0]), .pin3(n7486_1_pin3), .pin4(n74157_2_pin4), .pin5(DATA_IN[1]),
    .pin6(n7486_1_pin6), .pin7(n74157_2_pin7), .pin15(n74157_2_pin15), .pin14(DATA_IN[3]),
    .pin13(n7486_1_pin11), .pin12(n74157_2_pin12), .pin11(DATA_IN[2]), .pin10(n7486_1_pin8),
    .pin9(n74157_2_pin9));
  _74157 u_74157_3 (
    .pin1(n74138_1_pin7), .pin2(DATA_IN[4]), .pin3(n7486_1_pin3), .pin4(n74157_3_pin4), .pin5(DATA_IN[5]),
    .pin6(n7486_1_pin6), .pin7(n74157_3_pin7), .pin15(n74157_3_pin15), .pin14(DATA_IN[7]),
    .pin13(n7486_1_pin11), .pin12(n74157_3_pin12), .pin11(DATA_IN[6]), .pin10(n7486_1_pin8),
    .pin9(n74157_3_pin9));
  _74244 u_74244_1 (
    .pin1(flags_write), .pin2(DATA_IN[0]), .pin4(DATA_IN[1]), .pin6(DATA_IN[2]), .pin8(DATA_IN[3]),
    .pin9(intmask_result), .pin19(flags_write), .pin18(zero_result), .pin16(carry_result),
    .pin14(overflow_result), .pin12(negative_result), .pin11(DATA_IN[4]));  // open: pin3, pin5, pin7, pin17, pin15, pin13
  _7432 u_7432_1 (
    .pin1(upper_bus[0]), .pin2(lower_bus[0]), .pin3(n74125_1_pin2), .pin4(upper_bus[1]), .pin5(lower_bus[1]),
    .pin6(n74125_1_pin5), .pin13(upper_bus[3]), .pin12(lower_bus[3]), .pin11(n74125_1_pin12),
    .pin10(upper_bus[2]), .pin9(lower_bus[2]), .pin8(n74125_1_pin9));
  _74125 u_74125_3 (
    .pin1(select_left_shifter), .pin2(upper_bus[3]), .pin3(carry_result), .pin4(n74125_3_pin4),
    .pin13(n74125_3_pin13), .pin12(acc_bit_7));  // open: pin5, pin6, pin11, pin10, pin9, pin8
  _7474 u_7474_1 (
    .pin1(ULA_ENABLE), .pin2(select_nibble_high), .pin3(n7474_1_pin3), .pin5(select_nibble_low),
    .pin6(select_nibble_high));  // open: pin4, pin13, pin12, pin11, pin10, pin9, pin8
  not not_2 (n7474_1_pin3, n7408_1_pin6);
  _7408 u_7408_1 (
    .pin1(not_1_out), .pin2(CLOCK), .pin3(n7408_1_pin3), .pin4(CLOCK), .pin5(save_acc), .pin6(n7408_1_pin6),
    .pin13(n7408_1_pin6), .pin12(select_nibble_low), .pin11(n7408_1_pin11), .pin10(n7408_1_pin6),
    .pin9(select_nibble_high), .pin8(n7408_1_pin8));
  _7486 u_7486_2 (
    .pin1(invert_lower_bus), .pin2(n74157_1_pin4), .pin3(lower_bus[0]), .pin4(invert_lower_bus),
    .pin5(n74157_1_pin7), .pin6(lower_bus[1]), .pin13(n74157_1_pin12), .pin12(invert_lower_bus),
    .pin11(lower_bus[3]), .pin10(n74157_1_pin9), .pin9(invert_lower_bus), .pin8(lower_bus[2]));
  _74244 u_74244_2 (
    .pin1(select_adder), .pin2(n74283_1_pin4), .pin4(n74283_1_pin1), .pin6(n74283_1_pin13),
    .pin7(carry_result), .pin8(n74283_1_pin10), .pin19(select_adder), .pin18(ula_bus[0]), .pin16(ula_bus[1]),
    .pin14(ula_bus[2]), .pin13(n74283_1_pin9), .pin12(negative_result));  // open: pin3, pin5, pin9, pin17, pin15, pin11
  or or_1 (n74125_3_pin4, rotate, select_nibble_high);
  or or_2 (n74125_3_pin13, rotate, select_nibble_low);
  _7432 u_7432_2 (
    .pin1(n7408_1_pin3), .pin2(n7408_1_pin11), .pin3(n7432_2_pin3), .pin4(n7408_1_pin3), .pin5(n7408_1_pin8),
    .pin6(n7432_2_pin6));  // open: pin13, pin12, pin11, pin10, pin9, pin8
  _74175 u_74175_1 (
    .pin1(n74175_1_pin1), .pin2(acc_bit_4), .pin4(n74157_3_pin4), .pin5(n74157_3_pin7), .pin7(n74175_1_pin7),
    .pin15(acc_bit_7), .pin13(n74157_3_pin12), .pin12(n74157_3_pin9), .pin10(n74175_1_pin10),
    .pin9(n7432_2_pin3));  // open: pin3, pin6, pin14, pin11
  _74175 u_74175_2 (
    .pin1(n74175_2_pin1), .pin2(n74175_2_pin2), .pin4(n74157_2_pin4), .pin5(n74157_2_pin7),
    .pin7(n74175_2_pin7), .pin15(n74175_2_pin15), .pin13(n74157_2_pin12), .pin12(n74157_2_pin9),
    .pin10(n74175_2_pin10), .pin9(n7432_2_pin6));  // open: pin3, pin6, pin14, pin11
  _74125 u_74125_4 (
    .pin1(select_nibble_low), .pin2(n74175_2_pin2), .pin3(n74125_4_pin3), .pin4(select_nibble_low),
    .pin5(n74175_2_pin7), .pin6(n74125_4_pin6), .pin13(select_nibble_low), .pin12(n74175_2_pin15),
    .pin11(n74125_4_pin11), .pin10(select_nibble_low), .pin9(n74175_2_pin10), .pin8(n74125_4_pin8));
  _74125 u_74125_5 (
    .pin1(select_nibble_high), .pin2(acc_bit_4), .pin3(n74125_4_pin3), .pin4(select_nibble_high),
    .pin5(n74175_1_pin7), .pin6(n74125_4_pin6), .pin13(select_nibble_high), .pin12(acc_bit_7),
    .pin11(n74125_4_pin11), .pin10(select_nibble_high), .pin9(n74175_1_pin10), .pin8(n74125_4_pin8));
  not not_3 (not_3_out, flags_write);
  and and_1 (and_1_out, CLOCK, not_3_out);
  _74244 u_74244_3 (
    .pin1(read_acc), .pin2(n74175_2_pin2), .pin3(DATA_OUT[7]), .pin4(n74175_2_pin7), .pin5(DATA_OUT[6]),
    .pin6(n74175_2_pin10), .pin7(DATA_OUT[5]), .pin8(n74175_2_pin15), .pin9(DATA_OUT[4]), .pin19(read_acc),
    .pin18(DATA_OUT[0]), .pin17(acc_bit_7), .pin16(DATA_OUT[1]), .pin15(n74175_1_pin10), .pin14(DATA_OUT[2]),
    .pin13(n74175_1_pin7), .pin12(DATA_OUT[3]), .pin11(acc_bit_4));
  or or_3 (or_3_out, not_3_out, save_flags);
  _7486 u_7486_3 (
    .pin1(upper_bus[0]), .pin2(lower_bus[0]), .pin3(n7486_3_pin3), .pin4(upper_bus[1]), .pin5(lower_bus[1]),
    .pin6(n7486_3_pin6), .pin13(lower_bus[3]), .pin12(upper_bus[3]), .pin11(n7486_3_pin11),
    .pin10(lower_bus[2]), .pin9(upper_bus[2]), .pin8(n7486_3_pin8));
  not not_4 (not_4_out, ULA_ENABLE);
  _7486 u_7486_4 (
    .pin1(n74125_4_pin3), .pin2(invert_upper_bus), .pin3(upper_bus[0]), .pin4(n74125_4_pin6),
    .pin5(invert_upper_bus), .pin6(upper_bus[1]), .pin13(n74125_4_pin11), .pin12(invert_upper_bus),
    .pin11(upper_bus[3]), .pin10(n74125_4_pin8), .pin9(invert_upper_bus), .pin8(upper_bus[2]));
  and and_2 (and_2_out, or_3_out, CLOCK);
  _74125 u_74125_6 (
    .pin1(select_xor), .pin2(n7486_3_pin3), .pin3(ula_bus[0]), .pin4(select_xor), .pin5(n7486_3_pin6),
    .pin6(ula_bus[1]), .pin13(select_xor), .pin12(n7486_3_pin11), .pin11(negative_result),
    .pin10(select_xor), .pin9(n7486_3_pin8), .pin8(ula_bus[2]));
  _74125 u_74125_7 (
    .pin1(select_right_shifter), .pin2(upper_bus[1]), .pin3(ula_bus[0]), .pin4(select_right_shifter),
    .pin5(upper_bus[2]), .pin6(ula_bus[1]), .pin13(select_right_shifter), .pin10(select_right_shifter),
    .pin9(upper_bus[3]), .pin8(ula_bus[2]));  // open: pin12, pin11
  _74138 u_74138_2 (
    .pin1(READ_ADDR[0]), .pin2(READ_ADDR[1]), .pin3(READ_ADDR[2]), .pin4(READ_ADDR[3]), .pin5(READ_ADDR[3]),
    .pin6(not_4_out), .pin7(read_acc), .pin9(read_psw));  // open: pin15, pin14, pin13, pin12, pin11, pin10
  _7474 u_7474_2 (
    .pin1(clr_cf), .pin2(carry_result), .pin3(and_2_out), .pin4(set_cf), .pin5(CARRY_FLAG),
    .pin13(n7474_2_pin13), .pin12(overflow_result), .pin11(and_2_out), .pin10(n7474_2_pin13),
    .pin9(OVERFLOW_FLAG));  // open: pin6, pin8
  _7474 u_7474_3 (
    .pin1(n7474_3_pin1), .pin2(zero_result), .pin3(and_2_out), .pin4(n7474_3_pin1), .pin5(ZERO_FLAG),
    .pin13(n7474_3_pin1), .pin12(negative_result), .pin11(and_2_out), .pin10(n7474_3_pin1),
    .pin9(NEGATIVE_FLAG));  // open: pin6, pin8
  _7474 u_7474_4 (
    .pin1(clr_if), .pin2(intmask_result), .pin3(and_1_out), .pin4(set_if), .pin5(INTMASK_FLAG));  // open: pin6, pin13, pin12, pin11, pin10, pin9, pin8
  and and_3 (and_3_out, ula_sync, select_nibble_high);
  _74125 u_74125_8 (
    .pin1(n74125_8_pin1), .pin2(upper_bus[0]), .pin3(carry_result), .pin4(n74125_8_pin4), .pin5(CARRY_FLAG),
    .pin6(carry_result), .pin13(n74125_8_pin4), .pin12(n74125_8_pin12), .pin11(negative_result),
    .pin10(n74125_8_pin1), .pin9(acc_bit_4), .pin8(negative_result));
  _7474 u_7474_5 (
    .pin1(n7474_5_pin1), .pin2(CARRY_FLAG), .pin3(and_3_out), .pin4(n7474_5_pin1), .pin5(n74125_8_pin12));  // open: pin6, pin13, pin12, pin11, pin10, pin9, pin8
  or or_4 (n74125_8_pin4, select_right_shifter, select_nibble_high);
  or or_5 (n74125_8_pin1, select_right_shifter, select_nibble_low);
  _74244 u_74244_4 (
    .pin1(read_psw), .pin2(ZERO_FLAG), .pin3(DATA_OUT[7]), .pin4(CARRY_FLAG), .pin5(DATA_OUT[6]),
    .pin6(OVERFLOW_FLAG), .pin7(DATA_OUT[5]), .pin8(NEGATIVE_FLAG), .pin9(DATA_OUT[4]), .pin19(read_psw),
    .pin18(DATA_OUT[0]), .pin17(n74244_4_pin17), .pin16(DATA_OUT[1]), .pin15(n74244_4_pin17),
    .pin14(DATA_OUT[2]), .pin13(n74244_4_pin17), .pin12(DATA_OUT[3]), .pin11(INTMASK_FLAG));
  not not_5 (not_5_out, save_flags);
  _74125 u_74125_9 (
    .pin1(not_5_out), .pin2(n74125_9_pin2), .pin3(zero_result), .pin13(not_5_out), .pin12(n74125_9_pin12),
    .pin11(overflow_result));  // open: pin4, pin5, pin6, pin10, pin9, pin8
  not not_6 (n74125_9_pin2, or_6_out);
  _74138 u_74138_3 (
    .pin1(WRITE_ADDR[0]), .pin2(WRITE_ADDR[1]), .pin3(WRITE_ADDR[2]), .pin4(WRITE_ADDR[3]),
    .pin5(WRITE_ADDR[3]), .pin6(ULA_ENABLE), .pin7(n74138_3_pin7), .pin15(n74138_3_pin15),
    .pin14(n74138_3_pin14), .pin13(n74138_3_pin13), .pin12(n74138_3_pin12), .pin11(n74138_3_pin11),
    .pin10(select_xor), .pin9(n74138_3_pin9));
  _74138 u_74138_4 (
    .pin1(WRITE_ADDR[0]), .pin2(WRITE_ADDR[1]), .pin3(WRITE_ADDR[2]), .pin4(n74138_4_pin4),
    .pin5(n74138_4_pin4), .pin6(ULA_ENABLE), .pin7(clr_if), .pin15(n74138_4_pin15), .pin14(n74138_4_pin14),
    .pin13(n74138_4_pin13), .pin12(select_sx), .pin11(set_cf), .pin10(clr_cf), .pin9(set_if));
  or or_6 (or_6_out, and_4_out, negative_result, ula_bus[2], ula_bus[1], ula_bus[0]);
  _7400 u_7400_1 (
    .pin13(n7400_1_pin13), .pin12(n7400_1_pin12), .pin11(n7400_1_pin11));  // open: pin1, pin2, pin3, pin4, pin5, pin6, pin10, pin9, pin8
  _7486 u_7486_5 (
    .pin1(lower_bus[3]), .pin2(upper_bus[3]), .pin3(n7486_5_pin3), .pin4(n7486_5_pin3), .pin5(n7486_5_pin5),
    .pin6(n7400_1_pin13), .pin13(negative_result), .pin12(carry_result), .pin11(n7400_1_pin12),
    .pin10(n7400_1_pin11), .pin9(n7486_5_pin9), .pin8(n74125_9_pin12));
  _7404 u_7404_1 (
    .pin1(n74138_3_pin15), .pin2(n7404_1_pin2), .pin3(n74138_3_pin14), .pin4(n7404_1_pin4),
    .pin5(n74138_3_pin13), .pin6(n7404_1_pin6), .pin13(select_xor), .pin12(n7404_1_pin12),
    .pin11(n74138_3_pin11), .pin10(n7404_1_pin10), .pin9(n74138_3_pin12), .pin8(invert_upper_bus));
  _7404 u_7404_2 (
    .pin1(n74138_3_pin9), .pin2(n7404_2_pin2), .pin3(n74138_3_pin7), .pin4(n7404_2_pin4),
    .pin5(n74138_4_pin15), .pin6(n7404_2_pin6), .pin13(select_sx), .pin12(n7404_2_pin12),
    .pin11(n74138_4_pin13), .pin10(n7404_2_pin10), .pin9(n74138_4_pin14), .pin8(n7404_2_pin8));
  and and_4 (and_4_out, select_nibble_low, ~ZERO_FLAG);  // AND_Gate
  or or_7 (or_7_out, n7404_1_pin2, n7404_1_pin4, n7404_1_pin6);
  or or_8 (or_8_out, n7404_2_pin6, n7404_2_pin10);
  or or_9 (or_9_out, n7404_2_pin4, n7404_2_pin8);
  or or_10 (rotate, n7404_2_pin10, n7404_2_pin8);
  or or_11 (or_11_out, invert_upper_bus, n7404_1_pin10, n7404_2_pin2);
  _7404 u_7404_3 (
    .pin1(or_7_out), .pin2(select_adder), .pin3(or_11_out), .pin4(select_logic), .pin5(or_8_out),
    .pin6(select_left_shifter), .pin13(WRITE_ADDR[3]), .pin12(n74138_4_pin4), .pin9(or_9_out),
    .pin8(select_right_shifter));  // open: pin11, pin10
  or or_12 (save_acc, n7404_2_pin10, n7404_2_pin8, n7404_2_pin6, n7404_2_pin4, n7404_2_pin2, n7404_1_pin12, n7404_1_pin10, invert_upper_bus, n7404_1_pin4, n7404_1_pin2, n7404_2_pin12);
  or or_13 (invert_ula_bus, invert_upper_bus, n7404_2_pin2);
  or or_14 (invert_lower_bus, invert_upper_bus, n7404_1_pin6, n7404_1_pin4);
  or or_15 (save_flags, n7404_1_pin6, save_acc);
  // also tied to GND on the sheet: {n74157_1_pin15, n74157_2_pin15, n74157_3_pin15, n74244_4_pin17}
  // also tied to VCC on the sheet: {n74175_1_pin1, n74175_2_pin1, n7474_3_pin1, n7474_2_pin13, n7474_5_pin1, n7486_5_pin5, n7486_5_pin9}

  // Other names for the same wires on the sheet: ula_addr[3:0] = WRITE_ADDR; ula_bus[3] = negative_result

  // Notes on the sheet:
  //   LOGIC
  //   LEFT SHIFTER
  //   ADDER
  //   add
  //   sub
  //   cmp
  //   and
  //   or
  //   xor
  //   not
  //   shr
  //   shl
  //   ror
  //   rol
  //   sx
  //   setcf
  //   clrcf
  //   setif
  //   clrif
endmodule

module sp_reg (
  input  [7:0] DATA_IN,
  input  nADDR_SEL,
  input  INC,
  input  DEC,
  input  [4:0] RD_ADDR,
  input  CLOCK,
  input  WR_ENABLE,
  input  [4:0] WR_ADDR,
  output [7:0] DATA_OUT,
  output [15:0] ADDR
);

  wire count_0, count_1, count_2, count_3, count_4, count_5, count_6, count_7, count_8, count_9, count_10,
       count_11, count_12, count_13, count_14, count_15, LOAD_HIGH, LOAD_LOW, n7404_1_pin6, n74138_1_pin4,
       n74138_2_pin4, n74138_2_pin5, n74193_1_pin4, n74193_1_pin5, n74193_2_pin4, n74193_2_pin5,
       n74193_3_pin4, n74193_3_pin5, n74193_4_pin4, n74193_4_pin5, n_clock, READ_HIGH, READ_LOW;

  _74193 u_74193_1 (
    .pin1(DATA_IN[5]), .pin2(count_13), .pin3(count_12), .pin4(n74193_1_pin4), .pin5(n74193_1_pin5),
    .pin6(count_14), .pin7(count_15), .pin15(DATA_IN[4]), .pin11(LOAD_HIGH), .pin10(DATA_IN[6]),
    .pin9(DATA_IN[7]));  // open: pin14, pin13, pin12
  _74193 u_74193_2 (
    .pin1(DATA_IN[1]), .pin2(count_9), .pin3(count_8), .pin4(n74193_2_pin4), .pin5(n74193_2_pin5),
    .pin6(count_10), .pin7(count_11), .pin15(DATA_IN[0]), .pin13(n74193_1_pin4), .pin12(n74193_1_pin5),
    .pin11(LOAD_HIGH), .pin10(DATA_IN[2]), .pin9(DATA_IN[3]));  // open: pin14
  _74244 u_74244_1 (
    .pin1(nADDR_SEL), .pin2(count_8), .pin3(ADDR[15]), .pin4(count_9), .pin5(ADDR[14]), .pin6(count_10),
    .pin7(ADDR[13]), .pin8(count_11), .pin9(ADDR[12]), .pin19(nADDR_SEL), .pin18(ADDR[8]), .pin17(count_15),
    .pin16(ADDR[9]), .pin15(count_14), .pin14(ADDR[10]), .pin13(count_13), .pin12(ADDR[11]), .pin11(count_12));
  _74244 u_74244_2 (
    .pin1(READ_HIGH), .pin2(count_8), .pin3(DATA_OUT[7]), .pin4(count_9), .pin5(DATA_OUT[6]),
    .pin6(count_10), .pin7(DATA_OUT[5]), .pin8(count_11), .pin9(DATA_OUT[4]), .pin19(READ_HIGH),
    .pin18(DATA_OUT[0]), .pin17(count_15), .pin16(DATA_OUT[1]), .pin15(count_14), .pin14(DATA_OUT[2]),
    .pin13(count_13), .pin12(DATA_OUT[3]), .pin11(count_12));
  _74193 u_74193_3 (
    .pin1(DATA_IN[5]), .pin2(count_5), .pin3(count_4), .pin4(n74193_3_pin4), .pin5(n74193_3_pin5),
    .pin6(count_6), .pin7(count_7), .pin15(DATA_IN[4]), .pin13(n74193_2_pin4), .pin12(n74193_2_pin5),
    .pin11(LOAD_LOW), .pin10(DATA_IN[6]), .pin9(DATA_IN[7]));  // open: pin14
  _74244 u_74244_3 (
    .pin1(nADDR_SEL), .pin2(count_0), .pin3(ADDR[7]), .pin4(count_1), .pin5(ADDR[6]), .pin6(count_2),
    .pin7(ADDR[5]), .pin8(count_3), .pin9(ADDR[4]), .pin19(nADDR_SEL), .pin18(ADDR[0]), .pin17(count_7),
    .pin16(ADDR[1]), .pin15(count_6), .pin14(ADDR[2]), .pin13(count_5), .pin12(ADDR[3]), .pin11(count_4));
  _74244 u_74244_4 (
    .pin1(READ_LOW), .pin2(count_0), .pin3(DATA_OUT[7]), .pin4(count_1), .pin5(DATA_OUT[6]), .pin6(count_2),
    .pin7(DATA_OUT[5]), .pin8(count_3), .pin9(DATA_OUT[4]), .pin19(READ_LOW), .pin18(DATA_OUT[0]),
    .pin17(count_7), .pin16(DATA_OUT[1]), .pin15(count_6), .pin14(DATA_OUT[2]), .pin13(count_5),
    .pin12(DATA_OUT[3]), .pin11(count_4));
  _74193 u_74193_4 (
    .pin1(DATA_IN[1]), .pin2(count_1), .pin3(count_0), .pin4(n74193_4_pin4), .pin5(n74193_4_pin5),
    .pin6(count_2), .pin7(count_3), .pin15(DATA_IN[0]), .pin13(n74193_3_pin4), .pin12(n74193_3_pin5),
    .pin11(LOAD_LOW), .pin10(DATA_IN[2]), .pin9(DATA_IN[3]));  // open: pin14
  or or_1 (n74193_4_pin5, n_clock, INC);
  or or_2 (n74193_4_pin4, n_clock, DEC);
  _74138 u_74138_1 (
    .pin1(RD_ADDR[0]), .pin2(RD_ADDR[1]), .pin3(RD_ADDR[2]), .pin4(n74138_1_pin4), .pin5(n74138_1_pin4),
    .pin6(RD_ADDR[4]), .pin13(READ_LOW), .pin12(READ_HIGH));  // open: pin7, pin15, pin14, pin11, pin10, pin9
  _74138 u_74138_2 (
    .pin1(WR_ADDR[0]), .pin2(WR_ADDR[1]), .pin3(WR_ADDR[2]), .pin4(n74138_2_pin4), .pin5(n74138_2_pin5),
    .pin6(WR_ADDR[4]), .pin13(LOAD_LOW), .pin12(LOAD_HIGH));  // open: pin7, pin15, pin14, pin11, pin10, pin9
  _7404 u_7404_1 (
    .pin1(CLOCK), .pin2(n_clock), .pin3(WR_ADDR[3]), .pin4(n74138_2_pin4), .pin5(WR_ENABLE),
    .pin6(n7404_1_pin6), .pin13(RD_ADDR[3]), .pin12(n74138_1_pin4));  // open: pin11, pin10, pin9, pin8
  or or_3 (n74138_2_pin5, n7404_1_pin6, n_clock);

  // Other names for the same wires on the sheet: addr_0 = ADDR[0]; addr_1 = ADDR[1]; addr_2 = ADDR[2];
  //   addr_3 = ADDR[3]; addr_4 = ADDR[4]; addr_5 = ADDR[5]; addr_6 = ADDR[6]; addr_7 = ADDR[7]; addr_8 = ADDR[8];
  //   addr_9 = ADDR[9]; addr_10 = ADDR[10]; addr_11 = ADDR[11]; addr_12 = ADDR[12]; addr_13 = ADDR[13];
  //   addr_14 = ADDR[14]; addr_15 = ADDR[15]; data_in_0 = DATA_IN[0]; data_in_1 = DATA_IN[1]; data_in_2 = DATA_IN[2];
  //   data_in_3 = DATA_IN[3]; data_in_4 = DATA_IN[4]; data_in_5 = DATA_IN[5]; data_in_6 = DATA_IN[6];
  //   data_in_7 = DATA_IN[7]; data_out_0 = DATA_OUT[0]; data_out_1 = DATA_OUT[1]; data_out_2 = DATA_OUT[2];
  //   data_out_3 = DATA_OUT[3]; data_out_4 = DATA_OUT[4]; data_out_5 = DATA_OUT[5]; data_out_6 = DATA_OUT[6];
  //   data_out_7 = DATA_OUT[7]
endmodule

module memory (
  input  [15:0] ADDRESS,
  input  MEMORY_READ,
  input  [7:0] IN,
  input  CLOCK,
  input  MEMORY_WRITE,
  output [7:0] OUT
);

  wire n74138_1_pin4, n74138_1_pin7, n74138_1_pin9, n74138_1_pin10, n74138_1_pin11, n74138_1_pin12,
       n74138_1_pin13, n74138_1_pin14, n74138_1_pin15, read_ram, read_rom, write_clock;
  wire [7:0] ram_1_dout, rom_1_data;

  and and_1 (read_ram, n74138_1_pin15, n74138_1_pin15, n74138_1_pin15, n74138_1_pin15, n74138_1_pin15, n74138_1_pin15, n74138_1_pin15);
  and and_2 (write_clock, CLOCK, MEMORY_WRITE);
  and and_3 (read_rom, n74138_1_pin7, n74138_1_pin9, n74138_1_pin10, n74138_1_pin11, n74138_1_pin12, n74138_1_pin13, n74138_1_pin14);
  _74138 u_74138_1 (
    .pin1(ADDRESS[13]), .pin2(ADDRESS[14]), .pin3(ADDRESS[15]), .pin4(n74138_1_pin4), .pin5(n74138_1_pin4),
    .pin6(MEMORY_READ), .pin7(n74138_1_pin7), .pin15(n74138_1_pin15), .pin14(n74138_1_pin14),
    .pin13(n74138_1_pin13), .pin12(n74138_1_pin12), .pin11(n74138_1_pin11), .pin10(n74138_1_pin10),
    .pin9(n74138_1_pin9));
  RAM #(.addrWidth(16), .enables("line")) ram_1 (
    .addr(ADDRESS), .we(MEMORY_WRITE), .clk(write_clock), .din(IN), .dout(ram_1_dout));
  ROM #(.addrWidth(16)) rom_1 (.addr(ADDRESS), .data(rom_1_data));
  _74244 u_74244_1 (
    .pin1(read_ram), .pin2(ram_1_dout[0]), .pin3(OUT[7]), .pin4(ram_1_dout[1]), .pin5(OUT[6]),
    .pin6(ram_1_dout[2]), .pin7(OUT[5]), .pin8(ram_1_dout[3]), .pin9(OUT[4]), .pin19(read_ram),
    .pin18(OUT[0]), .pin17(ram_1_dout[7]), .pin16(OUT[1]), .pin15(ram_1_dout[6]), .pin14(OUT[2]),
    .pin13(ram_1_dout[5]), .pin12(OUT[3]), .pin11(ram_1_dout[4]));
  _74244 u_74244_2 (
    .pin1(read_rom), .pin2(rom_1_data[0]), .pin3(OUT[7]), .pin4(rom_1_data[1]), .pin5(OUT[6]),
    .pin6(rom_1_data[2]), .pin7(OUT[5]), .pin8(rom_1_data[3]), .pin9(OUT[4]), .pin19(read_rom),
    .pin18(OUT[0]), .pin17(rom_1_data[7]), .pin16(OUT[1]), .pin15(rom_1_data[6]), .pin14(OUT[2]),
    .pin13(rom_1_data[5]), .pin12(OUT[3]), .pin11(rom_1_data[4]));
  // also tied to GND on the sheet: n74138_1_pin4

  // Other names for the same wires on the sheet: write_enable = MEMORY_WRITE

  // Notes on the sheet:
  //   contents of rom_1 (hex, n*v repeats v):
  //   8192*0 28 b5 0 28 c6 7 20 2 35 a1 28 e3 1 21 b5 28 7e d8 1e 20 28 bc 0 35 b0 28 dc 23 20 3c d8 28 bc
  //   1 35 b0 28 e0 1 26 d8 57302*0 20
endmodule

module control (
  input  RESET,
  input  CLOCK,
  input  INT_REQUESTED,
  input  FLAG_I,
  input  FLAG_Z,
  input  FLAG_N,
  input  FLAG_C,
  input  FLAG_O,
  input  [7:0] IN,
  output WR_ENABLE,
  output RD_ENABLE,
  output ULA_ENABLE,
  output nSP_DEC,
  output nADDR_SEL_SP,
  output nSP_INC,
  output nADDR_SEL_MAR,
  output nMAR_DEC,
  output nADDR_SEL_PC,
  output nMAR_INC,
  output nPC_INC,
  output [3:0] RD_ADDR,
  output [3:0] WR_ADDR,
  output DEBUG_EXTEND,
  output [15:0] ADDR,
  output [7:0] DEBUG_INS
);

  wire and_1_out, and_2_out, and_5_out, and_6_out, and_7_out, and_8_out, condition, condition_result,
       constant_0, constant_1, e_xit, extend, finish, handle_interrupt, int_pending, n7474_1_pin1,
       n7474_1_pin2, n7474_1_pin3, n7474_3_pin1, n7474_3_pin6, n74138_1_pin4, n74138_2_pin10, n74138_3_pin4,
       n74138_3_pin6, n74193_1_pin4, n74244_1_pin2, n74244_1_pin17, n74244_2_pin6, n74244_2_pin17,
       naddr_sel_constant, nclear_interrupt, nclock, nreset, nreset_extend, or_1_out, or_2_out,
       reset_counter, write, xnor_1_out, xnor_2_out, xnor_3_out, xnor_4_out;
  wire [3:0] n74193_1_pin3;
  wire [7:4] rom_3_data;
  wire [7:5] n74138_1_pin1;

  not not_1 (nreset, RESET);
  not not_2 (nclock, CLOCK);
  or or_1 (or_1_out, extend, ~handle_interrupt);  // OR_Gate
  _7474 u_7474_1 (
    .pin1(n7474_1_pin1), .pin2(n7474_1_pin2), .pin3(n7474_1_pin3), .pin4(n7474_1_pin2), .pin5(int_pending),
    .pin13(nreset_extend), .pin12(n7474_1_pin2), .pin11(or_1_out), .pin10(nreset), .pin9(DEBUG_EXTEND));  // open: pin6, pin8
  and and_1 (and_1_out, CLOCK, condition);
  and and_2 (and_2_out, e_xit, n7474_3_pin6);
  _7474 u_7474_2 (
    .pin1(nreset), .pin2(IN[0]), .pin3(write), .pin4(handle_interrupt), .pin5(DEBUG_INS[0]), .pin13(nreset),
    .pin12(IN[1]), .pin11(write), .pin10(handle_interrupt), .pin9(DEBUG_INS[1]));  // open: pin6, pin8
  and and_3 (n7474_1_pin1, nreset, nclear_interrupt);
  and and_4 (n7474_1_pin3, INT_REQUESTED, FLAG_I);
  _7474 #(.ShowInternalStructure("true")) u_7474_3 (
    .pin1(n7474_3_pin1), .pin2(condition_result), .pin3(and_1_out), .pin4(n7474_3_pin1), .pin6(n7474_3_pin6));  // open: pin5, pin13, pin12, pin11, pin10, pin9, pin8
  or or_2 (or_2_out, finish, and_2_out);
  ROM #(.addrWidth(13)) rom_1 (.addr({DEBUG_EXTEND, DEBUG_INS, n74193_1_pin3}), .data({WR_ADDR, RD_ADDR}));
  _74193 u_74193_1 (
    .pin2(n74193_1_pin3[1]), .pin3(n74193_1_pin3[0]), .pin4(n74193_1_pin4), .pin5(nclock),
    .pin6(n74193_1_pin3[2]), .pin7(n74193_1_pin3[3]), .pin14(reset_counter));  // open: pin1, pin15, pin13, pin12, pin11, pin10, pin9
  not not_3 (nreset_extend, or_2_out);
  or or_3 (reset_counter, or_2_out, RESET, extend);
  _7474 u_7474_4 (
    .pin1(nreset), .pin2(IN[2]), .pin3(write), .pin4(handle_interrupt), .pin5(DEBUG_INS[2]), .pin13(nreset),
    .pin12(IN[3]), .pin11(write), .pin10(handle_interrupt), .pin9(DEBUG_INS[3]));  // open: pin6, pin8
  _74138 u_74138_1 (
    .pin1(n74138_1_pin1[5]), .pin2(n74138_1_pin1[6]), .pin3(n74138_1_pin1[7]), .pin4(n74138_1_pin4),
    .pin5(n74138_1_pin4), .pin6(CLOCK), .pin14(nPC_INC), .pin13(nMAR_INC), .pin12(nMAR_DEC), .pin11(nSP_INC),
    .pin10(nSP_DEC));  // open: pin7, pin15, pin9
  ROM #(.addrWidth(13)) rom_2 (
    .addr({DEBUG_EXTEND, DEBUG_INS, n74193_1_pin3}),
    .data({n74138_1_pin1, constant_1, constant_0, ULA_ENABLE, RD_ENABLE, WR_ENABLE}));
  or or_4 (condition_result, and_5_out, and_6_out, and_7_out, and_8_out);
  not not_4 (write, n74138_2_pin10);
  and and_5 (and_5_out, RD_ADDR[0], xnor_3_out);
  and and_6 (and_6_out, RD_ADDR[2], xnor_4_out);
  and and_7 (and_7_out, WR_ADDR[0], xnor_1_out);
  and and_8 (and_8_out, WR_ADDR[2], xnor_2_out);
  _7474 u_7474_5 (
    .pin1(nreset), .pin2(IN[4]), .pin3(write), .pin4(handle_interrupt), .pin5(DEBUG_INS[4]), .pin13(nreset),
    .pin12(IN[5]), .pin11(write), .pin10(handle_interrupt), .pin9(DEBUG_INS[5]));  // open: pin6, pin8
  _74138 u_74138_2 (
    .pin1(WR_ADDR[0]), .pin2(WR_ADDR[1]), .pin3(WR_ADDR[2]), .pin4(WR_ADDR[3]), .pin5(nclock),
    .pin6(WR_ENABLE), .pin10(n74138_2_pin10));  // open: pin7, pin15, pin14, pin13, pin12, pin11, pin9
  xnor xnor_1 (xnor_1_out, WR_ADDR[1], FLAG_C);
  xnor xnor_2 (xnor_2_out, WR_ADDR[3], FLAG_O);
  _74138 u_74138_3 (
    .pin1(rom_3_data[5]), .pin2(rom_3_data[6]), .pin3(rom_3_data[7]), .pin4(n74138_3_pin4),
    .pin5(n74138_3_pin4), .pin6(n74138_3_pin6), .pin14(nADDR_SEL_PC), .pin13(nADDR_SEL_MAR),
    .pin12(nADDR_SEL_SP), .pin11(naddr_sel_constant), .pin10(nclear_interrupt));  // open: pin7, pin15, pin9
  ROM #(.addrWidth(13)) rom_3 (
    .addr({DEBUG_EXTEND, DEBUG_INS, n74193_1_pin3}), .data({rom_3_data, e_xit, condition, extend, finish}));
  xnor xnor_3 (xnor_3_out, RD_ADDR[1], FLAG_Z);
  xnor xnor_4 (xnor_4_out, RD_ADDR[3], FLAG_N);
  _7474 u_7474_6 (
    .pin1(nreset), .pin2(IN[6]), .pin3(write), .pin4(handle_interrupt), .pin5(DEBUG_INS[6]), .pin13(nreset),
    .pin12(IN[7]), .pin11(write), .pin10(handle_interrupt), .pin9(DEBUG_INS[7]));  // open: pin6, pin8
  nand nand_1 (handle_interrupt, int_pending, finish);
  _74244 u_74244_1 (
    .pin1(naddr_sel_constant), .pin2(n74244_1_pin2), .pin3(ADDR[15]), .pin4(n74244_1_pin2), .pin5(ADDR[14]),
    .pin6(n74244_1_pin2), .pin7(ADDR[13]), .pin8(n74244_1_pin2), .pin9(ADDR[12]), .pin19(naddr_sel_constant),
    .pin18(ADDR[8]), .pin17(n74244_1_pin17), .pin16(ADDR[9]), .pin15(n74244_1_pin17), .pin14(ADDR[10]),
    .pin13(n74244_1_pin17), .pin12(ADDR[11]), .pin11(n74244_1_pin17));
  _74244 u_74244_2 (
    .pin1(naddr_sel_constant), .pin2(constant_0), .pin3(ADDR[7]), .pin4(constant_1), .pin5(ADDR[6]),
    .pin6(n74244_2_pin6), .pin7(ADDR[5]), .pin8(n74244_2_pin6), .pin9(ADDR[4]), .pin19(naddr_sel_constant),
    .pin18(ADDR[0]), .pin17(n74244_2_pin17), .pin16(ADDR[1]), .pin15(n74244_2_pin17), .pin14(ADDR[2]),
    .pin13(n74244_2_pin17), .pin12(ADDR[3]), .pin11(n74244_2_pin17));
  // also tied to GND on the sheet: {n74138_1_pin4, n74138_3_pin4}
  // also tied to VCC on the sheet: {n7474_3_pin1, n7474_1_pin2, n74193_1_pin4, n74138_3_pin6, n74244_1_pin2, n74244_2_pin6, n74244_1_pin17, n74244_2_pin17}

  // Other names for the same wires on the sheet: ins[7:0] = DEBUG_INS; ins_0 = DEBUG_INS[0]; ins_1 = DEBUG_INS[1];
  //   ins_2 = DEBUG_INS[2]; ins_3 = DEBUG_INS[3]; ins_4 = DEBUG_INS[4]; ins_5 = DEBUG_INS[5]; ins_6 = DEBUG_INS[6];
  //   ins_7 = DEBUG_INS[7]; addr_0 = ADDR[0]; addr_1 = ADDR[1]; addr_2 = ADDR[2]; addr_3 = ADDR[3]; addr_4 = ADDR[4];
  //   addr_5 = ADDR[5]; addr_6 = ADDR[6]; addr_7 = ADDR[7]; addr_8 = ADDR[8]; addr_9 = ADDR[9]; addr_10 = ADDR[10];
  //   addr_11 = ADDR[11]; addr_12 = ADDR[12]; addr_13 = ADDR[13]; addr_14 = ADDR[14]; addr_15 = ADDR[15];
  //   conditions[7:0] = {WR_ADDR, RD_ADDR}; data_in_0 = IN[0]; data_in_1 = IN[1]; data_in_2 = IN[2];
  //   data_in_3 = IN[3]; data_in_4 = IN[4]; data_in_5 = IN[5]; data_in_6 = IN[6]; data_in_7 = IN[7]

  // Notes on the sheet:
  //   contents of rom_1 (hex, n*v repeats v):
  //   54 15*0 54 27 14*0 54 28 14*0 54 29 14*0 54 2a 14*0 54 2c 14*0 54 2b 14*0 54 26 14*0 54 29 28 13*0
  //   54 2b 2c 13*0 54 2d 2d 13*0 54 20 21 13*0 54 24 24 94 84 11*0 54 24 24 b4 c4 11*0 54 24 24 d4 d4
  //   11*0 54 24 24 4 14 11*0 54 27 20 13*0 54 28 20 13*0 54 29 20 13*0 54 2a 20 13*0 54 2c 20 13*0 54 2b
  //   20 13*0 54 74 14*0 54 84 14*0 54 94 14*0 54 a4 14*0 54 c4 14*0 54 b4 14*0 54 64 14*0 54 97 b0 87 79
  //   11*0 54 b7 b0 c7 7b 11*0 54 15*0 54 94 84 13*0 54 b4 c4 13*0 54 d4 d4 13*0 54 24 24 2 12 11*0 54 29
  //   29 13*0 54 2b 2c 13*0 54 2d 2d 13*0 54 20 21 13*0 54 24 24 30 2 12 10*0 54 24 24 3 2 12 10*0 54 24
  //   24 10 2 12 10*0 54 24 24 1 2 12 10*0 54 28 29 13*0 54 2b 2c 13*0 54 2d 2d 13*0 54 20 21 13*0 54 24
  //   24 74 12*0 54 24 24 84 12*0 54 24 24 94 12*0 54 24 24 a4 12*0 54 24 24 c4 12*0 54 24 24 b4 12*0 54
  //   24 24 64 12*0 54 24 24 c 2 12 10*0 54 24 24 c0 2 12 10*0 54 24 24 4 2 12 10*0 54 24 24 40 2 12 10*0
  //   54 15*0 54 15*0 54 15*0 54 15*0 54 4 14*0 54 24 24 47 12*0 54 24 24 48 12*0 54 24 24 49 12*0 54 24
  //   24 4a 12*0 54 24 24 4c 12*0 54 24 24 4b 12*0 54 24 24 46 12*0 54 48 49 13*0 54 4c 4b 13*0 54 41 40
  //   13*0 54 15*0 54 24 24 4 12*0 54 29 28 4 12*0 54 2b 2c 4 12*0 54 d0 4 13*0 54 d0 24 24 4 11*0 54 47
  //   14*0 54 48 14*0 54 49 14*0 54 4a 14*0 54 4c 14*0 54 4b 14*0 54 46 14*0 54 0 74 13*0 54 0 84 13*0 54
  //   0 94 13*0 54 0 a4 13*0 54 0 c4 13*0 54 0 b4 13*0 54 0 64 13*0 54 d0 29 28 4 11*0 54 d0 2b 2c 4 11*0
  //   54 0 94 84 12*0 54 0 b4 c4 12*0 54 0 4 14 12*0 54 28 87 72 12*0 54 29 97 72 12*0 54 2a a7 72 12*0 54
  //   2c c7 72 12*0 54 2b b7 72 12*0 54 26 67 72 12*0 54 29 28 92 82 11*0 54 2b 2c b2 c2 11*0 54 14 14*0
  //   54 29 28 14 12*0 54 2b 2c 14 12*0 54 24 24 14 12*0 54 c0 14*0 54 7 14*0 54 8 14*0 54 9 14*0 54 a
  //   14*0 54 c 14*0 54 b 14*0 54 d0 7 13*0 54 d0 8 13*0 54 d0 9 13*0 54 d0 a 13*0 54 d0 c 13*0 54 d0 b
  //   13*0 54 c0 14 13*0 54 c0 29 28 14 11*0 54 c0 2b 2c 14 11*0 54 d0 10 13*0 54 17 14*0 54 18 14*0 54 19
  //   14*0 54 1a 14*0 54 1c 14*0 54 1b 14*0 54 c0 17 13*0 54 c0 18 13*0 54 c0 19 13*0 54 c0 1a 13*0 54 c0
  //   1c 13*0 54 c0 1b 13*0 54 c0 24 24 14 11*0 54 34 14*0 54 29 28 34 12*0 54 2b 2c 34 12*0 54 37 14*0 54
  //   38 14*0 54 39 14*0 54 3a 14*0 54 3c 14*0 54 3b 14*0 54 36 14*0 54 47 14*0 54 48 14*0 54 49 14*0 54
  //   4a 14*0 54 4c 14*0 54 4b 14*0 54 46 14*0 54 44 14*0 54 24 24 34 12*0 54 57 14*0 54 58 14*0 54 59
  //   14*0 54 5a 14*0 54 5c 14*0 54 5b 14*0 54 56 14*0 54 54 14*0 54 29 28 54 12*0 54 2b 2c 54 12*0 54 24
  //   24 54 12*0 54 29 28 44 12*0 54 2b 2c 44 12*0 54 24 24 44 12*0 54 24 24 64 12*0 54 67 14*0 54 87 14*0
  //   54 29 28 84 12*0 54 2b 2c 84 12*0 54 d0 87 13*0 54 d0 29 28 84 11*0 54 d0 2b 2c 84 11*0 54 77 14*0
  //   54 29 28 74 12*0 54 2b 2c 74 12*0 54 d0 77 13*0 54 d0 29 28 74 11*0 54 d0 2b 2c 74 11*0 54 29 28 a4
  //   12*0 54 2b 2c a4 12*0 54 29 28 94 12*0 54 2b 2c 94 12*0 54 a7 14*0 54 97 14*0 54 d0 14*0 54 c0 14*0
  //   54 24 24 64 c0 11*0 54 67 c0 13*0 29 28 64 c0 12*0 2b 2c 64 c0 12*0 54 29 28 64 12*0 54 2b 2c 64
  //   12*0 54 41 40 9 18 11*0 54 41 40 b 1c 11*0 54 41 40 29 28 4 14 9*0 54 41 40 2b 2c 4 14 9*0 54 9 18
  //   13*0 54 b 1c 13*0 54 24 24 2 12 11*0 54 24 24 4 14 11*0 54 29 28 4 14 11*0 54 2b 2c 4 14 11*0 54 0 4
  //   14 12*0 54 15*0 54 15*0 54 15*0 54 15*0 54 15*0 54 15*0 54 15*0 54 15*0 54 15*0 54 15*0 54 15*0 54
  //   24 14*0 54 27 14*0 54 28 14*0 54 29 14*0 54 2a 14*0 54 2c 14*0 54 2b 14*0 54 15*0 54 24 24 41 40 2
  //   12 9*0 54 24 24 41 40 4 14 9*0 54 28 82 13*0 54 29 92 13*0 54 2a a2 13*0 54 2c c2 13*0 54 2b b2 13*0
  //   54 15*0 54 29 28 92 82 11*0 54 2b 2c b2 c2 11*0 54 28 82 13*0 54 29 92 13*0 54 2a a2 13*0 54 2c c2
  //   13*0 54 2b b2 13*0 54 15*0 54 15*0 54 15*0 54 15*0 54 15*0 54 15*0 54 15*0 54 15*0 54 16*0 4 14 60
  //   12*0 54 15*0 54 15*0 54 15*0 54 15*0 54 15*0 54 15*0 54 15*0 54 15*0 54 15*0 54 15*0 54 15*0 54 15*0
  //   54 15*0 54 15*0 54 15*0 54 15*0 54 15*0 54 15*0 54 15*0 54 15*0 54 15*0 54 15*0 54 15*0 54 15*0 54
  //   15*0 54 15*0 54 15*0 54 15*0 54 15*0 54 15*0 54 15*0 54 15*0 54 15*0 54 15*0 54 15*0 54 15*0 54 15*0
  //   54 15*0 54 15*0 54 15*0 54 15*0 54 15*0 54 15*0 54 15*0 54 15*0 54 15*0 54 15*0 54 15*0 54 15*0 54
  //   15*0 54 15*0 54 15*0 54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
  //   contents of rom_2 (hex, n*v repeats v):
  //   23 15*0 23 3 14*0 23 3 14*0 23 3 14*0 23 3 14*0 23 3 14*0 23 3 14*0 23 3 14*0 23 3 3 13*0 23 3 3
  //   13*0 23 3 3 13*0 23 3 3 13*0 23 23 23 43 3 11*0 23 23 23 43 3 11*0 23 23 23 43 3 11*0 23 23 3 43 3
  //   11*0 23 3 1 13*0 23 3 1 13*0 23 3 1 13*0 23 3 1 13*0 23 3 1 13*0 23 3 1 13*0 23 23 14*0 23 23 14*0
  //   23 23 14*0 23 23 14*0 23 23 14*0 23 23 14*0 23 23 14*0 23 3 4 3 3 11*0 23 3 4 3 3 11*0 3 15*0 23 23
  //   23 13*0 23 23 23 13*0 23 23 23 13*0 23 23 3 3 3 11*0 23 3 3 13*0 23 3 3 13*0 23 3 3 13*0 23 3 3 13*0
  //   23 23 23 0 3 3 10*0 23 23 23 0 3 3 10*0 23 23 23 0 3 3 10*0 23 23 23 0 3 3 10*0 23 3 3 13*0 23 3 3
  //   13*0 23 3 3 13*0 23 3 3 13*0 23 23 23 3 12*0 23 23 23 3 12*0 23 23 23 3 12*0 23 23 23 3 12*0 23 23
  //   23 3 12*0 23 23 23 3 12*0 23 23 23 3 12*0 23 23 23 0 3 3 10*0 23 23 23 0 3 3 10*0 23 23 23 0 3 3
  //   10*0 23 23 23 0 3 3 10*0 23 15*0 23 15*0 23 15*0 23 15*0 23 26 14*0 23 23 23 3 12*0 23 23 23 3 12*0
  //   23 23 23 3 12*0 23 23 23 3 12*0 23 23 23 3 12*0 23 23 23 3 12*0 23 23 23 3 12*0 23 a3 a3 13*0 23 a3
  //   a3 13*0 23 a3 a3 13*0 23 15*0 23 23 23 6 12*0 23 3 3 6 12*0 23 3 3 6 12*0 23 4 26 13*0 23 4 23 23 6
  //   11*0 23 a3 14*0 23 a3 14*0 23 a3 14*0 23 a3 14*0 23 a3 14*0 23 a3 14*0 23 a3 14*0 23 80 3 13*0 23 80
  //   3 13*0 23 80 3 13*0 23 80 3 13*0 23 80 3 13*0 23 80 3 13*0 23 80 3 13*0 23 4 3 3 6 11*0 23 4 3 3 6
  //   11*0 23 80 83 3 12*0 23 80 83 3 12*0 23 80 83 3 12*0 23 3 3 3 12*0 23 3 3 3 12*0 23 3 3 3 12*0 23 3
  //   3 3 12*0 23 3 3 3 12*0 23 3 3 3 12*0 23 3 43 3 3 11*0 23 3 43 3 3 11*0 23 26 14*0 23 3 3 6 12*0 23 3
  //   3 6 12*0 23 23 23 6 12*0 23 4 4 13*0 23 6 14*0 23 6 14*0 23 6 14*0 23 6 14*0 23 6 14*0 23 6 14*0 23
  //   4 6 13*0 23 4 6 13*0 23 4 6 13*0 23 4 6 13*0 23 4 6 13*0 23 4 6 13*0 23 4 26 13*0 23 4 3 3 6 11*0 23
  //   4 3 3 6 11*0 23 4 4 13*0 23 6 14*0 23 6 14*0 23 6 14*0 23 6 14*0 23 6 14*0 23 6 14*0 23 4 6 13*0 23
  //   4 6 13*0 23 4 6 13*0 23 4 6 13*0 23 4 6 13*0 23 4 6 13*0 23 4 23 23 6 11*0 23 26 14*0 23 3 3 6 12*0
  //   23 3 3 6 12*0 23 6 14*0 23 6 14*0 23 6 14*0 23 6 14*0 23 6 14*0 23 6 14*0 23 6 14*0 23 6 14*0 23 6
  //   14*0 23 6 14*0 23 6 14*0 23 6 14*0 23 6 14*0 23 6 14*0 23 26 14*0 23 23 23 6 12*0 23 6 14*0 23 6
  //   14*0 23 6 14*0 23 6 14*0 23 6 14*0 23 6 14*0 23 6 14*0 23 26 14*0 23 3 3 6 12*0 23 3 3 6 12*0 23 23
  //   23 6 12*0 23 3 3 6 12*0 23 3 3 6 12*0 23 23 23 6 12*0 23 23 23 6 12*0 23 6 14*0 23 6 14*0 23 3 3 6
  //   12*0 23 3 3 6 12*0 23 4 6 13*0 23 4 3 3 6 11*0 23 4 3 3 6 11*0 23 6 14*0 23 3 3 6 12*0 23 3 3 6 12*0
  //   23 4 6 13*0 23 4 3 3 6 11*0 23 4 3 3 6 11*0 23 3 3 6 12*0 23 3 3 6 12*0 23 3 3 6 12*0 23 3 3 6 12*0
  //   23 6 14*0 23 6 14*0 23 4 14*0 23 4 14*0 23 23 23 6 4 4 10*0 23 6 4 4 12*0 3 3 6 4 4 11*0 3 3 6 4 4
  //   11*0 23 3 3 6 12*0 23 3 3 6 12*0 23 a3 a3 3 3 11*0 23 a3 a3 3 3 11*0 23 a3 a3 3 3 43 3 9*0 23 a3 a3
  //   3 3 43 3 9*0 23 3 3 13*0 23 3 3 13*0 23 23 3 3 3 11*0 23 23 3 43 3 11*0 23 3 3 43 3 11*0 23 3 3 43 3
  //   11*0 23 80 83 3 12*0 23 15*0 23 15*0 23 15*0 23 15*0 23 15*0 23 15*0 23 15*0 23 15*0 23 15*0 23 15*0
  //   23 15*0 23 23 14*0 23 3 14*0 23 3 14*0 23 3 14*0 23 3 14*0 23 3 14*0 23 3 14*0 23 15*0 23 23 23 a3
  //   a3 3 3 9*0 23 23 23 a3 a3 43 3 9*0 23 43 3 13*0 23 43 3 13*0 23 43 3 13*0 23 43 3 13*0 23 43 3 13*0
  //   23 15*0 23 3 63 3 3 11*0 23 3 63 3 3 11*0 23 63 3 13*0 23 63 3 13*0 23 63 3 13*0 23 63 3 13*0 23 63
  //   3 13*0 23 15*0 23 15*0 23 15*0 23 15*0 23 15*0 23 15*0 23 15*0 23 15*0 23 16*0 13 1b 1 12*0 23 15*0
  //   23 15*0 23 15*0 23 15*0 23 15*0 23 15*0 23 15*0 23 15*0 23 15*0 23 15*0 23 15*0 23 15*0 23 15*0 23
  //   15*0 23 15*0 23 15*0 23 15*0 23 15*0 23 15*0 23 15*0 23 15*0 23 15*0 23 15*0 23 15*0 23 15*0 23 15*0
  //   23 15*0 23 15*0 23 15*0 23 15*0 23 15*0 23 15*0 23 15*0 23 15*0 23 15*0 23 15*0 23 15*0 23 15*0 23
  //   15*0 23 15*0 23 15*0 23 15*0 23 15*0 23 15*0 23 15*0 23 15*0 23 15*0 23 15*0 23 15*0 23 15*0 23 15*0
  //   23 15*0 23 15*0 23 15*0 23 15*0 23 15*0 23 15*0 23 15*0 23 15*0 23 15*0 23 15*0 23 15*0 23 15*0 23
  //   15*0 23 15*0 23 15*0 23 15*0 23 15*0 23 15*0 23 15*0 23 15*0 23 15*0 23 15*0 23 15*0 23 15*0 23 15*0
  //   23 15*0 23 15*0 23 15*0 23 15*0 23 15*0 23 15*0 23 15*0 23 15*0 23 15*0 23 15*0 23 15*0 23 15*0 23
  //   15*0 23 15*0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
  //   contents of rom_3 (hex, n*v repeats v):
  //   20 1 14*0 20 0 2 13*0 20 0 2 13*0 20 0 2 13*0 20 0 2 13*0 20 0 2 13*0 20 0 2 13*0 20 0 2 13*0 20 0 0
  //   2 12*0 20 0 0 2 12*0 20 0 0 2 12*0 20 0 0 2 12*0 20 20 20 40 40 1 10*0 20 20 20 40 40 1 10*0 20 20
  //   20 40 40 1 10*0 20 20 20 40 40 1 10*0 20 0 0 2 12*0 20 0 0 2 12*0 20 0 0 2 12*0 20 0 0 2 12*0 20 0 0
  //   2 12*0 20 0 0 2 12*0 20 20 1 13*0 20 20 1 13*0 20 20 1 13*0 20 20 1 13*0 20 20 1 13*0 20 20 1 13*0
  //   20 20 1 13*0 20 4*0 1 10*0 20 4*0 1 10*0 20 1 14*0 20 20 20 1 12*0 20 20 20 1 12*0 20 20 20 1 12*0
  //   20 20 20 0 0 1 10*0 20 0 0 2 12*0 20 0 0 2 12*0 20 0 0 2 12*0 20 0 0 2 12*0 20 20 20 4 8 0 1 9*0 20
  //   20 20 4 8 0 1 9*0 20 20 20 4 8 0 1 9*0 20 20 20 4 8 0 1 9*0 20 0 0 2 12*0 20 0 0 2 12*0 20 0 0 2
  //   12*0 20 0 0 2 12*0 20 20 20 40 1 11*0 20 20 20 40 1 11*0 20 20 20 40 1 11*0 20 20 20 40 1 11*0 20 20
  //   20 40 1 11*0 20 20 20 40 1 11*0 20 20 20 40 1 11*0 20 20 20 4 8 0 1 9*0 20 20 20 4 8 0 1 9*0 20 20
  //   20 4 8 0 1 9*0 20 20 20 4 8 0 1 9*0 20 1 14*0 20 1 14*0 20 1 14*0 20 1 14*0 20 20 1 13*0 20 20 20 40
  //   1 11*0 20 20 20 40 1 11*0 20 20 20 40 1 11*0 20 20 20 40 1 11*0 20 20 20 40 1 11*0 20 20 20 40 1
  //   11*0 20 20 20 40 1 11*0 20 60 60 1 12*0 20 60 60 1 12*0 20 60 60 1 12*0 20 1 14*0 20 20 20 40 1 11*0
  //   20 0 0 40 1 11*0 20 0 0 40 1 11*0 20 0 20 1 12*0 20 0 20 20 40 1 10*0 20 60 1 13*0 20 60 1 13*0 20
  //   60 1 13*0 20 60 1 13*0 20 60 1 13*0 20 60 1 13*0 20 60 1 13*0 20 0 60 1 12*0 20 0 60 1 12*0 20 0 60
  //   1 12*0 20 0 60 1 12*0 20 0 60 1 12*0 20 0 60 1 12*0 20 0 60 1 12*0 20 0 0 0 40 1 10*0 20 0 0 0 40 1
  //   10*0 20 0 60 60 1 11*0 20 0 60 60 1 11*0 20 0 60 60 1 11*0 20 0 0 0 1 11*0 20 0 0 0 1 11*0 20 0 0 0
  //   1 11*0 20 0 0 0 1 11*0 20 0 0 0 1 11*0 20 0 0 0 1 11*0 20 4*0 1 10*0 20 4*0 1 10*0 20 20 1 13*0 20 0
  //   0 40 1 11*0 20 0 0 40 1 11*0 20 20 20 40 1 11*0 20 0 0 1 12*0 20 0 1 13*0 20 0 1 13*0 20 0 1 13*0 20
  //   0 1 13*0 20 0 1 13*0 20 0 1 13*0 20 0 0 1 12*0 20 0 0 1 12*0 20 0 0 1 12*0 20 0 0 1 12*0 20 0 0 1
  //   12*0 20 0 0 1 12*0 20 0 20 1 12*0 20 0 0 0 40 1 10*0 20 0 0 0 40 1 10*0 20 0 0 1 12*0 20 0 1 13*0 20
  //   0 1 13*0 20 0 1 13*0 20 0 1 13*0 20 0 1 13*0 20 0 1 13*0 20 0 0 1 12*0 20 0 0 1 12*0 20 0 0 1 12*0
  //   20 0 0 1 12*0 20 0 0 1 12*0 20 0 0 1 12*0 20 0 20 20 40 1 10*0 20 20 1 13*0 20 0 0 40 1 11*0 20 0 0
  //   40 1 11*0 20 0 1 13*0 20 0 1 13*0 20 0 1 13*0 20 0 1 13*0 20 0 1 13*0 20 0 1 13*0 20 0 1 13*0 20 0 1
  //   13*0 20 0 1 13*0 20 0 1 13*0 20 0 1 13*0 20 0 1 13*0 20 0 1 13*0 20 0 1 13*0 20 20 1 13*0 20 20 20
  //   40 1 11*0 20 0 1 13*0 20 0 1 13*0 20 0 1 13*0 20 0 1 13*0 20 0 1 13*0 20 0 1 13*0 20 0 1 13*0 20 20
  //   1 13*0 20 0 0 40 1 11*0 20 0 0 40 1 11*0 20 20 20 40 1 11*0 20 0 0 40 1 11*0 20 0 0 40 1 11*0 20 20
  //   20 40 1 11*0 20 20 20 40 1 11*0 20 0 1 13*0 20 0 1 13*0 20 0 0 40 1 11*0 20 0 0 40 1 11*0 20 0 0 1
  //   12*0 20 0 0 0 40 1 10*0 20 0 0 0 40 1 10*0 20 0 1 13*0 20 0 0 40 1 11*0 20 0 0 40 1 11*0 20 0 0 1
  //   12*0 20 0 0 0 40 1 10*0 20 0 0 0 40 1 10*0 20 0 0 40 1 11*0 20 0 0 40 1 11*0 20 0 0 40 1 11*0 20 0 0
  //   40 1 11*0 20 0 1 13*0 20 0 1 13*0 20 0 1 13*0 20 0 1 13*0 20 20 20 40 0 0 1 9*0 20 0 0 0 1 13*0 40 0
  //   0 1 12*0 40 0 0 1 10*0 20 0 0 40 1 11*0 20 0 0 40 1 11*0 20 60 60 0 0 1 10*0 20 60 60 0 0 1 10*0 20
  //   60 60 0 0 40 40 1 8*0 20 60 60 0 0 40 40 1 8*0 20 0 0 1 12*0 20 0 0 1 12*0 20 20 20 0 0 1 10*0 20 20
  //   20 40 40 1 10*0 20 0 0 40 40 1 10*0 20 0 0 40 40 1 10*0 20 0 60 60 1 11*0 20 1 14*0 20 1 14*0 20 1
  //   14*0 20 1 14*0 20 1 14*0 20 1 14*0 20 1 14*0 20 1 14*0 20 1 14*0 20 1 14*0 20 1 14*0 20 20 2 13*0 20
  //   0 2 13*0 20 0 2 13*0 20 0 2 13*0 20 0 2 13*0 20 0 2 13*0 20 0 2 13*0 20 1 14*0 20 20 20 60 60 0 0 1
  //   8*0 20 20 20 60 60 40 40 1 8*0 20 0 0 1 12*0 20 0 0 1 12*0 20 0 0 1 12*0 20 0 0 1 12*0 20 0 0 1 12*0
  //   20 1 14*0 20 4*0 1 10*0 20 4*0 1 10*0 20 0 0 1 12*0 20 0 0 1 12*0 20 0 0 1 12*0 20 0 0 1 12*0 20 0 0
  //   1 12*0 20 1 14*0 20 1 14*0 20 1 14*0 20 1 14*0 20 1 14*0 20 1 14*0 20 1 14*0 20 1 14*0 20 1 15*0 80
  //   80 a0 1 11*0 20 1 14*0 20 1 14*0 20 1 14*0 20 1 14*0 20 1 14*0 20 1 14*0 20 1 14*0 20 1 14*0 20 1
  //   14*0 20 1 14*0 20 1 14*0 20 1 14*0 20 1 14*0 20 1 14*0 20 1 14*0 20 1 14*0 20 1 14*0 20 1 14*0 20 1
  //   14*0 2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
endmodule

module in_out (
  input  [15:0] ADDR,
  input  [4:0] RD_ADDR,
  input  [7:0] PORT_INPUT,
  input  WR_ENABLE,
  input  [4:0] WR_ADDR,
  input  CLOCK,
  input  [7:0] DATA_IN,
  input  [7:0] PORT_INPUT_A,
  input  [7:0] PORT_INPUT_B,
  input  [7:0] PORT_INPUT_C,
  input  [7:0] PORT_INPUT_D,
  output [7:0] PORT_ADDR,
  output PORT_READ,
  output [7:0] PORT_OUTPUT,
  output PORT_WRITE,
  output [7:0] DATA_OUT,
  output [7:0] PORT_OUTPUT_A,
  output [7:0] PORT_OUTPUT_B,
  output [7:0] PORT_OUTPUT_C,
  output [7:0] PORT_OUTPUT_D
);

  wire n74138_2_pin6, n74138_3_pin6, n74138_4_pin6, n74377_1_pin1, n74377_2_pin1, n74377_3_pin1,
       n74377_4_pin1, read_A, read_B, read_C, read_D, write, write_A, write_B, write_C, write_D;

  and and_1 (PORT_WRITE, ~write, CLOCK);  // AND_Gate
  _74138 u_74138_1 (
    .pin1(RD_ADDR[0]), .pin2(RD_ADDR[1]), .pin3(RD_ADDR[2]), .pin4(RD_ADDR[3]), .pin5(RD_ADDR[3]),
    .pin6(RD_ADDR[4]), .pin15(PORT_READ));  // open: pin7, pin14, pin13, pin12, pin11, pin10, pin9
  _74138 u_74138_2 (
    .pin1(WR_ADDR[0]), .pin2(WR_ADDR[1]), .pin3(WR_ADDR[2]), .pin4(WR_ADDR[3]), .pin5(WR_ADDR[3]),
    .pin6(n74138_2_pin6), .pin15(write));  // open: pin7, pin14, pin13, pin12, pin11, pin10, pin9
  _74244 u_74244_1 (
    .pin1(write), .pin2(DATA_IN[0]), .pin3(PORT_OUTPUT[7]), .pin4(DATA_IN[1]), .pin5(PORT_OUTPUT[6]),
    .pin6(DATA_IN[2]), .pin7(PORT_OUTPUT[5]), .pin8(DATA_IN[3]), .pin9(PORT_OUTPUT[4]), .pin19(write),
    .pin18(PORT_OUTPUT[0]), .pin17(DATA_IN[7]), .pin16(PORT_OUTPUT[1]), .pin15(DATA_IN[6]),
    .pin14(PORT_OUTPUT[2]), .pin13(DATA_IN[5]), .pin12(PORT_OUTPUT[3]), .pin11(DATA_IN[4]));
  _74138 u_74138_3 (
    .pin1(ADDR[0]), .pin2(ADDR[1]), .pin3(ADDR[2]), .pin4(ADDR[3]), .pin5(ADDR[4]), .pin6(n74138_3_pin6),
    .pin15(write_A), .pin14(write_B), .pin13(write_C), .pin12(write_D));  // open: pin7, pin11, pin10, pin9
  and and_2 (n74138_2_pin6, WR_ENABLE, WR_ADDR[4]);
  and and_3 (n74138_3_pin6, PORT_WRITE, ~ADDR[5], ~ADDR[6], ~ADDR[7]);  // AND_Gate
  _74377 u_74377_1 (
    .pin1(n74377_1_pin1), .pin2(PORT_OUTPUT_A[0]), .pin3(PORT_OUTPUT[0]), .pin4(PORT_OUTPUT[1]),
    .pin5(PORT_OUTPUT_A[1]), .pin6(PORT_OUTPUT_A[2]), .pin7(PORT_OUTPUT[2]), .pin8(PORT_OUTPUT[3]),
    .pin9(PORT_OUTPUT_A[3]), .pin19(PORT_OUTPUT_A[7]), .pin18(PORT_OUTPUT[7]), .pin17(PORT_OUTPUT[6]),
    .pin16(PORT_OUTPUT_A[6]), .pin15(PORT_OUTPUT_A[5]), .pin14(PORT_OUTPUT[5]), .pin13(PORT_OUTPUT[4]),
    .pin12(PORT_OUTPUT_A[4]), .pin11(write_A));
  _74377 u_74377_2 (
    .pin1(n74377_2_pin1), .pin2(PORT_OUTPUT_C[0]), .pin3(PORT_OUTPUT[0]), .pin4(PORT_OUTPUT[1]),
    .pin5(PORT_OUTPUT_C[1]), .pin6(PORT_OUTPUT_C[2]), .pin7(PORT_OUTPUT[2]), .pin8(PORT_OUTPUT[3]),
    .pin9(PORT_OUTPUT_C[3]), .pin19(PORT_OUTPUT_C[7]), .pin18(PORT_OUTPUT[7]), .pin17(PORT_OUTPUT[6]),
    .pin16(PORT_OUTPUT_C[6]), .pin15(PORT_OUTPUT_C[5]), .pin14(PORT_OUTPUT[5]), .pin13(PORT_OUTPUT[4]),
    .pin12(PORT_OUTPUT_C[4]), .pin11(write_C));
  _74244 u_74244_2 (
    .pin1(read_A), .pin2(PORT_INPUT_A[0]), .pin3(PORT_INPUT[7]), .pin4(PORT_INPUT_A[1]),
    .pin5(PORT_INPUT[6]), .pin6(PORT_INPUT_A[2]), .pin7(PORT_INPUT[5]), .pin8(PORT_INPUT_A[3]),
    .pin9(PORT_INPUT[4]), .pin19(read_A), .pin18(PORT_INPUT[0]), .pin17(PORT_INPUT_A[7]),
    .pin16(PORT_INPUT[1]), .pin15(PORT_INPUT_A[6]), .pin14(PORT_INPUT[2]), .pin13(PORT_INPUT_A[5]),
    .pin12(PORT_INPUT[3]), .pin11(PORT_INPUT_A[4]));
  _74244 u_74244_3 (
    .pin1(read_C), .pin2(PORT_INPUT_C[0]), .pin3(PORT_INPUT[4]), .pin4(PORT_INPUT_C[1]),
    .pin5(PORT_INPUT[5]), .pin6(PORT_INPUT_C[2]), .pin7(PORT_INPUT[6]), .pin8(PORT_INPUT_C[3]),
    .pin9(PORT_INPUT[7]), .pin19(read_C), .pin18(PORT_INPUT[0]), .pin17(PORT_INPUT_C[7]),
    .pin16(PORT_INPUT[1]), .pin15(PORT_INPUT_C[6]), .pin14(PORT_INPUT[2]), .pin13(PORT_INPUT_C[5]),
    .pin12(PORT_INPUT[3]), .pin11(PORT_INPUT_C[4]));
  _74138 u_74138_4 (
    .pin1(ADDR[0]), .pin2(ADDR[1]), .pin3(ADDR[2]), .pin4(ADDR[3]), .pin5(ADDR[4]), .pin6(n74138_4_pin6),
    .pin15(read_A), .pin14(read_B), .pin13(read_C), .pin12(read_D));  // open: pin7, pin11, pin10, pin9
  _74244 u_74244_4 (
    .pin1(PORT_READ), .pin2(PORT_INPUT[0]), .pin3(DATA_OUT[7]), .pin4(PORT_INPUT[1]), .pin5(DATA_OUT[6]),
    .pin6(PORT_INPUT[2]), .pin7(DATA_OUT[5]), .pin8(PORT_INPUT[3]), .pin9(DATA_OUT[4]), .pin19(PORT_READ),
    .pin18(DATA_OUT[0]), .pin17(PORT_INPUT[7]), .pin16(DATA_OUT[1]), .pin15(PORT_INPUT[6]),
    .pin14(DATA_OUT[2]), .pin13(PORT_INPUT[5]), .pin12(DATA_OUT[3]), .pin11(PORT_INPUT[4]));
  and and_4 (n74138_4_pin6, ~PORT_READ, ~ADDR[5], ~ADDR[6], ~ADDR[7]);  // AND_Gate
  _74377 u_74377_3 (
    .pin1(n74377_3_pin1), .pin2(PORT_OUTPUT_B[0]), .pin3(PORT_OUTPUT[0]), .pin4(PORT_OUTPUT[1]),
    .pin5(PORT_OUTPUT_B[1]), .pin6(PORT_OUTPUT_B[2]), .pin7(PORT_OUTPUT[2]), .pin8(PORT_OUTPUT[3]),
    .pin9(PORT_OUTPUT_B[3]), .pin19(PORT_OUTPUT_B[7]), .pin18(PORT_OUTPUT[7]), .pin17(PORT_OUTPUT[6]),
    .pin16(PORT_OUTPUT_B[6]), .pin15(PORT_OUTPUT_B[5]), .pin14(PORT_OUTPUT[5]), .pin13(PORT_OUTPUT[4]),
    .pin12(PORT_OUTPUT_B[4]), .pin11(write_B));
  _74377 u_74377_4 (
    .pin1(n74377_4_pin1), .pin2(PORT_OUTPUT_D[0]), .pin3(PORT_OUTPUT[0]), .pin4(PORT_OUTPUT[1]),
    .pin5(PORT_OUTPUT_D[1]), .pin6(PORT_OUTPUT_D[2]), .pin7(PORT_OUTPUT[2]), .pin8(PORT_OUTPUT[3]),
    .pin9(PORT_OUTPUT_D[3]), .pin19(PORT_OUTPUT_D[7]), .pin18(PORT_OUTPUT[7]), .pin17(PORT_OUTPUT[6]),
    .pin16(PORT_OUTPUT_D[6]), .pin15(PORT_OUTPUT_D[5]), .pin14(PORT_OUTPUT[5]), .pin13(PORT_OUTPUT[4]),
    .pin12(PORT_OUTPUT_D[4]), .pin11(write_D));
  _74244 u_74244_5 (
    .pin1(read_B), .pin2(PORT_INPUT_B[0]), .pin3(PORT_INPUT[4]), .pin4(PORT_INPUT_B[1]),
    .pin5(PORT_INPUT[5]), .pin6(PORT_INPUT_B[2]), .pin7(PORT_INPUT[6]), .pin8(PORT_INPUT_B[3]),
    .pin9(PORT_INPUT[7]), .pin19(read_B), .pin18(PORT_INPUT[0]), .pin17(PORT_INPUT_B[7]),
    .pin16(PORT_INPUT[1]), .pin15(PORT_INPUT_B[6]), .pin14(PORT_INPUT[2]), .pin13(PORT_INPUT_B[5]),
    .pin12(PORT_INPUT[3]), .pin11(PORT_INPUT_B[4]));
  _74244 u_74244_6 (
    .pin1(read_D), .pin2(PORT_INPUT_D[0]), .pin3(PORT_INPUT[4]), .pin4(PORT_INPUT_D[1]),
    .pin5(PORT_INPUT[5]), .pin6(PORT_INPUT_D[2]), .pin7(PORT_INPUT[6]), .pin8(PORT_INPUT_D[3]),
    .pin9(PORT_INPUT[7]), .pin19(read_D), .pin18(PORT_INPUT[0]), .pin17(PORT_INPUT_D[7]),
    .pin16(PORT_INPUT[1]), .pin15(PORT_INPUT_D[6]), .pin14(PORT_INPUT[2]), .pin13(PORT_INPUT_D[5]),
    .pin12(PORT_INPUT[3]), .pin11(PORT_INPUT_D[4]));

  assign PORT_ADDR = ADDR[7:0];
  // also tied to GND on the sheet: {n74377_1_pin1, n74377_2_pin1, n74377_3_pin1, n74377_4_pin1}

  // Other names for the same wires on the sheet: addr_t[7:0] = ADDR[7:0]
endmodule

module mar_reg (
  input  [7:0] DATA_IN,
  input  INC,
  input  [4:0] RD_ADDR,
  input  nADDR_SEL,
  input  CLOCK,
  input  WR_ENABLE,
  input  [4:0] WR_ADDR,
  output [7:0] DATA_OUT,
  output [15:0] ADDR
);

  wire count_0, count_1, count_2, count_3, count_4, count_5, count_6, count_7, count_8, count_9, count_10,
       count_11, count_12, count_13, count_14, count_15, LOAD_HIGH, LOAD_LOW, n7404_1_pin6, n74138_1_pin4,
       n74138_2_pin4, n74138_2_pin5, n74193_1_pin4, n74193_1_pin5, n74193_2_pin4, n74193_2_pin5,
       n74193_3_pin4, n74193_3_pin5, n74193_4_pin4, n_clock, READ_HIGH, READ_LOW;

  _74193 u_74193_1 (
    .pin1(DATA_IN[5]), .pin2(count_13), .pin3(count_12), .pin4(n74193_1_pin4), .pin5(n74193_1_pin5),
    .pin6(count_14), .pin7(count_15), .pin15(DATA_IN[4]), .pin11(LOAD_HIGH), .pin10(DATA_IN[6]),
    .pin9(DATA_IN[7]));  // open: pin14, pin13, pin12
  _74244 u_74244_1 (
    .pin1(READ_HIGH), .pin2(count_8), .pin3(DATA_OUT[6]), .pin4(count_9), .pin5(DATA_OUT[7]),
    .pin6(count_10), .pin7(DATA_OUT[5]), .pin8(count_11), .pin9(DATA_OUT[4]), .pin19(READ_HIGH),
    .pin18(DATA_OUT[0]), .pin17(count_15), .pin16(DATA_OUT[1]), .pin15(count_14), .pin14(DATA_OUT[2]),
    .pin13(count_13), .pin12(DATA_OUT[3]), .pin11(count_12));
  _74193 u_74193_2 (
    .pin1(DATA_IN[1]), .pin2(count_9), .pin3(count_8), .pin4(n74193_2_pin4), .pin5(n74193_2_pin5),
    .pin6(count_10), .pin7(count_11), .pin15(DATA_IN[0]), .pin13(n74193_1_pin4), .pin12(n74193_1_pin5),
    .pin11(LOAD_HIGH), .pin10(DATA_IN[2]), .pin9(DATA_IN[3]));  // open: pin14
  _74244 u_74244_2 (
    .pin1(nADDR_SEL), .pin2(count_8), .pin3(ADDR[15]), .pin4(count_9), .pin5(ADDR[14]), .pin6(count_10),
    .pin7(ADDR[13]), .pin8(count_11), .pin9(ADDR[12]), .pin19(nADDR_SEL), .pin18(ADDR[8]), .pin17(count_15),
    .pin16(ADDR[9]), .pin15(count_14), .pin14(ADDR[10]), .pin13(count_13), .pin12(ADDR[11]), .pin11(count_12));
  _74193 u_74193_3 (
    .pin1(DATA_IN[5]), .pin2(count_5), .pin3(count_4), .pin4(n74193_3_pin4), .pin5(n74193_3_pin5),
    .pin6(count_6), .pin7(count_7), .pin15(DATA_IN[4]), .pin13(n74193_2_pin4), .pin12(n74193_2_pin5),
    .pin11(LOAD_LOW), .pin10(DATA_IN[6]), .pin9(DATA_IN[7]));  // open: pin14
  _74244 u_74244_3 (
    .pin1(READ_LOW), .pin2(count_0), .pin3(DATA_OUT[6]), .pin4(count_1), .pin5(DATA_OUT[7]), .pin6(count_2),
    .pin7(DATA_OUT[5]), .pin8(count_3), .pin9(DATA_OUT[4]), .pin19(READ_LOW), .pin18(DATA_OUT[0]),
    .pin17(count_7), .pin16(DATA_OUT[1]), .pin15(count_6), .pin14(DATA_OUT[2]), .pin13(count_5),
    .pin12(DATA_OUT[3]), .pin11(count_4));
  _74244 u_74244_4 (
    .pin1(nADDR_SEL), .pin2(count_0), .pin3(ADDR[7]), .pin4(count_1), .pin5(ADDR[6]), .pin6(count_2),
    .pin7(ADDR[5]), .pin8(count_3), .pin9(ADDR[4]), .pin19(nADDR_SEL), .pin18(ADDR[0]), .pin17(count_7),
    .pin16(ADDR[1]), .pin15(count_6), .pin14(ADDR[2]), .pin13(count_5), .pin12(ADDR[3]), .pin11(count_4));
  _74193 u_74193_4 (
    .pin1(DATA_IN[1]), .pin2(count_1), .pin3(count_0), .pin4(n74193_4_pin4), .pin5(INC), .pin6(count_2),
    .pin7(count_3), .pin15(DATA_IN[0]), .pin13(n74193_3_pin4), .pin12(n74193_3_pin5), .pin11(LOAD_LOW),
    .pin10(DATA_IN[2]), .pin9(DATA_IN[3]));  // open: pin14
  _74138 u_74138_1 (
    .pin1(RD_ADDR[0]), .pin2(RD_ADDR[1]), .pin3(RD_ADDR[2]), .pin4(n74138_1_pin4), .pin5(n74138_1_pin4),
    .pin6(RD_ADDR[4]), .pin11(READ_LOW), .pin10(READ_HIGH));  // open: pin7, pin15, pin14, pin13, pin12, pin9
  _74138 u_74138_2 (
    .pin1(WR_ADDR[0]), .pin2(WR_ADDR[1]), .pin3(WR_ADDR[2]), .pin4(n74138_2_pin4), .pin5(n74138_2_pin5),
    .pin6(WR_ADDR[4]), .pin11(LOAD_LOW), .pin10(LOAD_HIGH));  // open: pin7, pin15, pin14, pin13, pin12, pin9
  _7404 u_7404_1 (
    .pin1(CLOCK), .pin2(n_clock), .pin3(WR_ADDR[3]), .pin4(n74138_2_pin5), .pin5(WR_ENABLE),
    .pin6(n7404_1_pin6), .pin13(RD_ADDR[3]), .pin12(n74138_1_pin4));  // open: pin11, pin10, pin9, pin8
  or or_1 (n74138_2_pin4, n7404_1_pin6, n_clock);
  // also tied to VCC on the sheet: n74193_4_pin4

  // Other names for the same wires on the sheet: addr_0 = ADDR[0]; addr_1 = ADDR[1]; addr_2 = ADDR[2];
  //   addr_3 = ADDR[3]; addr_4 = ADDR[4]; addr_5 = ADDR[5]; addr_6 = ADDR[6]; addr_7 = ADDR[7]; addr_8 = ADDR[8];
  //   addr_9 = ADDR[9]; addr_10 = ADDR[10]; addr_11 = ADDR[11]; addr_12 = ADDR[12]; addr_13 = ADDR[13];
  //   addr_14 = ADDR[14]; addr_15 = ADDR[15]; data_in_0 = DATA_IN[0]; data_in_1 = DATA_IN[1]; data_in_2 = DATA_IN[2];
  //   data_in_3 = DATA_IN[3]; data_in_4 = DATA_IN[4]; data_in_5 = DATA_IN[5]; data_in_6 = DATA_IN[6];
  //   data_in_7 = DATA_IN[7]; data_out_0 = DATA_OUT[0]; data_out_1 = DATA_OUT[1]; data_out_2 = DATA_OUT[2];
  //   data_out_3 = DATA_OUT[3]; data_out_4 = DATA_OUT[4]; data_out_5 = DATA_OUT[5]; data_out_6 = DATA_OUT[6];
  //   data_out_7 = DATA_OUT[7]
endmodule

module pc_reg (
  input  [7:0] DATA_IN,
  input  nINC,
  input  [4:0] RD_ADDR,
  input  nADDR_SEL,
  input  WR_ENABLE,
  input  CLOCK,
  input  [4:0] WR_ADDR,
  output [7:0] DATA_OUT,
  output [15:0] ADDR,
  output [15:0] DEBUG_PC
);

  wire LOAD_HIGH, LOAD_LOW, n7404_1_pin6, n74138_1_pin4, n74138_2_pin4, n74138_2_pin5, n74193_1_pin4,
       n74193_1_pin5, n74193_2_pin4, n74193_2_pin5, n74193_3_pin4, n74193_3_pin5, n74193_4_pin4,
       n74193_4_pin5, n_clock, READ_HIGH, READ_LOW;

  _74193 u_74193_1 (
    .pin1(DATA_IN[5]), .pin2(DEBUG_PC[13]), .pin3(DEBUG_PC[12]), .pin4(n74193_1_pin4), .pin5(n74193_1_pin5),
    .pin6(DEBUG_PC[14]), .pin7(DEBUG_PC[15]), .pin15(DATA_IN[4]), .pin11(LOAD_HIGH), .pin10(DATA_IN[6]),
    .pin9(DATA_IN[7]));  // open: pin14, pin13, pin12
  _74244 u_74244_1 (
    .pin1(READ_HIGH), .pin2(DEBUG_PC[8]), .pin3(DATA_OUT[6]), .pin4(DEBUG_PC[9]), .pin5(DATA_OUT[7]),
    .pin6(DEBUG_PC[10]), .pin7(DATA_OUT[5]), .pin8(DEBUG_PC[11]), .pin9(DATA_OUT[4]), .pin19(READ_HIGH),
    .pin18(DATA_OUT[0]), .pin17(DEBUG_PC[15]), .pin16(DATA_OUT[1]), .pin15(DEBUG_PC[14]),
    .pin14(DATA_OUT[2]), .pin13(DEBUG_PC[13]), .pin12(DATA_OUT[3]), .pin11(DEBUG_PC[12]));
  _74193 u_74193_2 (
    .pin1(DATA_IN[1]), .pin2(DEBUG_PC[9]), .pin3(DEBUG_PC[8]), .pin4(n74193_2_pin4), .pin5(n74193_2_pin5),
    .pin6(DEBUG_PC[10]), .pin7(DEBUG_PC[11]), .pin15(DATA_IN[0]), .pin13(n74193_1_pin4),
    .pin12(n74193_1_pin5), .pin11(LOAD_HIGH), .pin10(DATA_IN[2]), .pin9(DATA_IN[3]));  // open: pin14
  _74244 u_74244_2 (
    .pin1(nADDR_SEL), .pin2(DEBUG_PC[8]), .pin3(ADDR[15]), .pin4(DEBUG_PC[9]), .pin5(ADDR[14]),
    .pin6(DEBUG_PC[10]), .pin7(ADDR[13]), .pin8(DEBUG_PC[11]), .pin9(ADDR[12]), .pin19(nADDR_SEL),
    .pin18(ADDR[8]), .pin17(DEBUG_PC[15]), .pin16(ADDR[9]), .pin15(DEBUG_PC[14]), .pin14(ADDR[10]),
    .pin13(DEBUG_PC[13]), .pin12(ADDR[11]), .pin11(DEBUG_PC[12]));
  _74193 u_74193_3 (
    .pin1(DATA_IN[5]), .pin2(DEBUG_PC[5]), .pin3(DEBUG_PC[4]), .pin4(n74193_3_pin4), .pin5(n74193_3_pin5),
    .pin6(DEBUG_PC[6]), .pin7(DEBUG_PC[7]), .pin15(DATA_IN[4]), .pin13(n74193_2_pin4), .pin12(n74193_2_pin5),
    .pin11(LOAD_LOW), .pin10(DATA_IN[6]), .pin9(DATA_IN[7]));  // open: pin14
  _74244 u_74244_3 (
    .pin1(READ_LOW), .pin2(DEBUG_PC[0]), .pin3(DATA_OUT[6]), .pin4(DEBUG_PC[1]), .pin5(DATA_OUT[7]),
    .pin6(DEBUG_PC[2]), .pin7(DATA_OUT[5]), .pin8(DEBUG_PC[3]), .pin9(DATA_OUT[4]), .pin19(READ_LOW),
    .pin18(DATA_OUT[0]), .pin17(DEBUG_PC[7]), .pin16(DATA_OUT[1]), .pin15(DEBUG_PC[6]), .pin14(DATA_OUT[2]),
    .pin13(DEBUG_PC[5]), .pin12(DATA_OUT[3]), .pin11(DEBUG_PC[4]));
  _74244 u_74244_4 (
    .pin1(nADDR_SEL), .pin2(DEBUG_PC[0]), .pin3(ADDR[7]), .pin4(DEBUG_PC[1]), .pin5(ADDR[6]),
    .pin6(DEBUG_PC[2]), .pin7(ADDR[5]), .pin8(DEBUG_PC[3]), .pin9(ADDR[4]), .pin19(nADDR_SEL),
    .pin18(ADDR[0]), .pin17(DEBUG_PC[7]), .pin16(ADDR[1]), .pin15(DEBUG_PC[6]), .pin14(ADDR[2]),
    .pin13(DEBUG_PC[5]), .pin12(ADDR[3]), .pin11(DEBUG_PC[4]));
  _74193 u_74193_4 (
    .pin1(DATA_IN[1]), .pin2(DEBUG_PC[1]), .pin3(DEBUG_PC[0]), .pin4(n74193_4_pin4), .pin5(n74193_4_pin5),
    .pin6(DEBUG_PC[2]), .pin7(DEBUG_PC[3]), .pin15(DATA_IN[0]), .pin13(n74193_3_pin4), .pin12(n74193_3_pin5),
    .pin11(LOAD_LOW), .pin10(DATA_IN[2]), .pin9(DATA_IN[3]));  // open: pin14
  or or_1 (n74193_4_pin5, n_clock, nINC);
  _74138 u_74138_1 (
    .pin1(RD_ADDR[0]), .pin2(RD_ADDR[1]), .pin3(RD_ADDR[2]), .pin4(n74138_1_pin4), .pin5(n74138_1_pin4),
    .pin6(RD_ADDR[4]), .pin15(READ_LOW), .pin14(READ_HIGH));  // open: pin7, pin13, pin12, pin11, pin10, pin9
  _74138 u_74138_2 (
    .pin1(WR_ADDR[0]), .pin2(WR_ADDR[1]), .pin3(WR_ADDR[2]), .pin4(n74138_2_pin4), .pin5(n74138_2_pin5),
    .pin6(WR_ADDR[4]), .pin15(LOAD_LOW), .pin14(LOAD_HIGH));  // open: pin7, pin13, pin12, pin11, pin10, pin9
  _7404 u_7404_1 (
    .pin1(CLOCK), .pin2(n_clock), .pin3(WR_ADDR[3]), .pin4(n74138_2_pin4), .pin5(WR_ENABLE),
    .pin6(n7404_1_pin6), .pin13(RD_ADDR[3]), .pin12(n74138_1_pin4));  // open: pin11, pin10, pin9, pin8
  or or_2 (n74138_2_pin5, n7404_1_pin6, n_clock);
  // also tied to VCC on the sheet: n74193_4_pin4

  // Other names for the same wires on the sheet: addr_0 = ADDR[0]; addr_1 = ADDR[1]; addr_2 = ADDR[2];
  //   addr_3 = ADDR[3]; addr_4 = ADDR[4]; addr_5 = ADDR[5]; addr_6 = ADDR[6]; addr_7 = ADDR[7]; addr_8 = ADDR[8];
  //   addr_9 = ADDR[9]; addr_10 = ADDR[10]; addr_11 = ADDR[11]; addr_12 = ADDR[12]; addr_13 = ADDR[13];
  //   addr_14 = ADDR[14]; addr_15 = ADDR[15]; data_in_0 = DATA_IN[0]; data_in_1 = DATA_IN[1]; data_in_2 = DATA_IN[2];
  //   data_in_3 = DATA_IN[3]; data_in_4 = DATA_IN[4]; data_in_5 = DATA_IN[5]; data_in_6 = DATA_IN[6];
  //   data_in_7 = DATA_IN[7]; data_out_0 = DATA_OUT[0]; data_out_1 = DATA_OUT[1]; data_out_2 = DATA_OUT[2];
  //   data_out_3 = DATA_OUT[3]; data_out_4 = DATA_OUT[4]; data_out_5 = DATA_OUT[5]; data_out_6 = DATA_OUT[6];
  //   data_out_7 = DATA_OUT[7]; count_0 = DEBUG_PC[0]; count_1 = DEBUG_PC[1]; count_2 = DEBUG_PC[2];
  //   count_3 = DEBUG_PC[3]; count_4 = DEBUG_PC[4]; count_5 = DEBUG_PC[5]; count_6 = DEBUG_PC[6];
  //   count_7 = DEBUG_PC[7]; count_8 = DEBUG_PC[8]; count_9 = DEBUG_PC[9]; count_10 = DEBUG_PC[10];
  //   count_11 = DEBUG_PC[11]; count_12 = DEBUG_PC[12]; count_13 = DEBUG_PC[13]; count_14 = DEBUG_PC[14];
  //   count_15 = DEBUG_PC[15]
endmodule

module ula_8 (
  input  CLOCK,
  input  [4:0] WRITE_ADDR,
  input  [4:0] READ_ADDR,
  input  WR_ENABLE,
  input  ULA_ENABLE,
  input  INTMASK_FLAG,
  input  [7:0] DATA_IN,
  output [7:0] DEBUG_ACC,
  output [7:0] DATA_OUT,
  output ZERO_FLAG,
  output CARRY_FLAG,
  output OVERFLOW_FLAG,
  output NEGATIVE_FLAG
);

  wire acc_read, acc_write, adder_carry_result, and_1_out, and_2_out, carry_result, clr_cf, flags_read,
       flags_write, invert_lower_bus, invert_ula_bus, invert_upper_bus, n7400_1_pin11, n7400_1_pin12,
       n7400_1_pin13, n7404_1_pin2, n7404_1_pin4, n7404_1_pin6, n7404_1_pin10, n7404_2_pin2, n7404_2_pin4,
       n7404_2_pin6, n7404_2_pin8, n7404_2_pin10, n7432_1_pin3, n7432_1_pin6, n7432_1_pin8, n7432_1_pin11,
       n7432_2_pin3, n7432_2_pin6, n7432_2_pin8, n7432_2_pin11, n7474_1_pin13, n7474_2_pin1, n7486_1_pin3,
       n7486_1_pin6, n7486_1_pin8, n7486_1_pin11, n7486_2_pin3, n7486_2_pin6, n7486_2_pin8, n7486_7_pin3,
       n7486_7_pin6, n7486_7_pin8, n7486_7_pin11, n7486_8_pin3, n7486_8_pin6, n7486_8_pin8, n7486_8_pin11,
       n7486_9_pin3, n7486_9_pin5, n7486_9_pin9, n74125_2_pin1, n74138_3_pin7, n74138_3_pin9, n74138_3_pin11,
       n74138_3_pin12, n74138_3_pin13, n74138_3_pin14, n74138_3_pin15, n74138_4_pin4, n74138_4_pin13,
       n74138_4_pin14, n74138_4_pin15, n74157_1_pin15, n74157_2_pin15, n74244_3_pin2, n74244_8_pin17,
       n74244_9_pin17, n74283_1_pin1, n74283_1_pin4, n74283_1_pin9, n74283_1_pin10, n74283_1_pin13,
       n74283_2_pin1, n74283_2_pin4, n74283_2_pin10, n74283_2_pin13, n_clock, negative_result, not_2_out,
       not_4_out, not_5_out, or_1_out, or_2_out, or_3_out, or_4_out, or_6_out, overflow_result, rotate,
       select_adder, select_left_shifter, select_logic, select_right_shifter, select_sx, select_xor, set_cf,
       ula_carry_result, ula_negative_result, ula_overflow_result, ula_zero_result, zero_result;
  wire [7:0] lower_bus, ula_bus, upper_bus;

  LED #(.active("false")) led_1 (.in(select_xor));
  LED #(.active("false")) led_2 (.in(select_right_shifter));
  LED #(.active("false")) led_3 (.in(select_logic));
  LED #(.active("false")) led_4 (.in(select_adder));
  LED #(.active("false")) led_5 (.in(select_left_shifter));
  LED #(.active("false")) led_6 (.in(select_sx));
  LED led_7 (.in(rotate));
  not not_1 (ula_zero_result, or_1_out);
  _74283 u_74283_1 (
    .pin1(n74283_1_pin1), .pin2(upper_bus[1]), .pin3(lower_bus[1]), .pin4(n74283_1_pin4),
    .pin5(upper_bus[0]), .pin6(lower_bus[0]), .pin7(CARRY_FLAG), .pin15(lower_bus[2]), .pin14(upper_bus[2]),
    .pin13(n74283_1_pin13), .pin12(upper_bus[3]), .pin11(lower_bus[3]), .pin10(n74283_1_pin10),
    .pin9(n74283_1_pin9));
  _74283 u_74283_2 (
    .pin1(n74283_2_pin1), .pin2(lower_bus[5]), .pin3(upper_bus[5]), .pin4(n74283_2_pin4),
    .pin5(upper_bus[4]), .pin6(lower_bus[4]), .pin7(n74283_1_pin9), .pin15(lower_bus[6]),
    .pin14(upper_bus[6]), .pin13(n74283_2_pin13), .pin12(upper_bus[7]), .pin11(lower_bus[7]),
    .pin10(n74283_2_pin10), .pin9(adder_carry_result));
  _7432 u_7432_1 (
    .pin1(upper_bus[0]), .pin2(lower_bus[0]), .pin3(n7432_1_pin3), .pin4(upper_bus[1]), .pin5(lower_bus[1]),
    .pin6(n7432_1_pin6), .pin13(lower_bus[2]), .pin12(upper_bus[2]), .pin11(n7432_1_pin11),
    .pin10(upper_bus[3]), .pin9(lower_bus[3]), .pin8(n7432_1_pin8));
  _7432 u_7432_2 (
    .pin1(lower_bus[4]), .pin2(upper_bus[4]), .pin3(n7432_2_pin3), .pin4(lower_bus[5]), .pin5(upper_bus[5]),
    .pin6(n7432_2_pin6), .pin13(lower_bus[6]), .pin12(upper_bus[6]), .pin11(n7432_2_pin11),
    .pin10(upper_bus[7]), .pin9(lower_bus[7]), .pin8(n7432_2_pin8));
  LED led_8 (.in(invert_upper_bus));
  LED led_9 (.in(invert_ula_bus));
  LED led_10 (.in(invert_lower_bus));
  LED #(.active("false")) led_11 (.in(set_cf));
  LED #(.active("false")) led_12 (.in(clr_cf));
  not not_2 (not_2_out, ULA_ENABLE);
  _7486 u_7486_1 (
    .pin1(ula_bus[0]), .pin2(invert_ula_bus), .pin3(n7486_1_pin3), .pin4(ula_bus[1]), .pin5(invert_ula_bus),
    .pin6(n7486_1_pin6), .pin13(ula_bus[3]), .pin12(invert_ula_bus), .pin11(n7486_1_pin11),
    .pin10(ula_bus[2]), .pin9(invert_ula_bus), .pin8(n7486_1_pin8));
  _7486 u_7486_2 (
    .pin1(ula_bus[4]), .pin2(invert_ula_bus), .pin3(n7486_2_pin3), .pin4(ula_bus[5]), .pin5(invert_ula_bus),
    .pin6(n7486_2_pin6), .pin13(ula_bus[7]), .pin12(invert_ula_bus), .pin11(ula_negative_result),
    .pin10(ula_bus[6]), .pin9(invert_ula_bus), .pin8(n7486_2_pin8));
  or or_1 (or_1_out, n7486_1_pin3, n7486_1_pin6, n7486_1_pin8, n7486_1_pin11, n7486_2_pin3, n7486_2_pin6, n7486_2_pin8, ula_negative_result);
  _74244 u_74244_1 (
    .pin1(flags_write), .pin2(DATA_IN[0]), .pin4(DATA_IN[1]), .pin6(DATA_IN[2]), .pin8(DATA_IN[3]),
    .pin19(flags_write), .pin18(zero_result), .pin16(carry_result), .pin14(overflow_result),
    .pin12(negative_result));  // open: pin3, pin5, pin7, pin9, pin17, pin15, pin13, pin11
  _74244 u_74244_2 (
    .pin1(select_sx), .pin2(lower_bus[7]), .pin3(ula_bus[7]), .pin4(lower_bus[7]), .pin5(ula_bus[6]),
    .pin6(lower_bus[7]), .pin7(ula_bus[5]), .pin8(lower_bus[7]), .pin9(ula_bus[4]), .pin19(select_sx),
    .pin18(ula_bus[0]), .pin17(lower_bus[7]), .pin16(ula_bus[1]), .pin15(lower_bus[7]), .pin14(ula_bus[2]),
    .pin13(lower_bus[7]), .pin12(ula_bus[3]), .pin11(lower_bus[7]));
  and and_1 (and_1_out, acc_write, not_2_out);
  _7486 u_7486_3 (
    .pin1(DATA_IN[0]), .pin2(invert_lower_bus), .pin3(lower_bus[0]), .pin4(DATA_IN[1]),
    .pin5(invert_lower_bus), .pin6(lower_bus[1]), .pin13(DATA_IN[3]), .pin12(invert_lower_bus),
    .pin11(lower_bus[3]), .pin10(DATA_IN[2]), .pin9(invert_lower_bus), .pin8(lower_bus[2]));
  _7486 u_7486_4 (
    .pin1(DATA_IN[4]), .pin2(invert_lower_bus), .pin3(lower_bus[4]), .pin4(DATA_IN[5]),
    .pin5(invert_lower_bus), .pin6(lower_bus[5]), .pin13(DATA_IN[7]), .pin12(invert_lower_bus),
    .pin11(lower_bus[7]), .pin10(DATA_IN[6]), .pin9(invert_lower_bus), .pin8(lower_bus[6]));
  _74125 u_74125_1 (
    .pin1(select_adder), .pin2(adder_carry_result), .pin3(ula_carry_result), .pin4(select_left_shifter),
    .pin5(lower_bus[7]), .pin6(ula_carry_result), .pin10(select_right_shifter), .pin9(lower_bus[0]),
    .pin8(ula_carry_result));  // open: pin13, pin12, pin11
  Pull_Resistor pull_resistor_1 (.node(ula_carry_result));
  _74244 u_74244_3 (
    .pin1(select_left_shifter), .pin2(n74244_3_pin2), .pin3(ula_bus[7]), .pin4(lower_bus[0]),
    .pin5(ula_bus[6]), .pin6(lower_bus[1]), .pin7(ula_bus[5]), .pin8(lower_bus[2]), .pin9(ula_bus[4]),
    .pin19(select_left_shifter), .pin18(ula_bus[0]), .pin17(lower_bus[6]), .pin16(ula_bus[1]),
    .pin15(lower_bus[5]), .pin14(ula_bus[2]), .pin13(lower_bus[4]), .pin12(ula_bus[3]), .pin11(lower_bus[3]));
  _74377 u_74377_1 (
    .pin1(and_1_out), .pin2(DEBUG_ACC[0]), .pin3(n7486_1_pin3), .pin4(n7486_1_pin6), .pin5(DEBUG_ACC[1]),
    .pin6(DEBUG_ACC[2]), .pin7(n7486_1_pin8), .pin8(n7486_1_pin11), .pin9(DEBUG_ACC[3]),
    .pin19(DEBUG_ACC[7]), .pin18(ula_negative_result), .pin17(n7486_2_pin8), .pin16(DEBUG_ACC[6]),
    .pin15(DEBUG_ACC[5]), .pin14(n7486_2_pin6), .pin13(n7486_2_pin3), .pin12(DEBUG_ACC[4]), .pin11(CLOCK));
  _74157 u_74157_1 (
    .pin1(rotate), .pin2(CARRY_FLAG), .pin3(lower_bus[7]), .pin4(n74244_3_pin2), .pin15(n74157_1_pin15));  // open: pin5, pin6, pin7, pin14, pin13, pin12, pin11, pin10, pin9
  _7486 u_7486_5 (
    .pin1(DEBUG_ACC[0]), .pin2(invert_upper_bus), .pin3(upper_bus[0]), .pin4(DEBUG_ACC[1]),
    .pin5(invert_upper_bus), .pin6(upper_bus[1]), .pin13(DEBUG_ACC[3]), .pin12(invert_upper_bus),
    .pin11(upper_bus[3]), .pin10(DEBUG_ACC[2]), .pin9(invert_upper_bus), .pin8(upper_bus[2]));
  _74244 u_74244_4 (
    .pin1(select_adder), .pin2(n74283_1_pin4), .pin3(ula_bus[7]), .pin4(n74283_1_pin1), .pin5(ula_bus[6]),
    .pin6(n74283_1_pin13), .pin7(ula_bus[5]), .pin8(n74283_1_pin10), .pin9(ula_bus[4]), .pin19(select_adder),
    .pin18(ula_bus[0]), .pin17(n74283_2_pin10), .pin16(ula_bus[1]), .pin15(n74283_2_pin13),
    .pin14(ula_bus[2]), .pin13(n74283_2_pin1), .pin12(ula_bus[3]), .pin11(n74283_2_pin4));
  _74244 u_74244_5 (
    .pin1(select_logic), .pin2(n7432_1_pin3), .pin3(ula_bus[7]), .pin4(n7432_1_pin6), .pin5(ula_bus[6]),
    .pin6(n7432_1_pin11), .pin7(ula_bus[5]), .pin8(n7432_1_pin8), .pin9(ula_bus[4]), .pin19(select_logic),
    .pin18(ula_bus[0]), .pin17(n7432_2_pin8), .pin16(ula_bus[1]), .pin15(n7432_2_pin11), .pin14(ula_bus[2]),
    .pin13(n7432_2_pin6), .pin12(ula_bus[3]), .pin11(n7432_2_pin3));
  _74244 u_74244_6 (
    .pin1(acc_write), .pin2(lower_bus[0]), .pin3(ula_bus[7]), .pin4(lower_bus[1]), .pin5(ula_bus[6]),
    .pin6(lower_bus[2]), .pin7(ula_bus[5]), .pin8(lower_bus[3]), .pin9(ula_bus[4]), .pin19(acc_write),
    .pin18(ula_bus[0]), .pin17(lower_bus[7]), .pin16(ula_bus[1]), .pin15(lower_bus[6]), .pin14(ula_bus[2]),
    .pin13(lower_bus[5]), .pin12(ula_bus[3]), .pin11(lower_bus[4]));
  _74244 u_74244_7 (
    .pin1(acc_read), .pin2(DEBUG_ACC[0]), .pin3(DATA_OUT[7]), .pin4(DEBUG_ACC[1]), .pin5(DATA_OUT[6]),
    .pin6(DEBUG_ACC[2]), .pin7(DATA_OUT[5]), .pin8(DEBUG_ACC[3]), .pin9(DATA_OUT[4]), .pin19(acc_read),
    .pin18(DATA_OUT[0]), .pin17(DEBUG_ACC[7]), .pin16(DATA_OUT[1]), .pin15(DEBUG_ACC[6]),
    .pin14(DATA_OUT[2]), .pin13(DEBUG_ACC[5]), .pin12(DATA_OUT[3]), .pin11(DEBUG_ACC[4]));
  _7486 u_7486_6 (
    .pin1(DEBUG_ACC[4]), .pin2(invert_upper_bus), .pin3(upper_bus[4]), .pin4(DEBUG_ACC[5]),
    .pin5(invert_upper_bus), .pin6(upper_bus[5]), .pin13(DEBUG_ACC[4]), .pin12(invert_upper_bus),
    .pin11(upper_bus[7]), .pin10(DEBUG_ACC[6]), .pin9(invert_upper_bus), .pin8(upper_bus[6]));
  not not_3 (n_clock, CLOCK);
  _74138 u_74138_1 (
    .pin1(READ_ADDR[0]), .pin2(READ_ADDR[1]), .pin3(READ_ADDR[2]), .pin4(READ_ADDR[3]), .pin5(READ_ADDR[3]),
    .pin6(READ_ADDR[4]), .pin11(flags_read), .pin10(acc_read));  // open: pin7, pin15, pin14, pin13, pin12, pin9
  not not_4 (not_4_out, flags_write);
  and and_2 (and_2_out, not_4_out, CLOCK);
  _7474 u_7474_1 (
    .pin1(clr_cf), .pin2(carry_result), .pin3(and_2_out), .pin4(set_cf), .pin5(CARRY_FLAG),
    .pin13(n7474_1_pin13), .pin12(overflow_result), .pin11(and_2_out), .pin10(n7474_1_pin13),
    .pin9(OVERFLOW_FLAG));  // open: pin6, pin8
  _7474 u_7474_2 (
    .pin1(n7474_2_pin1), .pin2(zero_result), .pin3(and_2_out), .pin4(n7474_2_pin1), .pin5(ZERO_FLAG),
    .pin13(n7474_2_pin1), .pin12(negative_result), .pin11(and_2_out), .pin10(n7474_2_pin1),
    .pin9(NEGATIVE_FLAG));  // open: pin6, pin8
  _7486 u_7486_7 (
    .pin1(upper_bus[0]), .pin2(lower_bus[0]), .pin3(n7486_7_pin3), .pin4(upper_bus[1]), .pin5(lower_bus[1]),
    .pin6(n7486_7_pin6), .pin13(lower_bus[2]), .pin12(upper_bus[2]), .pin11(n7486_7_pin11),
    .pin10(upper_bus[3]), .pin9(lower_bus[3]), .pin8(n7486_7_pin8));
  _7486 u_7486_8 (
    .pin1(lower_bus[4]), .pin2(upper_bus[4]), .pin3(n7486_8_pin3), .pin4(lower_bus[5]), .pin5(upper_bus[5]),
    .pin6(n7486_8_pin6), .pin13(lower_bus[6]), .pin12(upper_bus[6]), .pin11(n7486_8_pin11),
    .pin10(upper_bus[7]), .pin9(lower_bus[7]), .pin8(n7486_8_pin8));
  _74244 u_74244_8 (
    .pin1(select_right_shifter), .pin2(lower_bus[1]), .pin3(ula_bus[7]), .pin4(lower_bus[2]),
    .pin5(ula_bus[6]), .pin6(lower_bus[3]), .pin7(ula_bus[5]), .pin8(lower_bus[4]), .pin9(ula_bus[4]),
    .pin19(select_right_shifter), .pin18(ula_bus[0]), .pin17(n74244_8_pin17), .pin16(ula_bus[1]),
    .pin15(lower_bus[7]), .pin14(ula_bus[2]), .pin13(lower_bus[6]), .pin12(ula_bus[3]), .pin11(lower_bus[5]));
  _74244 #(.ShowInternalStructure("true")) u_74244_9 (
    .pin1(flags_read), .pin2(ZERO_FLAG), .pin3(DATA_OUT[7]), .pin4(CARRY_FLAG), .pin5(DATA_OUT[6]),
    .pin6(OVERFLOW_FLAG), .pin7(DATA_OUT[5]), .pin8(NEGATIVE_FLAG), .pin9(DATA_OUT[4]), .pin19(flags_read),
    .pin18(DATA_OUT[0]), .pin17(n74244_9_pin17), .pin16(DATA_OUT[1]), .pin15(n74244_9_pin17),
    .pin14(DATA_OUT[2]), .pin13(n74244_9_pin17), .pin12(DATA_OUT[3]), .pin11(INTMASK_FLAG));
  _7400 #(.ShowInternalStructure("true")) u_7400_1 (
    .pin13(n7400_1_pin13), .pin12(n7400_1_pin12), .pin11(n7400_1_pin11));  // open: pin1, pin2, pin3, pin4, pin5, pin6, pin10, pin9, pin8
  _74157 u_74157_2 (
    .pin1(rotate), .pin2(CARRY_FLAG), .pin3(lower_bus[0]), .pin4(n74244_8_pin17), .pin15(n74157_2_pin15));  // open: pin5, pin6, pin7, pin14, pin13, pin12, pin11, pin10, pin9
  _7486 #(.ShowInternalStructure("true")) u_7486_9 (
    .pin1(lower_bus[7]), .pin2(upper_bus[7]), .pin3(n7486_9_pin3), .pin4(n7486_9_pin3), .pin5(n7486_9_pin5),
    .pin6(n7400_1_pin13), .pin13(ula_negative_result), .pin12(ula_carry_result), .pin11(n7400_1_pin12),
    .pin10(n7400_1_pin11), .pin9(n7486_9_pin9), .pin8(ula_overflow_result));
  not not_5 (not_5_out, WR_ENABLE);
  _74244 u_74244_10 (
    .pin1(select_xor), .pin2(n7486_7_pin3), .pin3(ula_bus[7]), .pin4(n7486_7_pin6), .pin5(ula_bus[6]),
    .pin6(n7486_7_pin11), .pin7(ula_bus[5]), .pin8(n7486_7_pin8), .pin9(ula_bus[4]), .pin19(select_xor),
    .pin18(ula_bus[0]), .pin17(n7486_8_pin8), .pin16(ula_bus[1]), .pin15(n7486_8_pin11), .pin14(ula_bus[2]),
    .pin13(n7486_8_pin6), .pin12(ula_bus[3]), .pin11(n7486_8_pin3));
  _74138 u_74138_2 (
    .pin1(WRITE_ADDR[0]), .pin2(WRITE_ADDR[1]), .pin3(WRITE_ADDR[2]), .pin4(WRITE_ADDR[3]), .pin5(not_5_out),
    .pin6(WRITE_ADDR[4]), .pin11(flags_write), .pin10(acc_write));  // open: pin7, pin15, pin14, pin13, pin12, pin9
  _74125 u_74125_2 (
    .pin1(n74125_2_pin1), .pin2(ula_zero_result), .pin3(zero_result), .pin4(n74125_2_pin1),
    .pin5(ula_carry_result), .pin6(carry_result), .pin13(n74125_2_pin1), .pin12(ula_overflow_result),
    .pin11(overflow_result), .pin10(n74125_2_pin1), .pin9(ula_negative_result), .pin8(negative_result));
  _74138 u_74138_3 (
    .pin1(WRITE_ADDR[0]), .pin2(WRITE_ADDR[1]), .pin3(WRITE_ADDR[2]), .pin4(WRITE_ADDR[3]),
    .pin5(WRITE_ADDR[3]), .pin6(ULA_ENABLE), .pin7(n74138_3_pin7), .pin15(n74138_3_pin15),
    .pin14(n74138_3_pin14), .pin13(n74138_3_pin13), .pin12(n74138_3_pin12), .pin11(n74138_3_pin11),
    .pin10(select_xor), .pin9(n74138_3_pin9));
  _74138 u_74138_4 (
    .pin1(WRITE_ADDR[0]), .pin2(WRITE_ADDR[1]), .pin3(WRITE_ADDR[2]), .pin4(n74138_4_pin4),
    .pin5(n74138_4_pin4), .pin6(ULA_ENABLE), .pin15(n74138_4_pin15), .pin14(n74138_4_pin14),
    .pin13(n74138_4_pin13), .pin12(select_sx), .pin11(set_cf), .pin10(clr_cf));  // open: pin7, pin9
  not not_6 (n74125_2_pin1, ULA_ENABLE);
  _7404 u_7404_1 (
    .pin1(n74138_3_pin15), .pin2(n7404_1_pin2), .pin3(n74138_3_pin14), .pin4(n7404_1_pin4),
    .pin5(n74138_3_pin13), .pin6(n7404_1_pin6), .pin11(n74138_3_pin11), .pin10(n7404_1_pin10),
    .pin9(n74138_3_pin12), .pin8(invert_upper_bus));  // open: pin13, pin12
  _7404 u_7404_2 (
    .pin1(n74138_3_pin9), .pin2(n7404_2_pin2), .pin3(n74138_3_pin7), .pin4(n7404_2_pin4),
    .pin5(n74138_4_pin15), .pin6(n7404_2_pin6), .pin11(n74138_4_pin13), .pin10(n7404_2_pin10),
    .pin9(n74138_4_pin14), .pin8(n7404_2_pin8));  // open: pin13, pin12
  or or_2 (or_2_out, n7404_1_pin2, n7404_1_pin4, n7404_1_pin6);
  or or_3 (or_3_out, n7404_2_pin6, n7404_2_pin10);
  or or_4 (or_4_out, n7404_2_pin4, n7404_2_pin8);
  or or_5 (rotate, n7404_2_pin10, n7404_2_pin8);
  or or_6 (or_6_out, invert_upper_bus, n7404_1_pin10, n7404_2_pin2);
  _7404 u_7404_3 (
    .pin1(or_2_out), .pin2(select_adder), .pin3(or_6_out), .pin4(select_logic), .pin5(or_3_out),
    .pin6(select_left_shifter), .pin13(WRITE_ADDR[3]), .pin12(n74138_4_pin4), .pin9(or_4_out),
    .pin8(select_right_shifter));  // open: pin11, pin10
  or or_7 (invert_lower_bus, invert_upper_bus, n7404_1_pin4, n7404_1_pin6);
  or or_8 (invert_ula_bus, invert_upper_bus, n7404_2_pin2);
  // also tied to GND on the sheet: {n74157_1_pin15, n74157_2_pin15, n74244_9_pin17}
  // also tied to VCC on the sheet: {n7474_2_pin1, n7474_1_pin13, n7486_9_pin5, n7486_9_pin9}

  // Other names for the same wires on the sheet: rshifter_carry_result = lower_bus[0];
  //   lshifter_carry_result = lower_bus[7]

  // Notes on the sheet:
  //   LEFT SHIFTER
  //   SIGN EXTENDER
  //   ADDER
  //   LOGIC
  //   RIGHT SHIFTER
  //   XORER
  //   add
  //   sub
  //   cmp
  //   and
  //   or
  //   xor
  //   not
  //   shr
  //   shl
  //   ror
  //   rol
  //   sx
  //   setcf
  //   clrcf
endmodule
module control_v2 (
  input  RESET,
  input  CLOCK,
  input  INT_REQUESTED,
  input  FLAG_I,
  input  FLAG_Z,
  input  FLAG_C,
  input  FLAG_O,
  input  FLAG_N,
  input  [7:0] IN,
  output nADDR_SEL_PC,
  output nADDR_SEL_SP,
  output RD_ENABLE,
  output nADDR_SEL_MAR,
  output WR_ENABLE,
  output ULA_ENABLE,
  output [3:0] WR_ADDR,
  output nPC_INC,
  output M1,
  output nMAR_INC,
  output nMAR_DEC,
  output nSP_INC,
  output [3:0] RD_ADDR,
  output nSP_DEC,
  output DEBUG_EXTEND,
  output [15:0] ADDR,
  output [7:0] DEBUG_INS
);

  wire and_2_out, and_5_out, and_8_out, and_9_out, and_10_out, and_11_out, clock_t, condition,
       condition_result, constant_0, constant_1, e_xit, extend, finish, halt, handle_interrupt, int_pending,
       n7474_1_pin1, n7474_1_pin2, n7474_1_pin3, n7474_3_pin1, n7474_3_pin6, n74138_1_pin7, n74138_1_pin12,
       n74138_1_pin13, n74138_1_pin15, n74138_2_pin3, n74138_2_pin6, n74138_2_pin14, n74138_2_pin15,
       n74138_3_pin7, n74138_3_pin12, n74138_3_pin13, n74138_5_pin6, n74138_5_pin10, n74138_5_pin11,
       n74138_5_pin12, n74138_5_pin13, n74138_5_pin14, n74175_1_pin4, n74175_1_pin5, n74175_1_pin9,
       n74193_1_pin4, n74244_1_pin2, n74244_1_pin17, n74244_2_pin6, n74244_2_pin17, naddr_sel_constant,
       nclear_interrupt, nclock, not_4_out, not_5_out, not_6_out, not_7_out, not_8_out, not_13_out,
       not_15_out, not_condition, nreset, nreset_extend, nsel_services, or_1_out, or_2_out, reset_counter,
       sel_read_addr, sel_write_addr, xnor_1_out, xnor_2_out, xnor_3_out, xnor_4_out;
  wire [3:0] n74193_1_pin3;
  wire [7:0] rom_1_data;

  not not_1 (nreset, RESET);
  and and_1 (clock_t, halt, CLOCK);
  not not_2 (nclock, clock_t);
  or or_1 (or_1_out, extend, ~handle_interrupt);  // OR_Gate
  _7474 u_7474_1 (
    .pin1(n7474_1_pin1), .pin2(n7474_1_pin2), .pin3(n7474_1_pin3), .pin4(n7474_1_pin2), .pin5(int_pending),
    .pin13(nreset_extend), .pin12(n7474_1_pin2), .pin11(or_1_out), .pin10(nreset), .pin9(DEBUG_EXTEND));  // open: pin6, pin8
  and and_2 (and_2_out, clock_t, condition);
  _7474 u_7474_2 (
    .pin1(nreset), .pin2(IN[0]), .pin3(M1), .pin4(handle_interrupt), .pin5(DEBUG_INS[0]), .pin13(nreset),
    .pin12(IN[1]), .pin11(M1), .pin10(handle_interrupt), .pin9(DEBUG_INS[1]));  // open: pin6, pin8
  and and_3 (n7474_1_pin1, nreset, nclear_interrupt);
  and and_4 (n7474_1_pin3, INT_REQUESTED, FLAG_I);
  and and_5 (and_5_out, e_xit, n7474_3_pin6);
  _7474 u_7474_3 (
    .pin1(n7474_3_pin1), .pin2(condition_result), .pin3(and_2_out), .pin4(n7474_3_pin1), .pin6(n7474_3_pin6));  // open: pin5, pin13, pin12, pin11, pin10, pin9, pin8
  or or_2 (or_2_out, finish, and_5_out);
  ROM #(.addrWidth(13)) rom_1 (.addr({DEBUG_EXTEND, DEBUG_INS, n74193_1_pin3}), .data(rom_1_data));
  _74193 u_74193_1 (
    .pin2(n74193_1_pin3[1]), .pin3(n74193_1_pin3[0]), .pin4(n74193_1_pin4), .pin5(nclock),
    .pin6(n74193_1_pin3[2]), .pin7(n74193_1_pin3[3]), .pin14(reset_counter));  // open: pin1, pin15, pin13, pin12, pin11, pin10, pin9
  not not_3 (nreset_extend, or_2_out);
  or or_3 (reset_counter, or_2_out, RESET, extend);
  _7474 u_7474_4 (
    .pin1(nreset), .pin2(IN[2]), .pin3(M1), .pin4(handle_interrupt), .pin5(DEBUG_INS[2]), .pin13(nreset),
    .pin12(IN[3]), .pin11(M1), .pin10(handle_interrupt), .pin9(DEBUG_INS[3]));  // open: pin6, pin8
  or or_4 (M1, n74138_1_pin15, nclock);
  not not_4 (not_4_out, reset_counter);
  and and_6 (nADDR_SEL_SP, n74138_3_pin12, n74138_1_pin12);
  and and_7 (nADDR_SEL_MAR, n74138_3_pin7, n74138_3_pin13, n74138_1_pin7, n74138_1_pin13);
  _74138 u_74138_1 (
    .pin1(WR_ADDR[0]), .pin2(WR_ADDR[1]), .pin3(WR_ADDR[2]), .pin4(WR_ADDR[3]), .pin5(WR_ADDR[3]),
    .pin6(sel_read_addr), .pin7(n74138_1_pin7), .pin15(n74138_1_pin15), .pin13(n74138_1_pin13),
    .pin12(n74138_1_pin12));  // open: pin14, pin11, pin10, pin9
  _74175 u_74175_1 (
    .pin1(not_4_out), .pin2(constant_0), .pin4(n74175_1_pin4), .pin5(n74175_1_pin5), .pin7(constant_1),
    .pin9(n74175_1_pin9));  // open: pin3, pin6, pin15, pin14, pin13, pin12, pin11, pin10
  not not_5 (not_5_out, rom_1_data[0]);
  not not_6 (not_6_out, rom_1_data[1]);
  not not_7 (not_7_out, rom_1_data[2]);
  not not_8 (not_8_out, rom_1_data[3]);
  not not_9 (n74175_1_pin4, rom_1_data[4]);
  not not_10 (n74175_1_pin5, rom_1_data[5]);
  _74138 u_74138_2 (
    .pin1(rom_1_data[6]), .pin2(rom_1_data[7]), .pin3(n74138_2_pin3), .pin4(n74138_2_pin3),
    .pin5(n74138_2_pin3), .pin6(n74138_2_pin6), .pin15(n74138_2_pin15), .pin14(n74138_2_pin14),
    .pin13(nsel_services));  // open: pin7, pin12, pin11, pin10, pin9
  or or_5 (condition_result, and_8_out, and_9_out, and_10_out, and_11_out);
  not not_11 (sel_write_addr, n74138_2_pin15);
  not not_12 (sel_read_addr, n74138_2_pin14);
  and and_8 (and_8_out, WR_ADDR[0], xnor_1_out);
  and and_9 (and_9_out, WR_ADDR[1], xnor_2_out);
  and and_10 (and_10_out, WR_ADDR[2], xnor_3_out);
  and and_11 (and_11_out, WR_ADDR[3], xnor_4_out);
  _7474 u_7474_5 (
    .pin1(nreset), .pin2(IN[4]), .pin3(M1), .pin4(handle_interrupt), .pin5(DEBUG_INS[4]), .pin13(nreset),
    .pin12(IN[5]), .pin11(M1), .pin10(handle_interrupt), .pin9(DEBUG_INS[5]));  // open: pin6, pin8
  xnor xnor_1 (xnor_1_out, not_condition, FLAG_Z);
  xnor xnor_2 (xnor_2_out, not_condition, FLAG_C);
  xnor xnor_3 (xnor_3_out, not_condition, FLAG_O);
  xnor xnor_4 (xnor_4_out, not_condition, FLAG_N);
  _74175 u_74175_2 (
    .pin1(not_4_out), .pin2(WR_ADDR[0]), .pin4(not_5_out), .pin5(not_6_out), .pin7(WR_ADDR[1]),
    .pin15(WR_ADDR[3]), .pin13(not_8_out), .pin12(not_7_out), .pin10(WR_ADDR[2]), .pin9(n74175_1_pin9));  // open: pin3, pin6, pin14, pin11
  and and_12 (n74175_1_pin9, clock_t, sel_write_addr);
  _7474 u_7474_6 (
    .pin1(nreset), .pin2(IN[6]), .pin3(M1), .pin4(handle_interrupt), .pin5(DEBUG_INS[6]), .pin13(nreset),
    .pin12(IN[7]), .pin11(M1), .pin10(handle_interrupt), .pin9(DEBUG_INS[7]));  // open: pin6, pin8
  and and_13 (RD_ADDR[3], sel_read_addr, not_8_out);
  and and_14 (RD_ADDR[2], sel_read_addr, not_7_out);
  nand nand_1 (handle_interrupt, int_pending, finish);
  _74138 u_74138_3 (
    .pin1(RD_ADDR[0]), .pin2(RD_ADDR[1]), .pin3(RD_ADDR[2]), .pin4(RD_ADDR[3]), .pin5(RD_ADDR[3]),
    .pin6(RD_ENABLE), .pin7(n74138_3_pin7), .pin15(nADDR_SEL_PC), .pin14(naddr_sel_constant),
    .pin13(n74138_3_pin13), .pin12(n74138_3_pin12));  // open: pin11, pin10, pin9
  and and_15 (RD_ADDR[1], sel_read_addr, not_6_out);
  and and_16 (RD_ADDR[0], sel_read_addr, not_5_out);
  and and_17 (RD_ENABLE, sel_read_addr, n74175_1_pin4);
  and and_18 (ULA_ENABLE, sel_read_addr, not_13_out);
  and and_19 (WR_ENABLE, sel_read_addr, n74175_1_pin5);
  _74138 u_74138_4 (
    .pin1(not_5_out), .pin2(not_6_out), .pin3(not_7_out), .pin4(nsel_services), .pin5(nsel_services),
    .pin6(clock_t), .pin14(nPC_INC), .pin13(nMAR_INC), .pin12(nMAR_DEC), .pin11(nSP_INC), .pin10(nSP_DEC),
    .pin9(nclear_interrupt));  // open: pin7, pin15
  not not_13 (not_13_out, n74175_1_pin5);
  _74138 u_74138_5 (
    .pin1(not_8_out), .pin2(n74175_1_pin4), .pin3(n74175_1_pin5), .pin4(nsel_services), .pin5(nsel_services),
    .pin6(n74138_5_pin6), .pin14(n74138_5_pin14), .pin13(n74138_5_pin13), .pin12(n74138_5_pin12),
    .pin11(n74138_5_pin11), .pin10(n74138_5_pin10), .pin9(halt));  // open: pin7, pin15
  not not_14 (e_xit, n74138_5_pin14);
  not not_15 (not_15_out, n74138_5_pin13);
  not not_16 (extend, n74138_5_pin12);
  not not_17 (finish, n74138_5_pin11);
  not not_18 (not_condition, n74138_5_pin10);
  or or_6 (condition, not_15_out, not_condition);
  _74244 u_74244_1 (
    .pin1(naddr_sel_constant), .pin2(n74244_1_pin2), .pin3(ADDR[15]), .pin4(n74244_1_pin2), .pin5(ADDR[14]),
    .pin6(n74244_1_pin2), .pin7(ADDR[13]), .pin8(n74244_1_pin2), .pin9(ADDR[12]), .pin19(naddr_sel_constant),
    .pin18(ADDR[8]), .pin17(n74244_1_pin17), .pin16(ADDR[9]), .pin15(n74244_1_pin17), .pin14(ADDR[10]),
    .pin13(n74244_1_pin17), .pin12(ADDR[11]), .pin11(n74244_1_pin17));
  _74244 u_74244_2 (
    .pin1(naddr_sel_constant), .pin2(constant_0), .pin3(ADDR[7]), .pin4(constant_1), .pin5(ADDR[6]),
    .pin6(n74244_2_pin6), .pin7(ADDR[5]), .pin8(n74244_2_pin6), .pin9(ADDR[4]), .pin19(naddr_sel_constant),
    .pin18(ADDR[0]), .pin17(n74244_2_pin17), .pin16(ADDR[1]), .pin15(n74244_2_pin17), .pin14(ADDR[2]),
    .pin13(n74244_2_pin17), .pin12(ADDR[3]), .pin11(n74244_2_pin17));
  // also tied to GND on the sheet: n74138_2_pin3
  // also tied to VCC on the sheet: {n7474_3_pin1, n7474_1_pin2, n74193_1_pin4, n74138_2_pin6, n74138_5_pin6, n74244_1_pin2, n74244_2_pin6, n74244_1_pin17, n74244_2_pin17}

  // Other names for the same wires on the sheet: ins[7:0] = DEBUG_INS; ins_0 = DEBUG_INS[0]; ins_1 = DEBUG_INS[1];
  //   ins_2 = DEBUG_INS[2]; ins_3 = DEBUG_INS[3]; ins_4 = DEBUG_INS[4]; ins_5 = DEBUG_INS[5]; ins_6 = DEBUG_INS[6];
  //   ins_7 = DEBUG_INS[7]; addr_0 = ADDR[0]; addr_1 = ADDR[1]; addr_2 = ADDR[2]; addr_3 = ADDR[3]; addr_4 = ADDR[4];
  //   addr_5 = ADDR[5]; addr_6 = ADDR[6]; addr_7 = ADDR[7]; addr_8 = ADDR[8]; addr_9 = ADDR[9]; addr_10 = ADDR[10];
  //   addr_11 = ADDR[11]; addr_12 = ADDR[12]; addr_13 = ADDR[13]; addr_14 = ADDR[14]; addr_15 = ADDR[15];
  //   conditions[3:0] = WR_ADDR; data_in_0 = IN[0]; data_in_1 = IN[1]; data_in_2 = IN[2]; data_in_3 = IN[3];
  //   data_in_4 = IN[4]; data_in_5 = IN[5]; data_in_6 = IN[6]; data_in_7 = IN[7]; nwrite_ins = M1

  // Notes on the sheet:
  //   contents of rom_1 (hex, n*v repeats v):
  //   4f 86 98 13*0 4f 86 98 13*0 4f 86 98 13*0 4f 86 98 13*0 4f 86 98 13*0 4f 86 98 13*0 4f 86 98 13*0 4f
  //   86 98 13*0 4f 86 98 13*0 4f 86 98 13*0 4f 86 98 13*0 4f 86 98 13*0 4f 86 9 4f 86 4f 86 6 4d 85 7 4d
  //   98 0 0 0 4f 86 9 4f 86 4f 86 4 4d 85 3 4d 98 0 0 0 4f 86 9 4f 86 4f 86 2 4d 85 4d 98 4*0 4f 86 9 4f
  //   86 4f 86 b 4d 85 a 4d 98 0 0 0 4f 86 98 13*0 4f 86 98 13*0 4f 86 98 13*0 4f 86 98 13*0 4f 86 98 13*0
  //   4f 86 98 13*0 4f 86 0 4f 86 98 10*0 4f 86 7 4f 86 98 10*0 4f 86 6 4f 86 98 10*0 4f 86 5 4f 86 98
  //   10*0 4f 86 3 4f 86 98 10*0 4f 86 4 4f 86 98 10*0 4f 86 1 4f 86 98 10*0 4f 86 98 13*0 4f 86 98 13*0
  //   4f 86 88 98 12*0 4f 86 6 4f 86 7 4f 86 98 7*0 4f 86 4 4f 86 3 4f 86 98 7*0 4f 86 2 4f 86 4f 86 98
  //   8*0 4f 86 9 4f 86 4f b 49 a 49 98 5*0 4f 86 9 46 47 a0 10*0 4f 86 9 44 43 a0 10*0 4f 86 9 42 42 a0
  //   10*0 4f 86 9 4b 4a a0 10*0 4f 86 98 13*0 4f 86 98 13*0 4f 86 98 13*0 4f 86 98 13*0 4f 86 98 13*0 4f
  //   86 98 13*0 4f 86 98 13*0 4f 86 98 13*0 4f 86 9 4f 86 4f 86 0 4d 98 6*0 4f 86 9 4f 86 4f 86 7 4d 98
  //   6*0 4f 86 9 4f 86 4f 86 6 4d 98 6*0 4f 86 9 4f 86 4f 86 5 4d 98 6*0 4f 86 9 4f 86 4f 86 3 4d 98 6*0
  //   4f 86 9 4f 86 4f 86 4 4d 98 6*0 4f 86 9 4f 86 4f 86 1 4d 98 6*0 4f 86 98 13*0 4f 86 98 13*0 4f 86 98
  //   13*0 4f 86 98 13*0 4f 86 98 13*0 4f 86 98 13*0 4f 86 98 13*0 4f 86 98 13*0 4f 86 98 13*0 4f 86 98
  //   13*0 4f 86 98 13*0 4f 86 98 13*0 4f 86 98 13*0 4f 86 98 13*0 4f 86 98 13*0 4f 86 98 13*0 4f 86 98
  //   13*0 4f 86 98 13*0 4f 86 98 13*0 4f 86 31 7f 98 11*0 4f 86 98 13*0 4f 86 98 13*0 4f 86 98 13*0 4f 86
  //   98 13*0 4f 86 98 13*0 4f 86 98 13*0 4f 86 98 13*0 4f 86 98 13*0 4f 86 98 13*0 4f 86 98 13*0 4f 86 98
  //   13*0 4f 86 98 13*0 4f 86 98 13*0 4f 86 98 13*0 4f 86 98 13*0 4f 86 98 13*0 4f 86 98 13*0 4f 86 98
  //   13*0 4f 86 98 13*0 4f 86 98 13*0 4f 86 98 13*0 4f 86 98 13*0 4f 86 98 13*0 4f 86 98 13*0 4f 86 98
  //   13*0 4f 86 98 13*0 4f 86 98 13*0 4f 86 98 13*0 4f 86 98 13*0 4f 86 98 13*0 4f 86 9 46 47 85 6 49 7
  //   49 98 5*0 4f 86 9 44 43 85 4 49 3 49 98 5*0 4f 86 98 13*0 4f 86 98 13*0 4f 86 98 13*0 4f 86 98 13*0
  //   4f 86 33 7f 3f 7f 98 9*0 4f 86 98 13*0 4f 86 98 13*0 4f 86 98 13*0 4f 86 98 13*0 4f 86 98 13*0 4f 86
  //   98 13*0 4f 86 98 13*0 4f 86 98 13*0 4f 86 98 13*0 4f 86 98 13*0 4f 86 98 13*0 4f 86 98 13*0 4f 86 98
  //   13*0 4f 86 98 13*0 4f 86 98 13*0 4f 86 32 7f 3e 7f 98 9*0 4f 86 98 13*0 4f 86 98 13*0 4f 86 98 13*0
  //   4f 86 98 13*0 4f 86 98 13*0 4f 86 98 13*0 4f 86 98 13*0 4f 86 98 13*0 4f 86 98 13*0 4f 86 98 13*0 4f
  //   86 98 13*0 4f 86 98 13*0 4f 86 98 13*0 4f 86 98 13*0 4f 86 98 13*0 4f 86 98 13*0 4f 86 98 13*0 4f 86
  //   98 13*0 4f 86 98 13*0 4f 86 98 13*0 4f 86 98 13*0 4f 86 98 13*0 4f 86 98 13*0 4f 86 98 13*0 4f 86 98
  //   13*0 4f 86 98 13*0 4f 86 98 13*0 4f 86 98 13*0 4f 86 98 13*0 4f 86 98 13*0 4f 86 98 13*0 4f 86 98
  //   13*0 4f 86 98 13*0 4f 86 98 13*0 4f 86 98 13*0 4f 86 98 13*0 4f 86 98 13*0 4f 86 98 13*0 4f 86 98
  //   13*0 4f 86 98 13*0 4f 86 98 13*0 4f 86 98 13*0 4f 86 98 13*0 4f 86 98 13*0 4f 86 98 13*0 4f 86 98
  //   13*0 4f 86 98 13*0 4f 86 98 13*0 4f 86 98 13*0 4f 86 98 13*0 4f 86 98 13*0 4f 86 98 13*0 4f 86 98
  //   13*0 4f 86 98 13*0 4f 86 98 13*0 4f 86 98 13*0 4f 86 98 13*0 4f 86 98 13*0 4f 86 98 13*0 4f 86 98
  //   13*0 4f 86 98 13*0 4f 86 98 13*0 4f 86 98 13*0 4f 86 98 13*0 4f 86 98 13*0 4f 86 98 13*0 4f 86 32 7f
  //   98 11*0 4f 86 33 7f 98 11*0 4f 86 98 13*0 4f 86 98 13*0 4f 86 98 13*0 4f 86 98 13*0 4f 86 98 13*0 4f
  //   86 98 13*0 4f 86 98 13*0 4f 86 98 13*0 4f 86 98 13*0 4f 86 98 13*0 4f 86 b 46 a 47 98 9*0 4f 86 b 44
  //   a 43 98 9*0 4f 86 9 4f 86 4f b 49 a 49 98 5*0 4f 86 9 4f 86 4f b 4d 85 a 4d 98 4*0 4f 86 9 46 47 b
  //   4d 85 a 4d 98 5*0 4f 86 9 44 43 b 4d 85 a 4d 98 5*0 4f 86 98 13*0 4f 86 98 13*0 4f 86 98 13*0 4f 86
  //   98 13*0 4f 86 98 13*0 4f 86 98 13*0 4f 86 98 13*0 4f 86 98 13*0 4f 86 98 13*0 4f 86 98 13*0 4f 86 98
  //   13*0 4f 86 98 13*0 4f 86 9 4f 86 a0 10*0 4f 86 9 40 a0 11*0 4f 86 9 47 a0 11*0 4f 86 9 46 a0 11*0 4f
  //   86 9 45 a0 11*0 4f 86 9 43 a0 11*0 4f 86 9 44 a0 11*0 4f 86 98 13*0 4f 86 98 13*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
endmodule

module control_v3 (
  input  RESET,
  input  CLOCK,
  input  [7:0] IN,
  output MEMORY_WRITE,
  output nSP_DEC,
  output nMAR_INC,
  output M1,
  output nSP_INC,
  output nPC_INC,
  output nADDR_SEL_MAR,
  output nADDR_SEL_PC,
  output nADDR_SEL_SP,
  output MEMORY_READ,
  output [4:0] RD_ADDR,
  output [4:0] WR_ADDR,
  output WR_ENABLE,
  output [15:0] DEBUG_INS,
  output [15:0] ADDR
);

  wire and_1_out, and_2_out, and_3_out, and_4_out, finish, halt, n7474_1_pin4, n7474_1_pin5, n7474_1_pin6,
       n7474_10_pin2, n7474_10_pin3, n7474_10_pin12, n74125_1_pin2, n74125_1_pin3, n74125_1_pin5,
       n74125_1_pin6, n74125_2_pin2, n74125_2_pin3, n74125_2_pin5, n74125_2_pin6, n74125_3_pin3,
       n74125_3_pin6, n74125_3_pin12, n74125_3_pin13, n74125_4_pin2, n74125_4_pin3, n74125_4_pin6,
       n74125_5_pin2, n74125_5_pin3, n74125_5_pin6, n74125_5_pin11, n74125_5_pin12, n74125_5_pin13,
       n74125_6_pin2, n74125_6_pin3, n74125_6_pin6, n74125_6_pin11, n74125_6_pin12, n74125_6_pin13,
       n74125_7_pin2, n74125_7_pin3, n74125_7_pin6, n74125_7_pin8, n74125_7_pin9, n74125_7_pin10,
       n74125_7_pin11, n74125_7_pin13, n74125_8_pin2, n74125_8_pin3, n74125_8_pin6, n74125_8_pin11,
       n74125_8_pin12, n74125_8_pin13, n74125_9_pin2, n74125_9_pin3, n74125_9_pin6, n74125_9_pin8,
       n74125_9_pin10, n74125_9_pin11, n74125_9_pin13, n74125_10_pin2, n74125_10_pin3, n74125_11_pin2,
       n74125_11_pin3, n74125_11_pin6, n74125_11_pin11, n74125_11_pin12, n74125_11_pin13, n74138_1_pin4,
       n74138_1_pin13, n74138_1_pin14, n74138_2_pin6, n74138_4_pin7, n74138_4_pin9, n74138_4_pin10,
       n74138_4_pin11, n74138_4_pin12, n74138_4_pin13, n74138_4_pin14, n74138_5_pin11, n74138_5_pin13,
       n74138_5_pin14, n74138_6_pin11, n74138_6_pin13, n74138_6_pin14, n74157_1_pin1, n74157_1_pin2,
       n74157_3_pin1, n74157_3_pin2, n74157_5_pin1, n74157_5_pin2, n74193_1_pin1, n74193_1_pin2,
       n74193_1_pin3, n74193_1_pin4, n74193_1_pin6, n74193_2_pin2, n74193_2_pin3, n74193_2_pin4,
       n74193_2_pin5, n74193_2_pin6, n74244_1_pin2, n74244_1_pin4, n74244_1_pin6, n74244_1_pin8,
       n74244_1_pin11, n74244_4_pin17, n74244_5_pin2, n74244_5_pin17, n74244_10_pin4, n74244_10_pin6,
       n74244_10_pin8, n74244_10_pin11, n74244_11_pin4, n74244_11_pin6, n74244_11_pin8, n74244_11_pin11,
       n74244_12_pin2, n74244_12_pin4, n74244_12_pin6, n74244_12_pin8, n74244_12_pin11, n74244_13_pin2,
       n74244_13_pin4, n74244_13_pin6, n74244_13_pin8, n74244_13_pin11, n74244_14_pin2, n74244_14_pin4,
       n74244_14_pin6, n74244_14_pin8, n74244_14_pin11, n_8bit, n_const0, n_const1, n_cycle2, n_cycle3,
       n_cycle4, n_cycle5, n_cycle6, n_cycle7, n_fetch_cycle, n_fetch_low_cycle, n_first_cycle, n_first_mar,
       n_hold_clock, n_mar_read, n_mar_write, n_memd_mar_read, n_p1_read, n_p1_write, n_p2_read, n_p2_write,
       n_p3_read, n_p3_write, n_script_control, n_script_in_out, n_script_transfer8, n_script_transfer8_ind,
       n_script_transfer16, n_script_transfer16_ind, n_script_ula, n_script_ula_ind, n_script_ula_single,
       n_select_8bit_p1, n_select_8bit_p2, n_select_8bit_p3, n_select_addr_constant, n_select_mar_write,
       n_select_memd_pc_read, n_select_p1_read, n_select_p2_read, n_select_p3_write, n_temp_read,
       n_temp_write, nclock, not_3_out, not_4_out, not_5_out, not_6_out, nreset, or_2_out, or_3_out,
       or_4_out, or_5_out, or_6_out, or_9_out, or_10_out, or_11_out, or_12_out, or_15_out, or_16_out,
       or_17_out, or_18_out, or_19_out, or_20_out, or_21_out, or_22_out, or_28_out, or_29_out, or_30_out,
       or_32_out, restart_cycle;
  wire [4:0] ins_p1_shift, ins_p2_shift, ins_p3_shift;

  not not_1 (nreset, RESET);
  not not_2 (nclock, CLOCK);
  Pull_Resistor pull_resistor_1 (.node(finish));
  buf buffer_1 (halt, n7474_1_pin6);
  or or_1 (restart_cycle, finish, RESET);
  _7474 u_7474_1 (
    .pin1(nreset), .pin4(n7474_1_pin4), .pin5(n7474_1_pin5), .pin6(n7474_1_pin6));  // open: pin2, pin3, pin13, pin12, pin11, pin10, pin9, pin8
  and and_1 (and_1_out, CLOCK, ~n_fetch_low_cycle);  // AND_Gate
  and and_2 (and_2_out, CLOCK, ~M1);  // AND_Gate
  or or_2 (or_2_out, n_script_transfer8, n_cycle2);
  or or_3 (or_3_out, n_script_transfer8, n_cycle3);
  buf buffer_2 (n_p1_write, n74125_1_pin3);
  buf buffer_3 (n_p2_read, n74125_1_pin3);
  buf buffer_4 (finish, n74125_1_pin6);
  or or_4 (or_4_out, n_script_transfer16, n_cycle2);
  or or_5 (or_5_out, n_script_transfer16, n_cycle3);
  buf buffer_5 (n_p1_read, n74125_2_pin3);
  buf buffer_6 (n_p2_write, n74125_2_pin3);
  buf buffer_7 (n_8bit, n74125_2_pin3);
  buf buffer_8 (finish, n74125_2_pin6);
  or or_6 (or_6_out, n_script_control, n_cycle2);
  buf buffer_9 (finish, n74125_3_pin3);
  buf buffer_10 (halt, n74125_3_pin6);
  _7474 u_7474_2 (
    .pin2(IN[0]), .pin3(and_1_out), .pin4(nreset), .pin5(DEBUG_INS[0]), .pin12(IN[1]), .pin11(and_1_out),
    .pin10(nreset), .pin9(DEBUG_INS[1]));  // open: pin1, pin6, pin13, pin8
  _7474 u_7474_3 (
    .pin2(IN[0]), .pin3(and_2_out), .pin5(DEBUG_INS[8]), .pin12(IN[1]), .pin11(and_2_out), .pin9(DEBUG_INS[9]));  // open: pin1, pin4, pin6, pin13, pin10, pin8
  _74125 u_74125_1 (
    .pin1(or_2_out), .pin2(n74125_1_pin2), .pin3(n74125_1_pin3), .pin4(or_3_out), .pin5(n74125_1_pin5),
    .pin6(n74125_1_pin6));  // open: pin13, pin12, pin11, pin10, pin9, pin8
  _74125 u_74125_2 (
    .pin1(or_4_out), .pin2(n74125_2_pin2), .pin3(n74125_2_pin3), .pin4(or_5_out), .pin5(n74125_2_pin5),
    .pin6(n74125_2_pin6));  // open: pin13, pin12, pin11, pin10, pin9, pin8
  _74125 u_74125_3 (
    .pin1(or_6_out), .pin2(DEBUG_INS[8]), .pin3(n74125_3_pin3), .pin4(or_6_out), .pin5(DEBUG_INS[9]),
    .pin6(n74125_3_pin6), .pin13(n74125_3_pin13), .pin12(n74125_3_pin12), .pin11(finish));  // open: pin10, pin9, pin8
  _74193 u_74193_1 (
    .pin1(n74193_1_pin1), .pin2(n74193_1_pin2), .pin3(n74193_1_pin3), .pin4(n74193_1_pin4), .pin5(nclock),
    .pin6(n74193_1_pin6), .pin15(n74193_1_pin1), .pin14(n7474_1_pin5), .pin11(nreset), .pin10(n74193_1_pin1),
    .pin9(n74193_1_pin1));  // open: pin7, pin13, pin12
  _74193 u_74193_2 (
    .pin2(n74193_2_pin2), .pin3(n74193_2_pin3), .pin4(n74193_2_pin4), .pin5(n74193_2_pin5),
    .pin6(n74193_2_pin6), .pin14(restart_cycle));  // open: pin1, pin7, pin15, pin13, pin12, pin11, pin10, pin9
  or or_7 (n74125_3_pin13, n_script_control, n_cycle3);
  buf buffer_11 (n_fetch_cycle, and_3_out);
  buf buffer_12 (n_select_memd_pc_read, and_3_out);
  or or_8 (n74193_2_pin5, halt, and_4_out);
  _7474 u_7474_4 (
    .pin1(nreset), .pin2(IN[2]), .pin3(and_1_out), .pin5(DEBUG_INS[2]), .pin12(IN[3]), .pin11(and_1_out),
    .pin10(nreset), .pin9(DEBUG_INS[3]));  // open: pin4, pin6, pin13, pin8
  _7474 u_7474_5 (
    .pin2(IN[2]), .pin3(and_2_out), .pin5(DEBUG_INS[10]), .pin12(IN[3]), .pin11(and_2_out),
    .pin9(DEBUG_INS[11]));  // open: pin1, pin4, pin6, pin13, pin10, pin8
  _74138 u_74138_1 (
    .pin1(n74193_1_pin3), .pin2(n74193_1_pin2), .pin3(n74193_1_pin6), .pin4(n74138_1_pin4),
    .pin5(n74138_1_pin4), .pin6(n7474_1_pin6), .pin14(n74138_1_pin14), .pin13(n74138_1_pin13),
    .pin12(n7474_1_pin4));  // open: pin7, pin15, pin11, pin10, pin9
  and and_3 (and_3_out, n_fetch_low_cycle, M1);
  _74138 u_74138_2 (
    .pin1(n74193_2_pin3), .pin2(n74193_2_pin2), .pin3(n74193_2_pin6), .pin4(halt), .pin5(halt),
    .pin6(n74138_2_pin6), .pin7(n_cycle7), .pin15(M1), .pin14(n_fetch_low_cycle), .pin13(n_cycle2),
    .pin12(n_cycle3), .pin11(n_cycle4), .pin10(n_cycle5), .pin9(n_cycle6));
  and and_4 (and_4_out, nclock, n_hold_clock);
  _74125 u_74125_4 (
    .pin1(n74138_1_pin14), .pin2(n74125_4_pin2), .pin3(n74125_4_pin3), .pin4(n74138_1_pin13),
    .pin5(n74125_4_pin2), .pin6(n74125_4_pin6));  // open: pin13, pin12, pin11, pin10, pin9, pin8
  buf buffer_13 (n_p1_read, n74125_4_pin3);
  buf buffer_14 (n_p2_write, n74125_4_pin3);
  buf buffer_15 (n_const0, n74125_4_pin3);
  buf buffer_16 (n_8bit, n74125_4_pin3);
  buf buffer_17 (n_p1_read, n74125_4_pin6);
  buf buffer_18 (n_p2_write, n74125_4_pin6);
  buf buffer_19 (n_8bit, n74125_4_pin6);
  _7474 u_7474_6 (
    .pin1(nreset), .pin2(IN[4]), .pin3(and_1_out), .pin5(DEBUG_INS[4]), .pin13(nreset), .pin12(IN[5]),
    .pin11(and_1_out), .pin9(DEBUG_INS[5]));  // open: pin4, pin6, pin10, pin8
  _7474 u_7474_7 (
    .pin2(IN[4]), .pin3(and_2_out), .pin5(DEBUG_INS[12]), .pin12(IN[5]), .pin11(and_2_out),
    .pin9(DEBUG_INS[13]));  // open: pin1, pin4, pin6, pin13, pin10, pin8
  _7474 u_7474_8 (
    .pin2(IN[6]), .pin3(and_1_out), .pin4(nreset), .pin5(DEBUG_INS[6]), .pin12(IN[7]), .pin11(and_1_out),
    .pin10(nreset), .pin9(DEBUG_INS[7]));  // open: pin1, pin6, pin13, pin8
  _7474 u_7474_9 (
    .pin2(IN[6]), .pin3(and_2_out), .pin5(DEBUG_INS[14]), .pin12(IN[7]), .pin11(and_2_out),
    .pin9(DEBUG_INS[15]));  // open: pin1, pin4, pin6, pin13, pin10, pin8
  or or_9 (or_9_out, n_script_transfer8_ind, n_cycle2);
  or or_10 (or_10_out, n_script_transfer8_ind, n_cycle3);
  buf buffer_20 (n_p2_read, n74125_5_pin3);
  buf buffer_21 (n_mar_write, n74125_5_pin3);
  buf buffer_22 (n_8bit, n74125_5_pin3);
  buf buffer_23 (n_p3_read, n74125_5_pin6);
  buf buffer_24 (n_p1_write, n74125_5_pin6);
  or or_11 (or_11_out, n_script_transfer16_ind, n_cycle2);
  or or_12 (or_12_out, n_script_transfer16_ind, n_cycle3);
  buf buffer_25 (n_p2_read, n74125_6_pin3);
  buf buffer_26 (n_mar_write, n74125_6_pin3);
  buf buffer_27 (n_8bit, n74125_6_pin3);
  buf buffer_28 (n_p3_read, n74125_6_pin6);
  buf buffer_29 (n_p1_write, n74125_6_pin6);
  buf buffer_30 (n_8bit, n74125_6_pin6);
  _74125 u_74125_5 (
    .pin1(or_9_out), .pin2(n74125_5_pin2), .pin3(n74125_5_pin3), .pin4(or_10_out), .pin5(n74125_5_pin2),
    .pin6(n74125_5_pin6), .pin13(n74125_5_pin13), .pin12(n74125_5_pin12), .pin11(n74125_5_pin11));  // open: pin10, pin9, pin8
  _74125 u_74125_6 (
    .pin1(or_11_out), .pin2(n74125_6_pin2), .pin3(n74125_6_pin3), .pin4(or_12_out), .pin5(n74125_6_pin2),
    .pin6(n74125_6_pin6), .pin13(n74125_6_pin13), .pin12(n74125_6_pin12), .pin11(n74125_6_pin11));  // open: pin10, pin9, pin8
  _7474 u_7474_10 (
    .pin2(n7474_10_pin2), .pin3(n7474_10_pin3), .pin4(nreset), .pin5(n_hold_clock), .pin6(n7474_10_pin2),
    .pin13(nreset), .pin12(n7474_10_pin12), .pin11(nclock), .pin10(n_8bit), .pin9(n_first_cycle),
    .pin8(n7474_10_pin12));  // open: pin1
  not not_3 (not_3_out, DEBUG_INS[15]);
  or or_13 (n74125_5_pin13, n_script_transfer8_ind, n_cycle4);
  or or_14 (n74125_6_pin13, n_script_transfer16_ind, n_cycle4);
  and and_5 (n7474_10_pin3, CLOCK, ~n_8bit);  // AND_Gate
  _74244 u_74244_1 (
    .pin1(n_select_memd_pc_read), .pin2(n74244_1_pin2), .pin4(n74244_1_pin4), .pin6(n74244_1_pin6),
    .pin8(n74244_1_pin8), .pin9(RD_ADDR[4]), .pin19(n_select_memd_pc_read), .pin18(RD_ADDR[0]),
    .pin16(RD_ADDR[1]), .pin14(RD_ADDR[2]), .pin12(RD_ADDR[3]), .pin11(n74244_1_pin11));  // open: pin3, pin5, pin7, pin17, pin15, pin13
  _74138 u_74138_3 (
    .pin1(DEBUG_INS[12]), .pin2(DEBUG_INS[13]), .pin3(DEBUG_INS[14]), .pin4(DEBUG_INS[15]),
    .pin5(DEBUG_INS[15]), .pin6(n_fetch_cycle), .pin7(n_script_ula_single), .pin15(n_script_control),
    .pin14(n_script_transfer8), .pin13(n_script_transfer16), .pin12(n_script_transfer8_ind),
    .pin11(n_script_transfer16_ind), .pin10(n_script_ula), .pin9(n_script_ula_ind));
  _74138 u_74138_4 (
    .pin1(DEBUG_INS[12]), .pin2(DEBUG_INS[13]), .pin3(DEBUG_INS[14]), .pin4(not_3_out), .pin5(not_3_out),
    .pin6(n_fetch_cycle), .pin7(n74138_4_pin7), .pin15(n_script_in_out), .pin14(n74138_4_pin14),
    .pin13(n74138_4_pin13), .pin12(n74138_4_pin12), .pin11(n74138_4_pin11), .pin10(n74138_4_pin10),
    .pin9(n74138_4_pin9));
  buf buffer_31 (finish, n74125_5_pin11);
  buf buffer_32 (finish, n74125_6_pin11);
  Pull_Resistor #(.pull(1)) pull_resistor_2 (.node(n_8bit));
  Pull_Resistor #(.pull(1)) pull_resistor_3 (.node(WR_ENABLE));
  or or_15 (or_15_out, n_script_ula, n_cycle2);
  or or_16 (or_16_out, n_script_ula, n_cycle3);
  buf buffer_33 (n_p1_read, n74125_7_pin3);
  buf buffer_34 (n_temp_write, n74125_7_pin3);
  buf buffer_35 (n_p2_read, n74125_7_pin6);
  buf buffer_36 (n_p3_write, n74125_7_pin6);
  buf buffer_37 (WR_ENABLE, n74125_7_pin6);
  buf buffer_38 (finish, n74125_10_pin3);
  not not_4 (not_4_out, DEBUG_INS[3]);
  Pull_Resistor #(.pull(1)) pull_resistor_4 (.node(n_const0));
  Pull_Resistor #(.pull(1)) pull_resistor_5 (.node(n_const1));
  _74125 u_74125_7 (
    .pin1(or_15_out), .pin2(n74125_7_pin2), .pin3(n74125_7_pin3), .pin4(or_16_out), .pin5(n74125_7_pin2),
    .pin6(n74125_7_pin6), .pin13(n74125_7_pin13), .pin12(n74125_7_pin2), .pin11(n74125_7_pin11),
    .pin10(n74125_7_pin10), .pin9(n74125_7_pin9), .pin8(n74125_7_pin8));
  or or_17 (or_17_out, n_script_ula_single, n_cycle2);
  or or_18 (or_18_out, n_script_ula_single, n_cycle3);
  buf buffer_39 (n_p3_write, n74125_8_pin3);
  buf buffer_40 (n_p2_read, n74125_8_pin3);
  buf buffer_41 (WR_ENABLE, n74125_8_pin3);
  buf buffer_42 (n_p1_write, n74125_8_pin6);
  buf buffer_43 (n_temp_read, n74125_8_pin6);
  or or_19 (or_19_out, n_script_ula_ind, n_cycle2);
  or or_20 (or_20_out, n_script_ula_ind, n_cycle3);
  buf buffer_44 (n_temp_write, n74125_9_pin3);
  buf buffer_45 (n_p1_read, n74125_9_pin3);
  buf buffer_46 (n_mar_write, n74125_9_pin6);
  buf buffer_47 (n_p2_read, n74125_9_pin6);
  buf buffer_48 (n_8bit, n74125_9_pin6);
  or or_21 (or_21_out, n_script_ula_ind, n_cycle6);
  _74157 u_74157_1 (
    .pin1(n74157_1_pin1), .pin2(n74157_1_pin2), .pin3(DEBUG_INS[3]), .pin4(ins_p1_shift[4]),
    .pin15(n74157_1_pin2));  // open: pin5, pin6, pin7, pin14, pin13, pin12, pin11, pin10, pin9
  _74157 u_74157_2 (
    .pin1(n74157_1_pin1), .pin2(DEBUG_INS[0]), .pin3(n_first_cycle), .pin4(ins_p1_shift[0]),
    .pin5(DEBUG_INS[1]), .pin6(DEBUG_INS[0]), .pin7(ins_p1_shift[1]), .pin15(n74157_1_pin2),
    .pin14(DEBUG_INS[3]), .pin13(DEBUG_INS[2]), .pin12(ins_p1_shift[3]), .pin11(DEBUG_INS[2]),
    .pin10(DEBUG_INS[1]), .pin9(ins_p1_shift[2]));
  or or_22 (or_22_out, DEBUG_INS[2], not_4_out);
  Pull_Resistor #(.pull(1)) pull_resistor_6 (.node(n_p1_read));
  Pull_Resistor #(.pull(1)) pull_resistor_7 (.node(n_p1_write));
  Pull_Resistor #(.pull(1)) pull_resistor_8 (.node(n_select_addr_constant));
  or or_23 (n74125_7_pin13, n_script_ula, n_cycle4);
  or or_24 (n74125_7_pin10, n_script_ula, n_cycle5);
  _74125 u_74125_8 (
    .pin1(or_17_out), .pin2(n74125_8_pin2), .pin3(n74125_8_pin3), .pin4(or_18_out), .pin5(n74125_8_pin2),
    .pin6(n74125_8_pin6), .pin13(n74125_8_pin13), .pin12(n74125_8_pin12), .pin11(n74125_8_pin11));  // open: pin10, pin9, pin8
  _74125 u_74125_9 (
    .pin1(or_19_out), .pin2(n74125_9_pin2), .pin3(n74125_9_pin3), .pin4(or_20_out), .pin5(n74125_9_pin2),
    .pin6(n74125_9_pin6), .pin13(n74125_9_pin13), .pin12(n74125_9_pin2), .pin11(n74125_9_pin11),
    .pin10(n74125_9_pin10), .pin9(n74125_9_pin2), .pin8(n74125_9_pin8));
  _74125 u_74125_10 (
    .pin1(or_21_out), .pin2(n74125_10_pin2), .pin3(n74125_10_pin3));  // open: pin4, pin5, pin6, pin13, pin12, pin11, pin10, pin9, pin8
  and and_6 (n74157_1_pin1, or_22_out, n_8bit);
  _74244 u_74244_2 (
    .pin1(n_p1_read), .pin2(ins_p1_shift[0]), .pin4(ins_p1_shift[1]), .pin6(ins_p1_shift[2]),
    .pin8(ins_p1_shift[3]), .pin9(RD_ADDR[4]), .pin19(n_p1_read), .pin18(RD_ADDR[0]), .pin16(RD_ADDR[1]),
    .pin14(RD_ADDR[2]), .pin12(RD_ADDR[3]), .pin11(ins_p1_shift[4]));  // open: pin3, pin5, pin7, pin17, pin15, pin13
  _74244 u_74244_3 (
    .pin1(n_p1_write), .pin2(ins_p1_shift[0]), .pin4(ins_p1_shift[1]), .pin6(ins_p1_shift[2]),
    .pin8(ins_p1_shift[3]), .pin9(WR_ADDR[4]), .pin19(n_p1_write), .pin18(WR_ADDR[0]), .pin16(WR_ADDR[1]),
    .pin14(WR_ADDR[2]), .pin12(WR_ADDR[3]), .pin11(ins_p1_shift[4]));  // open: pin3, pin5, pin7, pin17, pin15, pin13
  _74244 u_74244_4 (
    .pin1(n_select_addr_constant), .pin2(n_const0), .pin3(ADDR[7]), .pin4(n_const1), .pin5(ADDR[6]),
    .pin6(n_const1), .pin7(ADDR[5]), .pin8(n_const1), .pin9(ADDR[4]), .pin19(n_select_addr_constant),
    .pin18(ADDR[0]), .pin17(n74244_4_pin17), .pin16(ADDR[1]), .pin15(n74244_4_pin17), .pin14(ADDR[2]),
    .pin13(n74244_4_pin17), .pin12(ADDR[3]), .pin11(n74244_4_pin17));
  _74244 u_74244_5 (
    .pin1(n_select_addr_constant), .pin2(n74244_5_pin2), .pin3(ADDR[15]), .pin4(n74244_5_pin2),
    .pin5(ADDR[14]), .pin6(n74244_5_pin2), .pin7(ADDR[13]), .pin8(n74244_5_pin2), .pin9(ADDR[12]),
    .pin19(n_select_addr_constant), .pin18(ADDR[8]), .pin17(n74244_5_pin17), .pin16(ADDR[9]),
    .pin15(n74244_5_pin17), .pin14(ADDR[10]), .pin13(n74244_5_pin17), .pin12(ADDR[11]), .pin11(n74244_5_pin17));
  buf buffer_49 (n_temp_read, n74125_7_pin11);
  buf buffer_50 (n_p1_write, n74125_7_pin11);
  buf buffer_51 (finish, n74125_7_pin8);
  or or_25 (n74125_8_pin13, n_script_ula_single, n_cycle4);
  buf buffer_52 (finish, n74125_8_pin11);
  or or_26 (n74125_9_pin13, n_script_ula_ind, n_cycle4);
  or or_27 (n74125_9_pin10, n_script_ula_ind, n_cycle5);
  buf buffer_53 (n_memd_mar_read, n74125_9_pin11);
  buf buffer_54 (n_p3_write, n74125_9_pin11);
  buf buffer_55 (WR_ENABLE, n74125_9_pin11);
  buf buffer_56 (n_temp_read, n74125_9_pin8);
  buf buffer_57 (n_p1_write, n74125_9_pin8);
  _74157 u_74157_3 (
    .pin1(n74157_3_pin1), .pin2(n74157_3_pin2), .pin3(DEBUG_INS[7]), .pin4(ins_p2_shift[4]),
    .pin15(n74157_3_pin2));  // open: pin5, pin6, pin7, pin14, pin13, pin12, pin11, pin10, pin9
  _74157 u_74157_4 (
    .pin1(n74157_3_pin1), .pin2(DEBUG_INS[4]), .pin3(n_first_cycle), .pin4(ins_p2_shift[0]),
    .pin5(DEBUG_INS[5]), .pin6(DEBUG_INS[4]), .pin7(ins_p2_shift[1]), .pin15(n74157_3_pin2),
    .pin14(DEBUG_INS[7]), .pin13(DEBUG_INS[6]), .pin12(ins_p2_shift[3]), .pin11(DEBUG_INS[6]),
    .pin10(DEBUG_INS[5]), .pin9(ins_p2_shift[2]));
  or or_28 (or_28_out, DEBUG_INS[6], not_5_out);
  not not_5 (not_5_out, DEBUG_INS[7]);
  and and_7 (n74157_3_pin1, or_28_out, n_8bit);
  Pull_Resistor #(.pull(1)) pull_resistor_9 (.node(n_p2_read));
  Pull_Resistor #(.pull(1)) pull_resistor_10 (.node(n_p2_write));
  _74244 u_74244_6 (
    .pin1(n_p2_read), .pin2(ins_p2_shift[0]), .pin4(ins_p2_shift[1]), .pin6(ins_p2_shift[2]),
    .pin8(ins_p2_shift[3]), .pin9(RD_ADDR[4]), .pin19(n_p2_read), .pin18(RD_ADDR[0]), .pin16(RD_ADDR[1]),
    .pin14(RD_ADDR[2]), .pin12(RD_ADDR[3]), .pin11(ins_p2_shift[4]));  // open: pin3, pin5, pin7, pin17, pin15, pin13
  _74244 u_74244_7 (
    .pin1(n_p2_write), .pin2(ins_p2_shift[0]), .pin4(ins_p2_shift[1]), .pin6(ins_p2_shift[2]),
    .pin8(ins_p2_shift[3]), .pin9(WR_ADDR[4]), .pin19(n_p2_write), .pin18(WR_ADDR[0]), .pin16(WR_ADDR[1]),
    .pin14(WR_ADDR[2]), .pin12(WR_ADDR[3]), .pin11(ins_p2_shift[4]));  // open: pin3, pin5, pin7, pin17, pin15, pin13
  or or_29 (or_29_out, n_script_in_out, n_cycle2);
  or or_30 (or_30_out, n_script_in_out, n_cycle3);
  buf buffer_58 (n_select_p1_read, n74125_11_pin3);
  buf buffer_59 (n_select_mar_write, n74125_11_pin3);
  buf buffer_60 (n_select_8bit_p1, n74125_11_pin3);
  buf buffer_61 (n_first_mar, n74125_11_pin3);
  buf buffer_62 (n_select_p2_read, n74125_11_pin6);
  buf buffer_63 (n_select_p3_write, n74125_11_pin6);
  buf buffer_64 (n_select_8bit_p2, n74125_11_pin6);
  buf buffer_65 (n_select_8bit_p3, n74125_11_pin6);
  not not_6 (not_6_out, DEBUG_INS[11]);
  _74125 u_74125_11 (
    .pin1(or_29_out), .pin2(n74125_11_pin2), .pin3(n74125_11_pin3), .pin4(or_30_out), .pin5(n74125_11_pin2),
    .pin6(n74125_11_pin6), .pin13(n74125_11_pin13), .pin12(n74125_11_pin12), .pin11(n74125_11_pin11));  // open: pin10, pin9, pin8
  or or_31 (n74125_11_pin13, n_script_in_out, n_cycle4);
  _74157 u_74157_5 (
    .pin1(n74157_5_pin1), .pin2(n74157_5_pin2), .pin3(DEBUG_INS[11]), .pin4(ins_p3_shift[4]),
    .pin15(n74157_5_pin2));  // open: pin5, pin6, pin7, pin14, pin13, pin12, pin11, pin10, pin9
  _74157 u_74157_6 (
    .pin1(n74157_5_pin1), .pin2(DEBUG_INS[8]), .pin3(n_first_cycle), .pin4(ins_p3_shift[0]),
    .pin5(DEBUG_INS[9]), .pin6(DEBUG_INS[8]), .pin7(ins_p3_shift[1]), .pin15(n74157_5_pin2),
    .pin14(DEBUG_INS[11]), .pin13(DEBUG_INS[10]), .pin12(ins_p3_shift[3]), .pin11(DEBUG_INS[10]),
    .pin10(DEBUG_INS[9]), .pin9(ins_p3_shift[2]));
  or or_32 (or_32_out, DEBUG_INS[10], not_6_out);
  buf buffer_66 (finish, n74125_11_pin11);
  and and_8 (n74157_5_pin1, or_32_out, n_8bit);
  Pull_Resistor #(.pull(1)) pull_resistor_11 (.node(n_p3_read));
  Pull_Resistor #(.pull(1)) pull_resistor_12 (.node(n_p3_write));
  _74244 u_74244_8 (
    .pin1(n_p3_read), .pin2(ins_p3_shift[0]), .pin4(ins_p3_shift[1]), .pin6(ins_p3_shift[2]),
    .pin8(ins_p3_shift[3]), .pin9(RD_ADDR[4]), .pin19(n_p3_read), .pin18(RD_ADDR[0]), .pin16(RD_ADDR[1]),
    .pin14(RD_ADDR[2]), .pin12(RD_ADDR[3]), .pin11(ins_p3_shift[4]));  // open: pin3, pin5, pin7, pin17, pin15, pin13
  _74244 u_74244_9 (
    .pin1(n_p3_write), .pin2(ins_p3_shift[0]), .pin4(ins_p3_shift[1]), .pin6(ins_p3_shift[2]),
    .pin8(ins_p3_shift[3]), .pin9(WR_ADDR[4]), .pin19(n_p3_write), .pin18(WR_ADDR[0]), .pin16(WR_ADDR[1]),
    .pin14(WR_ADDR[2]), .pin12(WR_ADDR[3]), .pin11(ins_p3_shift[4]));  // open: pin3, pin5, pin7, pin17, pin15, pin13
  _74138 u_74138_5 (
    .pin1(WR_ADDR[0]), .pin2(WR_ADDR[1]), .pin3(WR_ADDR[2]), .pin4(WR_ADDR[4]), .pin5(WR_ADDR[4]),
    .pin6(WR_ADDR[3]), .pin14(n74138_5_pin14), .pin13(n74138_5_pin13), .pin11(n74138_5_pin11));  // open: pin7, pin15, pin12, pin10, pin9
  _74138 u_74138_6 (
    .pin1(RD_ADDR[0]), .pin2(RD_ADDR[1]), .pin3(RD_ADDR[2]), .pin4(RD_ADDR[4]), .pin5(RD_ADDR[4]),
    .pin6(RD_ADDR[3]), .pin15(nADDR_SEL_PC), .pin14(n74138_6_pin14), .pin13(n74138_6_pin13),
    .pin12(n_select_addr_constant), .pin11(n74138_6_pin11));  // open: pin7, pin10, pin9
  and and_9 (nADDR_SEL_MAR, n74138_5_pin14, n74138_6_pin14, n74138_5_pin11, n74138_6_pin11);
  nand nand_1 (MEMORY_WRITE, n74138_5_pin13, n74138_5_pin14);
  _7432 u_7432_1 (
    .pin1(nclock), .pin2(n74138_6_pin13), .pin3(nSP_INC), .pin4(nclock), .pin5(nADDR_SEL_PC), .pin6(nPC_INC),
    .pin13(nclock), .pin12(n74138_5_pin13), .pin11(nSP_DEC), .pin10(nclock), .pin9(nADDR_SEL_MAR),
    .pin8(nMAR_INC));
  nand nand_2 (MEMORY_READ, nADDR_SEL_PC, n74138_6_pin14, n74138_6_pin13, n_select_addr_constant);
  and and_10 (nADDR_SEL_SP, n74138_5_pin13, n74138_6_pin13);
  _74244 u_74244_10 (
    .pin1(n_mar_read), .pin2(n_first_cycle), .pin4(n74244_10_pin4), .pin6(n74244_10_pin6),
    .pin8(n74244_10_pin8), .pin9(RD_ADDR[4]), .pin19(n_mar_read), .pin18(RD_ADDR[0]), .pin16(RD_ADDR[1]),
    .pin14(RD_ADDR[2]), .pin12(RD_ADDR[3]), .pin11(n74244_10_pin11));  // open: pin3, pin5, pin7, pin17, pin15, pin13
  _74244 u_74244_11 (
    .pin1(n_mar_write), .pin2(n_first_cycle), .pin4(n74244_11_pin4), .pin6(n74244_11_pin6),
    .pin8(n74244_11_pin8), .pin9(WR_ADDR[4]), .pin19(n_mar_write), .pin18(WR_ADDR[0]), .pin16(WR_ADDR[1]),
    .pin14(WR_ADDR[2]), .pin12(WR_ADDR[3]), .pin11(n74244_11_pin11));  // open: pin3, pin5, pin7, pin17, pin15, pin13
  Pull_Resistor #(.pull(1)) pull_resistor_13 (.node(n_mar_read));
  Pull_Resistor #(.pull(1)) pull_resistor_14 (.node(n_mar_write));
  Pull_Resistor #(.pull(1)) pull_resistor_15 (.node(n_temp_read));
  _74244 u_74244_12 (
    .pin1(n_temp_read), .pin2(n74244_12_pin2), .pin4(n74244_12_pin4), .pin6(n74244_12_pin6),
    .pin8(n74244_12_pin8), .pin9(RD_ADDR[4]), .pin19(n_temp_read), .pin18(RD_ADDR[0]), .pin16(RD_ADDR[1]),
    .pin14(RD_ADDR[2]), .pin12(RD_ADDR[3]), .pin11(n74244_12_pin11));  // open: pin3, pin5, pin7, pin17, pin15, pin13
  Pull_Resistor #(.pull(1)) pull_resistor_16 (.node(n_temp_write));
  _74244 u_74244_13 (
    .pin1(n_temp_write), .pin2(n74244_13_pin2), .pin4(n74244_13_pin4), .pin6(n74244_13_pin6),
    .pin8(n74244_13_pin8), .pin9(WR_ADDR[4]), .pin19(n_temp_write), .pin18(WR_ADDR[0]), .pin16(WR_ADDR[1]),
    .pin14(WR_ADDR[2]), .pin12(WR_ADDR[3]), .pin11(n74244_13_pin11));  // open: pin3, pin5, pin7, pin17, pin15, pin13
  _74244 u_74244_14 (
    .pin1(n_memd_mar_read), .pin2(n74244_14_pin2), .pin4(n74244_14_pin4), .pin6(n74244_14_pin6),
    .pin8(n74244_14_pin8), .pin9(RD_ADDR[4]), .pin19(n_memd_mar_read), .pin18(RD_ADDR[0]),
    .pin16(RD_ADDR[1]), .pin14(RD_ADDR[2]), .pin12(RD_ADDR[3]), .pin11(n74244_14_pin11));  // open: pin3, pin5, pin7, pin17, pin15, pin13
  Pull_Resistor #(.pull(1)) pull_resistor_17 (.node(n_memd_mar_read));
  // also tied to GND on the sheet: {n74125_1_pin2, n74125_2_pin2, n74193_1_pin1, n74138_1_pin4, n74125_4_pin2, n74125_5_pin2, n74125_6_pin2, n74244_1_pin2, n74244_1_pin4, n74244_1_pin6, n74244_1_pin11, n74125_7_pin2, n74125_8_pin2, n74125_9_pin2, n74157_1_pin2, n74157_3_pin2, n74125_11_pin2, n74157_5_pin2, n74244_10_pin4, n74244_11_pin4, n74244_12_pin11, n74244_13_pin11, n74244_14_pin4, n74244_14_pin6, n74244_14_pin11}
  // also tied to VCC on the sheet: {n74193_1_pin4, n74125_2_pin5, n74125_1_pin5, n74125_3_pin12, n74193_2_pin4, n74138_2_pin6, n74125_5_pin12, n74125_6_pin12, n74244_1_pin8, n74125_10_pin2, n74125_7_pin9, n74125_8_pin12, n74244_5_pin2, n74244_4_pin17, n74244_5_pin17, n74125_11_pin12, n74244_10_pin6, n74244_10_pin8, n74244_11_pin6, n74244_11_pin8, n74244_10_pin11, n74244_11_pin11, n74244_12_pin2, n74244_12_pin4, n74244_12_pin6, n74244_12_pin8, n74244_13_pin2, n74244_13_pin4, n74244_13_pin6, n74244_13_pin8, n74244_14_pin2, n74244_14_pin8}

  // Other names for the same wires on the sheet: addr_0 = ADDR[0]; addr_1 = ADDR[1]; addr_2 = ADDR[2];
  //   addr_3 = ADDR[3]; addr_4 = ADDR[4]; addr_5 = ADDR[5]; addr_6 = ADDR[6]; addr_7 = ADDR[7]; addr_8 = ADDR[8];
  //   addr_9 = ADDR[9]; addr_10 = ADDR[10]; addr_11 = ADDR[11]; addr_12 = ADDR[12]; addr_13 = ADDR[13];
  //   addr_14 = ADDR[14]; addr_15 = ADDR[15]; data_in_0 = IN[0]; data_in_1 = IN[1]; data_in_2 = IN[2];
  //   data_in_3 = IN[3]; data_in_4 = IN[4]; data_in_5 = IN[5]; data_in_6 = IN[6]; data_in_7 = IN[7];
  //   ins[15:0] = DEBUG_INS; ins_0 = DEBUG_INS[0]; ins_p1[3:0] = DEBUG_INS[3:0]; ins_1 = DEBUG_INS[1];
  //   ins_2 = DEBUG_INS[2]; ins_3 = DEBUG_INS[3]; ins_4 = DEBUG_INS[4]; ins_p2[3:0] = DEBUG_INS[7:4];
  //   ins_5 = DEBUG_INS[5]; ins_6 = DEBUG_INS[6]; ins_7 = DEBUG_INS[7]; ins_8 = DEBUG_INS[8];
  //   ins_p3[3:0] = DEBUG_INS[11:8]; ins_9 = DEBUG_INS[9]; ins_10 = DEBUG_INS[10]; ins_11 = DEBUG_INS[11];
  //   ins_12 = DEBUG_INS[12]; ins_name[3:0] = DEBUG_INS[15:12]; ins_13 = DEBUG_INS[13]; ins_14 = DEBUG_INS[14];
  //   ins_15 = DEBUG_INS[15]; ins_read_reg[4:0] = RD_ADDR; ins_write_reg[4:0] = WR_ADDR; n_double_cycle = n_8bit;
  //   n_fetch_high_cycle = M1; n_ula_enable = WR_ENABLE
endmodule

module control_v4 (
  input  RESET,
  input  CLOCK,
  input  [7:0] IN,
  input  FLAG_Z,
  input  FLAG_C,
  input  FLAG_O,
  input  FLAG_N,
  input  INT_REQUESTED,
  input  FLAG_I,
  output M1,
  output PC_LR_SWAP,
  output [4:0] RD_ADDR,
  output [7:0] DEBUG_INS,
  output [15:0] ADDR
);

  wire and_1_out, and_5_out, and_6_out, and_7_out, and_8_out, and_9_out, and_10_out, finish, halt,
       int_pending, n7474_1_pin1, n7474_1_pin2, n7474_1_pin3, n7474_3_pin1, n7474_7_pin5, n7474_7_pin9,
       n74138_1_pin6, n74138_2_pin4, n74138_2_pin12, n74138_2_pin13, n74138_2_pin14, n74138_2_pin15,
       n74193_1_pin2, n74193_1_pin3, n74193_1_pin4, n74193_1_pin5, n74193_1_pin6, n74244_1_pin1,
       n74244_2_pin1, n74377_1_pin2, n74377_1_pin5, n74377_1_pin6, n74377_1_pin9, n74377_1_pin12,
       n74377_1_pin15, n74377_1_pin16, n74377_1_pin18, n74377_1_pin19, n74377_2_pin2, n74377_2_pin5,
       n74377_2_pin6, n74377_2_pin9, n74377_2_pin12, n74377_2_pin15, n74377_2_pin16, n74377_2_pin19,
       n_finish_cycle, n_high_cycle, n_ins_cond, n_ins_control, n_ins_control1, n_ins_control2, n_ins_read,
       n_ins_swap, n_ins_ula, n_ins_write, n_ins_write_b, n_ins_write_w, n_low_cycle, n_pc_lr_swap,
       n_run_isr, nclear_interrupt, nclock, not_3_out, not_4_out, not_5_out, not_6_out, not_7_out, nreset,
       or_3_out, or_4_out, or_8_out, or_10_out, restart_cycle, run_isr, xnor_1_out, xnor_2_out, xnor_3_out,
       xnor_4_out;

  Pull_Resistor pull_resistor_1 (.node(finish));
  not not_1 (nreset, RESET);
  not not_2 (nclock, CLOCK);
  or or_1 (restart_cycle, finish, RESET);
  not not_3 (not_3_out, n_ins_control);
  not not_4 (not_4_out, n_ins_swap);
  _7474 u_7474_1 (
    .pin1(n7474_1_pin1), .pin2(n7474_1_pin2), .pin3(n7474_1_pin3), .pin4(n7474_1_pin2), .pin5(int_pending));  // open: pin6, pin13, pin12, pin11, pin10, pin9, pin8
  and and_1 (and_1_out, CLOCK, ~M1);  // AND_Gate
  and and_2 (halt, not_3_out, IN[0]);
  _7474 u_7474_2 (
    .pin2(IN[0]), .pin3(and_1_out), .pin4(nreset), .pin5(DEBUG_INS[0]), .pin12(IN[1]), .pin11(and_1_out),
    .pin10(nreset), .pin9(DEBUG_INS[1]));  // open: pin1, pin6, pin13, pin8
  _7474 u_7474_3 (
    .pin1(n7474_3_pin1), .pin2(n_pc_lr_swap), .pin3(not_4_out), .pin4(n7474_3_pin1), .pin5(PC_LR_SWAP),
    .pin6(n_pc_lr_swap));  // open: pin13, pin12, pin11, pin10, pin9, pin8
  and and_3 (n7474_1_pin3, INT_REQUESTED, FLAG_I);
  _74193 u_74193_1 (
    .pin2(n74193_1_pin2), .pin3(n74193_1_pin3), .pin4(n74193_1_pin4), .pin5(n74193_1_pin5),
    .pin6(n74193_1_pin6), .pin14(restart_cycle));  // open: pin1, pin7, pin15, pin13, pin12, pin11, pin10, pin9
  and and_4 (n7474_1_pin1, nreset, nclear_interrupt);
  or or_2 (n74193_1_pin5, halt, nclock);
  _7474 u_7474_4 (
    .pin1(nreset), .pin2(IN[2]), .pin3(and_1_out), .pin5(DEBUG_INS[2]), .pin12(IN[3]), .pin11(and_1_out),
    .pin10(nreset), .pin9(DEBUG_INS[3]));  // open: pin4, pin6, pin13, pin8
  _74138 u_74138_1 (
    .pin1(n74193_1_pin3), .pin2(n74193_1_pin2), .pin3(n74193_1_pin6), .pin4(halt), .pin5(halt),
    .pin6(n74138_1_pin6), .pin15(M1), .pin14(n_low_cycle), .pin13(n_high_cycle), .pin12(n_finish_cycle));  // open: pin7, pin11, pin10, pin9
  or or_3 (or_3_out, run_isr, n_ins_read);
  or or_4 (or_4_out, n_run_isr, n_ins_read);
  _7474 u_7474_5 (
    .pin1(nreset), .pin2(IN[4]), .pin3(and_1_out), .pin5(DEBUG_INS[4]), .pin13(nreset), .pin12(IN[5]),
    .pin11(and_1_out), .pin9(DEBUG_INS[5]));  // open: pin4, pin6, pin10, pin8
  _74377 u_74377_1 (
    .pin1(or_3_out), .pin2(n74377_1_pin2), .pin3(IN[0]), .pin4(IN[1]), .pin5(n74377_1_pin5),
    .pin6(n74377_1_pin6), .pin7(IN[2]), .pin8(IN[3]), .pin9(n74377_1_pin9), .pin19(n74377_1_pin19),
    .pin18(n74377_1_pin18), .pin17(n74377_1_pin18), .pin16(n74377_1_pin16), .pin15(n74377_1_pin15),
    .pin14(n74377_1_pin18), .pin13(IN[4]), .pin12(n74377_1_pin12), .pin11(CLOCK));
  _74377 u_74377_2 (
    .pin1(or_4_out), .pin2(n74377_2_pin2), .pin3(IN[0]), .pin4(IN[1]), .pin5(n74377_2_pin5),
    .pin6(n74377_2_pin6), .pin7(IN[2]), .pin8(IN[3]), .pin9(n74377_2_pin9), .pin19(n74377_2_pin19),
    .pin18(n74377_1_pin18), .pin17(n74377_1_pin18), .pin16(n74377_2_pin16), .pin15(n74377_2_pin15),
    .pin14(n74377_1_pin18), .pin13(IN[4]), .pin12(n74377_2_pin12), .pin11(CLOCK));
  _7474 u_7474_6 (
    .pin2(IN[6]), .pin3(and_1_out), .pin4(nreset), .pin5(DEBUG_INS[6]), .pin12(IN[7]), .pin11(and_1_out),
    .pin10(nreset), .pin9(DEBUG_INS[7]));  // open: pin1, pin6, pin13, pin8
  _74244 u_74244_1 (
    .pin1(n74244_1_pin1), .pin2(n74377_1_pin2), .pin4(n74377_1_pin5), .pin6(n74377_1_pin6),
    .pin8(n74377_1_pin9), .pin9(RD_ADDR[4]), .pin19(n74244_1_pin1), .pin18(RD_ADDR[0]),
    .pin17(n74377_1_pin19), .pin16(RD_ADDR[1]), .pin15(n74377_1_pin16), .pin14(RD_ADDR[2]),
    .pin13(n74377_1_pin15), .pin12(RD_ADDR[3]), .pin11(n74377_1_pin12));  // open: pin3, pin5, pin7
  _74244 u_74244_2 (
    .pin1(n74244_2_pin1), .pin2(n74377_2_pin2), .pin4(n74377_2_pin5), .pin6(n74377_2_pin6),
    .pin8(n74377_2_pin9), .pin9(RD_ADDR[4]), .pin19(n74244_2_pin1), .pin18(RD_ADDR[0]),
    .pin17(n74377_2_pin19), .pin16(RD_ADDR[1]), .pin15(n74377_2_pin15), .pin14(RD_ADDR[2]),
    .pin13(n74377_2_pin16), .pin12(RD_ADDR[3]), .pin11(n74377_2_pin12));  // open: pin3, pin5, pin7
  or or_5 (n74244_1_pin1, run_isr, n_ins_write);
  _74138 u_74138_2 (
    .pin1(DEBUG_INS[5]), .pin2(DEBUG_INS[6]), .pin3(DEBUG_INS[7]), .pin4(n74138_2_pin4),
    .pin5(n74138_2_pin4), .pin6(M1), .pin7(n_ins_ula), .pin15(n74138_2_pin15), .pin14(n74138_2_pin14),
    .pin13(n74138_2_pin13), .pin12(n74138_2_pin12), .pin11(n_ins_control2), .pin10(n_ins_write_b),
    .pin9(n_ins_write_w));
  _74138 u_74138_3 (
    .pin1(IN[5]), .pin2(IN[6]), .pin3(IN[7]), .pin4(M1), .pin5(M1), .pin6(CLOCK), .pin15(n_ins_control1),
    .pin14(n_ins_read), .pin12(n_ins_cond));  // open: pin7, pin13, pin11, pin10, pin9
  or or_6 (n_ins_write, n_ins_write_b, n_ins_write_w);
  or or_7 (n74244_2_pin1, n_run_isr, n_ins_write);
  and and_5 (and_5_out, n_ins_ula, n_ins_write_b);
  and and_6 (and_6_out, n74138_2_pin15, n74138_2_pin14, n74138_2_pin13, n74138_2_pin12);
  or or_8 (or_8_out, n_high_cycle, and_5_out);
  not not_5 (not_5_out, n_finish_cycle);
  not not_6 (not_6_out, or_8_out);
  not not_7 (not_7_out, and_6_out);
  or or_9 (finish, not_5_out, not_6_out, not_7_out);
  or or_10 (or_10_out, and_7_out, and_8_out, and_9_out, and_10_out);
  _7474 u_7474_7 (
    .pin2(or_10_out), .pin5(n7474_7_pin5), .pin12(or_10_out), .pin9(n7474_7_pin9));  // open: pin1, pin3, pin4, pin6, pin13, pin11, pin10, pin8
  and and_7 (and_7_out, IN[0], xnor_1_out);
  and and_8 (and_8_out, IN[1], xnor_2_out);
  and and_9 (and_9_out, IN[2], xnor_3_out);
  and and_10 (and_10_out, IN[3], xnor_4_out);
  xnor xnor_1 (xnor_1_out, IN[4], FLAG_Z);
  xnor xnor_2 (xnor_2_out, IN[4], FLAG_C);
  xnor xnor_3 (xnor_3_out, IN[4], FLAG_O);
  xnor xnor_4 (xnor_4_out, IN[4], FLAG_N);
  // also tied to GND on the sheet: {n74377_1_pin18, n74138_2_pin4}
  // also tied to VCC on the sheet: {n7474_3_pin1, n7474_1_pin2, n74193_1_pin4, n74138_1_pin6}

  // Other names for the same wires on the sheet: addr_0 = ADDR[0]; addr_1 = ADDR[1]; addr_2 = ADDR[2];
  //   addr_3 = ADDR[3]; addr_4 = ADDR[4]; addr_5 = ADDR[5]; addr_6 = ADDR[6]; addr_7 = ADDR[7]; addr_8 = ADDR[8];
  //   addr_9 = ADDR[9]; addr_10 = ADDR[10]; addr_11 = ADDR[11]; addr_12 = ADDR[12]; addr_13 = ADDR[13];
  //   addr_14 = ADDR[14]; addr_15 = ADDR[15]; data_in_5 = IN[5]; data_in_name[2:0] = IN[7:5]; data_in_6 = IN[6];
  //   data_in_7 = IN[7]; data_in_0 = IN[0]; data_in_1 = IN[1]; data_in_2 = IN[2]; data_in_3 = IN[3];
  //   data_in_4 = IN[4]; ins[7:0] = DEBUG_INS; ins_0 = DEBUG_INS[0]; ins_p[4:0] = DEBUG_INS[4:0];
  //   ins_1 = DEBUG_INS[1]; ins_2 = DEBUG_INS[2]; ins_3 = DEBUG_INS[3]; ins_4 = DEBUG_INS[4]; ins_5 = DEBUG_INS[5];
  //   ins_name[2:0] = DEBUG_INS[7:5]; ins_6 = DEBUG_INS[6]; ins_7 = DEBUG_INS[7]; ins_read_reg[4:0] = RD_ADDR;
  //   n_fetch_cycle = M1
endmodule

module pc_lr_reg (
  input  [4:0] RD_ADDR,
  input  [7:0] DATA_IN,
  input  CLOCK,
  input  WR_ENABLE,
  input  [4:0] WR_ADDR,
  input  PC_LR_SWAP,
  input  nINC,
  input  n_ADDR_SEL,
  output [7:0] DATA_OUT,
  output [15:0] ADDR
);

  wire a_count_0, a_count_1, a_count_2, a_count_3, a_count_4, a_count_5, a_count_6, a_count_7, a_count_8,
       a_count_9, a_count_10, a_count_11, a_count_12, a_count_13, a_count_14, a_count_15, A_LOAD_HIGH,
       A_LOAD_LOW, A_READ_HIGH, A_READ_LOW, b_count_0, b_count_1, b_count_2, b_count_3, b_count_4, b_count_5,
       b_count_6, b_count_7, b_count_8, b_count_9, b_count_10, b_count_11, b_count_12, b_count_13,
       b_count_14, b_count_15, B_LOAD_HIGH, B_LOAD_LOW, B_READ_HIGH, B_READ_LOW, n7404_1_pin6, n74138_1_pin4,
       n74138_2_pin4, n74138_2_pin5, n74157_1_pin2, n74157_1_pin3, n74157_1_pin5, n74157_1_pin6,
       n74157_1_pin15, n74157_2_pin2, n74157_2_pin3, n74157_2_pin5, n74157_2_pin6, n74157_2_pin15,
       n74157_3_pin2, n74157_3_pin3, n74157_3_pin13, n74157_3_pin15, n74193_1_pin4, n74193_1_pin5,
       n74193_2_pin4, n74193_2_pin5, n74193_3_pin4, n74193_3_pin5, n74193_4_pin4, n74193_4_pin5,
       n74193_5_pin4, n74193_5_pin5, n74193_6_pin4, n74193_6_pin5, n74193_7_pin4, n74193_8_pin4,
       n_a_addr_sel, n_a_inc, n_b_addr_sel, n_b_inc, n_clock;

  _74193 u_74193_1 (
    .pin1(DATA_IN[5]), .pin2(a_count_13), .pin3(a_count_12), .pin4(n74193_1_pin4), .pin5(n74193_1_pin5),
    .pin6(a_count_14), .pin7(a_count_15), .pin15(DATA_IN[4]), .pin11(A_LOAD_HIGH), .pin10(DATA_IN[6]),
    .pin9(DATA_IN[7]));  // open: pin14, pin13, pin12
  _74193 u_74193_2 (
    .pin1(DATA_IN[5]), .pin2(b_count_13), .pin3(b_count_12), .pin4(n74193_2_pin4), .pin5(n74193_2_pin5),
    .pin6(b_count_14), .pin7(b_count_15), .pin15(DATA_IN[4]), .pin11(B_LOAD_HIGH), .pin10(DATA_IN[6]),
    .pin9(DATA_IN[7]));  // open: pin14, pin13, pin12
  _74244 u_74244_1 (
    .pin1(A_READ_HIGH), .pin2(a_count_8), .pin3(DATA_OUT[6]), .pin4(a_count_9), .pin5(DATA_OUT[7]),
    .pin6(a_count_10), .pin7(DATA_OUT[5]), .pin8(a_count_11), .pin9(DATA_OUT[4]), .pin19(A_READ_HIGH),
    .pin18(DATA_OUT[0]), .pin17(a_count_15), .pin16(DATA_OUT[1]), .pin15(a_count_14), .pin14(DATA_OUT[2]),
    .pin13(a_count_13), .pin12(DATA_OUT[3]), .pin11(a_count_12));
  _74244 u_74244_2 (
    .pin1(n_a_addr_sel), .pin2(a_count_8), .pin3(ADDR[15]), .pin4(a_count_9), .pin5(ADDR[14]),
    .pin6(a_count_10), .pin7(ADDR[13]), .pin8(a_count_11), .pin9(ADDR[12]), .pin19(n_a_addr_sel),
    .pin18(ADDR[8]), .pin17(a_count_15), .pin16(ADDR[9]), .pin15(a_count_14), .pin14(ADDR[10]),
    .pin13(a_count_13), .pin12(ADDR[11]), .pin11(a_count_12));
  _74193 u_74193_3 (
    .pin1(DATA_IN[1]), .pin2(a_count_9), .pin3(a_count_8), .pin4(n74193_3_pin4), .pin5(n74193_3_pin5),
    .pin6(a_count_10), .pin7(a_count_11), .pin15(DATA_IN[0]), .pin13(n74193_1_pin4), .pin12(n74193_1_pin5),
    .pin11(A_LOAD_HIGH), .pin10(DATA_IN[2]), .pin9(DATA_IN[3]));  // open: pin14
  _74193 u_74193_4 (
    .pin1(DATA_IN[1]), .pin2(b_count_9), .pin3(b_count_8), .pin4(n74193_4_pin4), .pin5(n74193_4_pin5),
    .pin6(b_count_10), .pin7(b_count_11), .pin15(DATA_IN[0]), .pin13(n74193_2_pin4), .pin12(n74193_2_pin5),
    .pin11(B_LOAD_HIGH), .pin10(DATA_IN[2]), .pin9(DATA_IN[3]));  // open: pin14
  _74244 u_74244_3 (
    .pin1(n_a_addr_sel), .pin2(a_count_0), .pin3(ADDR[7]), .pin4(a_count_1), .pin5(ADDR[6]),
    .pin6(a_count_2), .pin7(ADDR[5]), .pin8(a_count_3), .pin9(ADDR[4]), .pin19(n_a_addr_sel),
    .pin18(ADDR[0]), .pin17(a_count_7), .pin16(ADDR[1]), .pin15(a_count_6), .pin14(ADDR[2]),
    .pin13(a_count_5), .pin12(ADDR[3]), .pin11(a_count_4));
  _74193 u_74193_5 (
    .pin1(DATA_IN[5]), .pin2(a_count_5), .pin3(a_count_4), .pin4(n74193_5_pin4), .pin5(n74193_5_pin5),
    .pin6(a_count_6), .pin7(a_count_7), .pin15(DATA_IN[4]), .pin13(n74193_3_pin4), .pin12(n74193_3_pin5),
    .pin11(A_LOAD_LOW), .pin10(DATA_IN[6]), .pin9(DATA_IN[7]));  // open: pin14
  _74193 u_74193_6 (
    .pin1(DATA_IN[5]), .pin2(b_count_5), .pin3(b_count_4), .pin4(n74193_6_pin4), .pin5(n74193_6_pin5),
    .pin6(b_count_6), .pin7(b_count_7), .pin15(DATA_IN[4]), .pin13(n74193_4_pin4), .pin12(n74193_4_pin5),
    .pin11(B_LOAD_LOW), .pin10(DATA_IN[6]), .pin9(DATA_IN[7]));  // open: pin14
  _74244 u_74244_4 (
    .pin1(A_READ_LOW), .pin2(a_count_0), .pin3(DATA_OUT[6]), .pin4(a_count_1), .pin5(DATA_OUT[7]),
    .pin6(a_count_2), .pin7(DATA_OUT[5]), .pin8(a_count_3), .pin9(DATA_OUT[4]), .pin19(A_READ_LOW),
    .pin18(DATA_OUT[0]), .pin17(a_count_7), .pin16(DATA_OUT[1]), .pin15(a_count_6), .pin14(DATA_OUT[2]),
    .pin13(a_count_5), .pin12(DATA_OUT[3]), .pin11(a_count_4));
  _74193 u_74193_7 (
    .pin1(DATA_IN[1]), .pin2(a_count_1), .pin3(a_count_0), .pin4(n74193_7_pin4), .pin5(n_a_inc),
    .pin6(a_count_2), .pin7(a_count_3), .pin15(DATA_IN[0]), .pin13(n74193_5_pin4), .pin12(n74193_5_pin5),
    .pin11(A_LOAD_LOW), .pin10(DATA_IN[2]), .pin9(DATA_IN[3]));  // open: pin14
  _74193 u_74193_8 (
    .pin1(DATA_IN[1]), .pin2(b_count_1), .pin3(b_count_0), .pin4(n74193_8_pin4), .pin5(n_b_inc),
    .pin6(b_count_2), .pin7(b_count_3), .pin15(DATA_IN[0]), .pin13(n74193_6_pin4), .pin12(n74193_6_pin5),
    .pin11(B_LOAD_LOW), .pin10(DATA_IN[2]), .pin9(DATA_IN[3]));  // open: pin14
  _74244 u_74244_5 (
    .pin1(n_b_addr_sel), .pin2(b_count_8), .pin3(ADDR[15]), .pin4(b_count_9), .pin5(ADDR[14]),
    .pin6(b_count_10), .pin7(ADDR[13]), .pin8(b_count_11), .pin9(ADDR[12]), .pin19(n_b_addr_sel),
    .pin18(ADDR[8]), .pin17(b_count_15), .pin16(ADDR[9]), .pin15(b_count_14), .pin14(ADDR[10]),
    .pin13(b_count_13), .pin12(ADDR[11]), .pin11(b_count_12));
  _74244 u_74244_6 (
    .pin1(B_READ_HIGH), .pin2(b_count_8), .pin3(DATA_OUT[6]), .pin4(b_count_9), .pin5(DATA_OUT[7]),
    .pin6(b_count_10), .pin7(DATA_OUT[5]), .pin8(b_count_11), .pin9(DATA_OUT[4]), .pin19(B_READ_HIGH),
    .pin18(DATA_OUT[0]), .pin17(b_count_15), .pin16(DATA_OUT[1]), .pin15(b_count_14), .pin14(DATA_OUT[2]),
    .pin13(b_count_13), .pin12(DATA_OUT[3]), .pin11(b_count_12));
  _74244 u_74244_7 (
    .pin1(n_b_addr_sel), .pin2(b_count_0), .pin3(ADDR[7]), .pin4(b_count_1), .pin5(ADDR[6]),
    .pin6(b_count_2), .pin7(ADDR[5]), .pin8(b_count_3), .pin9(ADDR[4]), .pin19(n_b_addr_sel),
    .pin18(ADDR[0]), .pin17(b_count_7), .pin16(ADDR[1]), .pin15(b_count_6), .pin14(ADDR[2]),
    .pin13(b_count_5), .pin12(ADDR[3]), .pin11(b_count_4));
  _74244 u_74244_8 (
    .pin1(B_READ_LOW), .pin2(b_count_0), .pin3(DATA_OUT[6]), .pin4(b_count_1), .pin5(DATA_OUT[7]),
    .pin6(b_count_2), .pin7(DATA_OUT[5]), .pin8(b_count_3), .pin9(DATA_OUT[4]), .pin19(B_READ_LOW),
    .pin18(DATA_OUT[0]), .pin17(b_count_7), .pin16(DATA_OUT[1]), .pin15(b_count_6), .pin14(DATA_OUT[2]),
    .pin13(b_count_5), .pin12(DATA_OUT[3]), .pin11(b_count_4));
  _74157 u_74157_1 (
    .pin1(PC_LR_SWAP), .pin2(n74157_1_pin2), .pin3(n74157_1_pin3), .pin4(A_READ_LOW), .pin5(n74157_1_pin5),
    .pin6(n74157_1_pin6), .pin7(A_READ_HIGH), .pin15(n74157_1_pin15), .pin14(n74157_1_pin6),
    .pin13(n74157_1_pin5), .pin12(B_READ_HIGH), .pin11(n74157_1_pin3), .pin10(n74157_1_pin2),
    .pin9(B_READ_LOW));
  _74157 u_74157_2 (
    .pin1(PC_LR_SWAP), .pin2(n74157_2_pin2), .pin3(n74157_2_pin3), .pin4(A_LOAD_LOW), .pin5(n74157_2_pin5),
    .pin6(n74157_2_pin6), .pin7(A_LOAD_HIGH), .pin15(n74157_2_pin15), .pin14(n74157_2_pin6),
    .pin13(n74157_2_pin5), .pin12(B_LOAD_HIGH), .pin11(n74157_2_pin3), .pin10(n74157_2_pin2),
    .pin9(B_LOAD_LOW));
  _74157 u_74157_3 (
    .pin1(PC_LR_SWAP), .pin2(n74157_3_pin2), .pin3(n74157_3_pin3), .pin4(n_a_inc), .pin5(n74157_3_pin3),
    .pin6(n74157_3_pin2), .pin7(n_b_inc), .pin15(n74157_3_pin15), .pin14(n_ADDR_SEL), .pin13(n74157_3_pin13),
    .pin12(n_a_addr_sel), .pin11(n74157_3_pin13), .pin10(n_ADDR_SEL), .pin9(n_b_addr_sel));
  _74138 u_74138_1 (
    .pin1(RD_ADDR[0]), .pin2(RD_ADDR[1]), .pin3(RD_ADDR[2]), .pin4(n74138_1_pin4), .pin5(n74138_1_pin4),
    .pin6(RD_ADDR[4]), .pin7(n74157_1_pin6), .pin15(n74157_1_pin2), .pin14(n74157_1_pin5),
    .pin9(n74157_1_pin3));  // open: pin13, pin12, pin11, pin10
  _74138 u_74138_2 (
    .pin1(WR_ADDR[0]), .pin2(WR_ADDR[1]), .pin3(WR_ADDR[2]), .pin4(n74138_2_pin4), .pin5(n74138_2_pin5),
    .pin6(WR_ADDR[4]), .pin7(n74157_2_pin6), .pin15(n74157_2_pin2), .pin14(n74157_2_pin5),
    .pin9(n74157_2_pin3));  // open: pin13, pin12, pin11, pin10
  or or_1 (n74157_3_pin2, n_clock, nINC);
  _7404 u_7404_1 (
    .pin1(CLOCK), .pin2(n_clock), .pin3(WR_ADDR[3]), .pin4(n74138_2_pin4), .pin5(WR_ENABLE),
    .pin6(n7404_1_pin6), .pin13(RD_ADDR[3]), .pin12(n74138_1_pin4));  // open: pin11, pin10, pin9, pin8
  or or_2 (n74138_2_pin5, n7404_1_pin6, n_clock);
  // also tied to GND on the sheet: {n74157_1_pin15, n74157_2_pin15, n74157_3_pin15}
  // also tied to VCC on the sheet: {n74193_7_pin4, n74193_8_pin4, n74157_3_pin3, n74157_3_pin13}

  // Other names for the same wires on the sheet: addr_0 = ADDR[0]; addr_1 = ADDR[1]; addr_2 = ADDR[2];
  //   addr_3 = ADDR[3]; addr_4 = ADDR[4]; addr_5 = ADDR[5]; addr_6 = ADDR[6]; addr_7 = ADDR[7]; addr_8 = ADDR[8];
  //   addr_9 = ADDR[9]; addr_10 = ADDR[10]; addr_11 = ADDR[11]; addr_12 = ADDR[12]; addr_13 = ADDR[13];
  //   addr_14 = ADDR[14]; addr_15 = ADDR[15]; data_in_0 = DATA_IN[0]; data_in_1 = DATA_IN[1]; data_in_2 = DATA_IN[2];
  //   data_in_3 = DATA_IN[3]; data_in_4 = DATA_IN[4]; data_in_5 = DATA_IN[5]; data_in_6 = DATA_IN[6];
  //   data_in_7 = DATA_IN[7]; data_out_0 = DATA_OUT[0]; data_out_1 = DATA_OUT[1]; data_out_2 = DATA_OUT[2];
  //   data_out_3 = DATA_OUT[3]; data_out_4 = DATA_OUT[4]; data_out_5 = DATA_OUT[5]; data_out_6 = DATA_OUT[6];
  //   data_out_7 = DATA_OUT[7]
endmodule

module control_v5 (
  input  RESET,
  input  CLOCK,
  input  [7:0] IN,
  input  FLAG_ZERO,
  input  FLAG_CARRY,
  input  FLAG_NEGATIVE,
  input  FLAG_OVERFLOW,
  input  INT_REQUEST,
  output [7:0] DEBUG_INS,
  output DEBUG_FETCH,
  output WRITE_ENABLE,
  output ULA_ENABLE,
  output PCIA_SWAP,
  output PCLR_SWAP,
  output [15:0] ADDR_OUT,
  output [4:0] READ_ADDR,
  output [4:0] WRITE_ADDRESS,
  output FLAG_INTMASK
);

  wire and_3_out, and_4_out, and_5_out, and_7_out, and_8_out, clear_cond_register, finish_cycle, halt,
       high_cycle, int_pending, low_cycle, n7474_1_pin2, n7474_1_pin4, n7474_1_pin12, n7474_2_pin4,
       n74138_1_pin4, n74138_1_pin6, n74138_2_pin4, n74138_2_pin6, n74138_2_pin9, n74138_2_pin10,
       n74138_2_pin11, n74138_2_pin12, n74138_2_pin13, n74138_2_pin14, n74138_3_pin14, n74157_1_pin15,
       n74157_2_pin15, n74193_1_pin1, n74193_1_pin2, n74193_1_pin3, n74193_1_pin4, n74193_1_pin6,
       n74193_1_pin9, n74193_1_pin10, n74193_1_pin11, n74193_1_pin15, n74244_1_pin4, n74244_1_pin6,
       n74244_1_pin8, n74244_1_pin11, n74244_3_pin1, n74244_3_pin2, n74244_3_pin4, n74244_3_pin6,
       n74244_3_pin8, n74244_3_pin11, n74244_4_pin2, n74244_4_pin4, n74244_4_pin6, n74244_4_pin8,
       n74244_4_pin11, n74244_5_pin11, n74244_5_pin13, n74244_9_pin4, n74244_9_pin6, n74244_9_pin8,
       n74244_9_pin11, n74244_14_pin1, n74244_14_pin6, n74244_15_pin2, n74377_1_pin1, n74377_1_pin2,
       n74377_1_pin5, n74377_1_pin6, n74377_1_pin9, n74377_1_pin12, n74377_1_pin15, n74377_1_pin16,
       n74377_1_pin19, n74377_2_pin2, n_clear_int_mask, n_clear_int_pending, n_inhibit_write, n_int_mask,
       n_int_pending, n_select_code_0, n_select_code_1, n_select_code_2, n_select_code_3, n_select_code_4,
       n_select_code_5, n_select_code_6, n_select_code_7, n_set_int_mask, nand_1_out, nclock, nor_1_out,
       not_2_out, not_3_out, not_6_out, not_7_out, not_8_out, not_10_out, not_15_out, or_1_out, or_4_out,
       or_5_out, or_6_out, or_7_out, or_8_out, or_9_out, or_10_out, or_11_out, or_12_out,
       read_address_INTERRUPT, read_mem_const, reset_high, reset_low, restart_fetch, save_cond_register,
       save_src_register, ula_enable_t, write_address_t, write_const, write_enable_t, xnor_1_out, xnor_2_out,
       xnor_3_out, xnor_4_out, xor_1_out, xor_2_out;

  Pull_Resistor pull_resistor_1 (.node(write_const));
  Pull_Resistor pull_resistor_2 (.node(write_enable_t));
  or or_1 (or_1_out, write_const, write_enable_t);
  _74377 u_74377_1 (
    .pin1(n74377_1_pin1), .pin2(n74377_1_pin2), .pin3(IN[0]), .pin4(IN[1]), .pin5(n74377_1_pin5),
    .pin6(n74377_1_pin6), .pin7(IN[2]), .pin8(IN[3]), .pin9(n74377_1_pin9), .pin19(n74377_1_pin19),
    .pin18(IN[7]), .pin17(IN[6]), .pin16(n74377_1_pin16), .pin15(n74377_1_pin15), .pin14(IN[5]),
    .pin13(IN[4]), .pin12(n74377_1_pin12), .pin11(CLOCK));
  not not_1 (n74377_1_pin1, DEBUG_FETCH);
  or or_2 (read_mem_const, reset_low, reset_high);
  or or_3 (write_const, reset_low, reset_high);
  and and_1 (WRITE_ENABLE, or_1_out, n_inhibit_write);
  and and_2 (ULA_ENABLE, n_inhibit_write, ula_enable_t);
  Pull_Resistor pull_resistor_3 (.node(ula_enable_t));
  Pull_Resistor pull_resistor_4 (.node(save_src_register));
  xor xor_1 (xor_1_out, n74377_2_pin2, high_cycle);
  or or_4 (or_4_out, DEBUG_FETCH, read_mem_const);
  Pull_Resistor #(.pull(1)) pull_resistor_5 (.node(n_clear_int_pending));
  and and_3 (and_3_out, INT_REQUEST, FLAG_INTMASK);
  _74157 u_74157_1 (
    .pin1(DEBUG_FETCH), .pin2(n74377_1_pin2), .pin3(IN[0]), .pin4(DEBUG_INS[0]), .pin5(n74377_1_pin5),
    .pin6(IN[1]), .pin7(DEBUG_INS[1]), .pin15(n74157_1_pin15), .pin14(n74377_1_pin9), .pin13(IN[3]),
    .pin12(DEBUG_INS[3]), .pin11(n74377_1_pin6), .pin10(IN[2]), .pin9(DEBUG_INS[2]));
  _74157 u_74157_2 (
    .pin1(DEBUG_FETCH), .pin2(n74377_1_pin12), .pin3(IN[4]), .pin4(DEBUG_INS[4]), .pin5(n74377_1_pin15),
    .pin6(IN[5]), .pin7(DEBUG_INS[5]), .pin15(n74157_2_pin15), .pin14(n74377_1_pin19), .pin13(IN[7]),
    .pin12(DEBUG_INS[7]), .pin11(n74377_1_pin16), .pin10(IN[6]), .pin9(DEBUG_INS[6]));
  not not_2 (not_2_out, save_src_register);
  _74244 u_74244_1 (
    .pin1(or_4_out), .pin2(xor_1_out), .pin4(n74244_1_pin4), .pin6(n74244_1_pin6), .pin8(n74244_1_pin8),
    .pin9(READ_ADDR[4]), .pin19(or_4_out), .pin18(READ_ADDR[0]), .pin16(READ_ADDR[1]), .pin14(READ_ADDR[2]),
    .pin12(READ_ADDR[3]), .pin11(n74244_1_pin11));  // open: pin3, pin5, pin7, pin17, pin15, pin13
  xor xor_2 (xor_2_out, high_cycle, DEBUG_INS[0]);
  _7474 u_7474_1 (
    .pin1(n_clear_int_pending), .pin2(n7474_1_pin2), .pin3(and_3_out), .pin4(n7474_1_pin4),
    .pin5(int_pending), .pin6(n_int_pending), .pin13(n_clear_int_mask), .pin12(n7474_1_pin12), .pin11(RESET),
    .pin10(n_set_int_mask), .pin9(FLAG_INTMASK), .pin8(n_int_mask));
  _74377 u_74377_2 (
    .pin1(not_2_out), .pin2(n74377_2_pin2), .pin3(DEBUG_INS[0]), .pin4(DEBUG_INS[1]), .pin5(n74244_1_pin4),
    .pin6(n74244_1_pin6), .pin7(DEBUG_INS[2]), .pin8(DEBUG_INS[3]), .pin9(n74244_1_pin8),
    .pin13(DEBUG_INS[4]), .pin12(n74244_1_pin11), .pin11(CLOCK));  // open: pin19, pin18, pin17, pin16, pin15, pin14
  not not_3 (not_3_out, write_address_t);
  _74244 u_74244_2 (
    .pin1(not_3_out), .pin2(xor_2_out), .pin4(DEBUG_INS[1]), .pin6(DEBUG_INS[2]), .pin8(DEBUG_INS[3]),
    .pin9(WRITE_ADDRESS[4]), .pin19(not_3_out), .pin18(WRITE_ADDRESS[0]), .pin16(WRITE_ADDRESS[1]),
    .pin14(WRITE_ADDRESS[2]), .pin12(WRITE_ADDRESS[3]), .pin11(DEBUG_INS[4]));  // open: pin3, pin5, pin7, pin17, pin15, pin13
  Pull_Resistor pull_resistor_6 (.node(write_address_t));
  _74244 u_74244_3 (
    .pin1(n74244_3_pin1), .pin2(n74244_3_pin2), .pin4(n74244_3_pin4), .pin6(n74244_3_pin6),
    .pin8(n74244_3_pin8), .pin9(READ_ADDR[4]), .pin19(n74244_3_pin1), .pin18(READ_ADDR[0]),
    .pin16(READ_ADDR[1]), .pin14(READ_ADDR[2]), .pin12(READ_ADDR[3]), .pin11(n74244_3_pin11));  // open: pin3, pin5, pin7, pin17, pin15, pin13
  not not_4 (n74244_3_pin1, read_mem_const);
  not not_5 (nclock, CLOCK);
  not not_6 (not_6_out, DEBUG_FETCH);
  not not_7 (not_7_out, DEBUG_FETCH);
  Pull_Resistor pull_resistor_7 (.node(write_const));
  or or_5 (or_5_out, n_int_pending, not_6_out);
  and and_4 (and_4_out, n_int_pending, low_cycle);
  Pull_Resistor #(.pull(1)) pull_resistor_8 (.node(read_address_INTERRUPT));
  _74244 u_74244_4 (
    .pin1(not_7_out), .pin2(n74244_4_pin2), .pin4(n74244_4_pin4), .pin6(n74244_4_pin6), .pin8(n74244_4_pin8),
    .pin9(READ_ADDR[4]), .pin19(not_7_out), .pin18(READ_ADDR[0]), .pin16(READ_ADDR[1]), .pin14(READ_ADDR[2]),
    .pin12(READ_ADDR[3]), .pin11(n74244_4_pin11));  // open: pin3, pin5, pin7, pin17, pin15, pin13
  not not_8 (not_8_out, write_const);
  or or_6 (or_6_out, high_cycle, reset_high);
  _74193 u_74193_1 (
    .pin1(n74193_1_pin1), .pin2(n74193_1_pin2), .pin3(n74193_1_pin3), .pin4(n74193_1_pin4), .pin5(nclock),
    .pin6(n74193_1_pin6), .pin15(n74193_1_pin15), .pin14(RESET), .pin11(n74193_1_pin11),
    .pin10(n74193_1_pin10), .pin9(n74193_1_pin9));  // open: pin7, pin13, pin12
  _74138 u_74138_1 (
    .pin1(DEBUG_INS[5]), .pin2(DEBUG_INS[6]), .pin3(DEBUG_INS[7]), .pin4(n74138_1_pin4),
    .pin5(n74138_1_pin4), .pin6(n74138_1_pin6), .pin7(n_select_code_7), .pin15(n_select_code_0),
    .pin14(n_select_code_1), .pin13(n_select_code_2), .pin12(n_select_code_3), .pin11(n_select_code_4),
    .pin10(n_select_code_5), .pin9(n_select_code_6));
  or or_7 (or_7_out, n_select_code_0, not_10_out);
  _74244 u_74244_5 (
    .pin1(n_select_code_0), .pin2(or_5_out), .pin4(and_4_out), .pin7(DEBUG_FETCH),
    .pin9(read_address_INTERRUPT), .pin19(or_7_out), .pin18(PCIA_SWAP), .pin16(restart_fetch),
    .pin13(n74244_5_pin13), .pin11(n74244_5_pin11));  // open: pin3, pin5, pin6, pin8, pin17, pin15, pin14, pin12
  Pull_Resistor #(.pull(1)) pull_resistor_9 (.node(PCIA_SWAP));
  _74244 u_74244_6 (
    .pin1(n_select_code_1), .pin2(DEBUG_FETCH), .pin4(low_cycle), .pin19(n_select_code_1),
    .pin18(save_src_register), .pin16(restart_fetch));  // open: pin3, pin5, pin6, pin7, pin8, pin9, pin17, pin15, pin14, pin13, pin12, pin11
  _74244 u_74244_7 (
    .pin1(n_select_code_2), .pin4(low_cycle), .pin19(n_select_code_2), .pin16(restart_fetch));  // open: pin2, pin3, pin5, pin6, pin7, pin8, pin9, pin18, pin17, pin15, pin14, pin13, pin12, pin11
  _74244 u_74244_8 (
    .pin1(n_select_code_3), .pin2(DEBUG_FETCH), .pin4(low_cycle), .pin19(n_select_code_3),
    .pin18(save_cond_register), .pin16(restart_fetch));  // open: pin3, pin5, pin6, pin7, pin8, pin9, pin17, pin15, pin14, pin13, pin12, pin11
  _74244 u_74244_9 (
    .pin1(not_8_out), .pin2(or_6_out), .pin4(n74244_9_pin4), .pin6(n74244_9_pin6), .pin8(n74244_9_pin8),
    .pin9(WRITE_ADDRESS[4]), .pin19(not_8_out), .pin18(WRITE_ADDRESS[0]), .pin16(WRITE_ADDRESS[1]),
    .pin14(WRITE_ADDRESS[2]), .pin12(WRITE_ADDRESS[3]), .pin11(n74244_9_pin11));  // open: pin3, pin5, pin7, pin17, pin15, pin13
  Pull_Resistor pull_resistor_10 (.node(restart_fetch));
  not not_9 (n74193_1_pin11, restart_fetch);
  and and_5 (and_5_out, low_cycle, high_cycle);
  not not_10 (not_10_out, and_5_out);
  _74138 u_74138_2 (
    .pin1(n74193_1_pin3), .pin2(n74193_1_pin2), .pin3(n74193_1_pin6), .pin4(n74138_2_pin4),
    .pin5(n74138_2_pin4), .pin6(n74138_2_pin6), .pin14(n74138_2_pin14), .pin13(n74138_2_pin13),
    .pin12(n74138_2_pin12), .pin11(n74138_2_pin11), .pin10(n74138_2_pin10), .pin9(n74138_2_pin9));  // open: pin7, pin15
  not not_11 (reset_low, n74138_2_pin14);
  not not_12 (reset_high, n74138_2_pin13);
  not not_13 (DEBUG_FETCH, n74138_2_pin12);
  not not_14 (low_cycle, n74138_2_pin11);
  not not_15 (not_15_out, low_cycle);
  or or_8 (or_8_out, low_cycle, high_cycle);
  Pull_Resistor #(.pull(1)) pull_resistor_11 (.node(read_address_INTERRUPT));
  not not_16 (high_cycle, n74138_2_pin10);
  not not_17 (finish_cycle, n74138_2_pin9);
  and and_6 (n74138_2_pin4, halt, CLOCK);
  _74244 u_74244_10 (
    .pin1(n_select_code_4), .pin2(not_15_out), .pin8(high_cycle), .pin19(n_select_code_4), .pin18(PCLR_SWAP),
    .pin12(restart_fetch));  // open: pin3, pin4, pin5, pin6, pin7, pin9, pin17, pin16, pin15, pin14, pin13, pin11
  _74244 u_74244_11 (
    .pin1(n_select_code_5), .pin2(low_cycle), .pin4(low_cycle), .pin6(high_cycle), .pin8(high_cycle),
    .pin19(n_select_code_5), .pin18(write_address_t), .pin16(write_enable_t), .pin14(clear_cond_register),
    .pin12(restart_fetch));  // open: pin3, pin5, pin7, pin9, pin17, pin15, pin13, pin11
  _74244 u_74244_12 (
    .pin1(n_select_code_6), .pin2(or_8_out), .pin4(or_8_out), .pin6(finish_cycle), .pin8(finish_cycle),
    .pin19(n_select_code_6), .pin18(write_address_t), .pin16(write_enable_t), .pin14(clear_cond_register),
    .pin12(restart_fetch));  // open: pin3, pin5, pin7, pin9, pin17, pin15, pin13, pin11
  _74244 u_74244_13 (
    .pin1(n_select_code_7), .pin2(low_cycle), .pin4(low_cycle), .pin6(high_cycle), .pin8(high_cycle),
    .pin19(n_select_code_7), .pin18(write_address_t), .pin16(ula_enable_t), .pin14(clear_cond_register),
    .pin12(restart_fetch));  // open: pin3, pin5, pin7, pin9, pin17, pin15, pin13, pin11
  _74244 u_74244_14 (
    .pin1(n74244_14_pin1), .pin2(reset_high), .pin3(ADDR_OUT[7]), .pin4(read_address_INTERRUPT),
    .pin5(ADDR_OUT[6]), .pin6(n74244_14_pin6), .pin7(ADDR_OUT[5]), .pin8(n74244_14_pin6), .pin9(ADDR_OUT[4]),
    .pin19(n74244_14_pin1), .pin18(ADDR_OUT[0]), .pin17(n74244_14_pin6), .pin16(ADDR_OUT[1]),
    .pin15(n74244_14_pin6), .pin14(ADDR_OUT[2]), .pin13(n74244_14_pin6), .pin12(ADDR_OUT[3]),
    .pin11(n74244_14_pin6));
  _74244 u_74244_15 (
    .pin1(n74244_14_pin1), .pin2(n74244_15_pin2), .pin3(ADDR_OUT[15]), .pin4(n74244_15_pin2),
    .pin5(ADDR_OUT[14]), .pin6(n74244_15_pin2), .pin7(ADDR_OUT[13]), .pin8(n74244_15_pin2),
    .pin9(ADDR_OUT[12]), .pin19(n74244_14_pin1), .pin18(ADDR_OUT[8]), .pin17(n74244_15_pin2),
    .pin16(ADDR_OUT[9]), .pin15(n74244_15_pin2), .pin14(ADDR_OUT[10]), .pin13(n74244_15_pin2),
    .pin12(ADDR_OUT[11]), .pin11(n74244_15_pin2));
  xnor xnor_1 (xnor_1_out, FLAG_ZERO, DEBUG_INS[4]);
  xnor xnor_2 (xnor_2_out, FLAG_CARRY, DEBUG_INS[4]);
  xnor xnor_3 (xnor_3_out, FLAG_NEGATIVE, DEBUG_INS[4]);
  xnor xnor_4 (xnor_4_out, FLAG_OVERFLOW, DEBUG_INS[4]);
  Pull_Resistor #(.pull(1)) pull_resistor_12 (.node(PCLR_SWAP));
  not not_18 (n74244_14_pin1, read_mem_const);
  Pull_Resistor pull_resistor_13 (.node(save_cond_register));
  or or_9 (or_9_out, DEBUG_INS[0], xnor_1_out);
  or or_10 (or_10_out, DEBUG_INS[1], xnor_2_out);
  or or_11 (or_11_out, DEBUG_INS[2], xnor_3_out);
  or or_12 (or_12_out, DEBUG_INS[3], xnor_4_out);
  and and_7 (and_7_out, save_cond_register, CLOCK);
  nor nor_1 (nor_1_out, clear_cond_register, RESET);
  nand nand_1 (nand_1_out, or_9_out, or_10_out, or_11_out, or_12_out);
  and and_8 (and_8_out, DEBUG_FETCH, CLOCK);
  Pull_Resistor pull_resistor_14 (.node(clear_cond_register));
  _7474 u_7474_2 (
    .pin1(nor_1_out), .pin2(nand_1_out), .pin3(and_7_out), .pin4(n7474_2_pin4), .pin6(n_inhibit_write));  // open: pin5, pin13, pin12, pin11, pin10, pin9, pin8
  _74138 u_74138_3 (
    .pin1(DEBUG_INS[0]), .pin2(DEBUG_INS[1]), .pin3(DEBUG_INS[2]), .pin4(DEBUG_INS[4]),
    .pin5(n_select_code_0), .pin6(and_8_out), .pin14(n74138_3_pin14), .pin13(n_set_int_mask),
    .pin12(n_clear_int_mask));  // open: pin7, pin15, pin11, pin10, pin9
  not not_19 (halt, n74138_3_pin14);
  // also tied to GND on the sheet: {n74157_1_pin15, n74157_2_pin15, n7474_1_pin12, n74244_3_pin2, n74244_3_pin11, n74244_4_pin2, n74244_4_pin4, n74244_4_pin6, n74138_1_pin4, n74244_9_pin4, n74244_9_pin6, n74244_4_pin11, n74244_5_pin11, n74193_1_pin10, n74193_1_pin9}
  // also tied to VCC on the sheet: {n7474_1_pin2, n7474_1_pin4, n74244_3_pin4, n74244_3_pin6, n74244_3_pin8, n74244_4_pin8, n74138_1_pin6, n74244_9_pin8, n74244_5_pin13, n74193_1_pin1, n74244_9_pin11, n74193_1_pin15, n74193_1_pin4, n74138_2_pin6, n74244_14_pin6, n74244_15_pin2, n7474_2_pin4}

  // Other names for the same wires on the sheet: ins_0 = DEBUG_INS[0]; ins_1 = DEBUG_INS[1]; ins_2 = DEBUG_INS[2];
  //   ins_3 = DEBUG_INS[3]; ins_4 = DEBUG_INS[4]; ins_5 = DEBUG_INS[5]; ins_6 = DEBUG_INS[6]; ins_7 = DEBUG_INS[7];
  //   data_in_0 = IN[0]; data_in_1 = IN[1]; data_in_2 = IN[2]; data_in_3 = IN[3]; data_in_4 = IN[4];
  //   data_in_5 = IN[5]; data_in_6 = IN[6]; data_in_7 = IN[7]; int_mask = FLAG_INTMASK; fetch_cycle = DEBUG_FETCH;
  //   read_mem_pc = DEBUG_FETCH

  // Notes on the sheet:
  //   IN: initial=0x21
endmodule

module reg16_file (
  input  WR_ENABLE,
  input  CLOCK,
  input  PCLR_SWAP,
  input  PCIA_SWAP,
  input  [4:0] WRITE_ADDR,
  input  [4:0] READ_ADDR,
  output nSelWriteSPL,
  output nSelReadSPL,
  output nSelWriteSPH,
  output nSelReadSPH,
  output nSelWriteMARL,
  output nSelReadMARL,
  output nSelWriteMARH,
  output nSelReadMARH,
  output MEMORY_WRITE,
  output MEMORY_READ,
  output nSelWrite0L,
  output nSelWrite1L,
  output nSelWrite2L,
  output nSelWrite0H,
  output nSelWrite1H,
  output nSelWrite2H,
  output nSelRead0L,
  output nSelRead1L,
  output nSelRead2L,
  output nSelRead0H,
  output nSelRead1H,
  output nSelRead2H,
  output nADDR_0,
  output nADDR_1,
  output nADDR_2,
  output nADDR_MAR,
  output INC_0,
  output INC_1,
  output INC_2,
  output MAR_INC,
  output nADDR_SP,
  output SP_DEC,
  output SP_INC
);

  wire and_2_out, lr_at_0, lr_at_1, lr_at_2, n74125_1_pin1, n74125_1_pin3, n74125_1_pin4, n74125_1_pin6,
       n74138_1_pin4, n74138_1_pin5, n74138_2_pin4, n74138_2_pin10, n74138_2_pin11, n74138_2_pin12,
       n74138_2_pin13, n74138_2_pin14, n74138_2_pin15, n74138_3_pin4, n74138_4_pin4, n74138_4_pin6,
       n74138_4_pin10, n74138_4_pin11, n74138_4_pin12, n74138_4_pin13, n74138_4_pin14, n74138_4_pin15,
       n74138_7_pin4, n74138_7_pin6, n74138_7_pin9, n74138_7_pin10, n74138_7_pin11, n74138_7_pin12,
       n74138_7_pin13, n74138_7_pin14, n74138_7_pin15, n74193_1_pin1, n74193_1_pin2, n74193_1_pin6,
       n74193_1_pin9, n74193_1_pin10, n74193_1_pin11, n74193_1_pin14, n74193_1_pin15, naddr_pc,
       naddr_read_mar, naddr_read_pc, naddr_read_sp, naddr_write_mar, naddr_write_pc, naddr_write_sp,
       not_1_out, not_2_out, not_6_out, not_7_out, not_12_out, not_13_out, not_14_out, not_15_out,
       not_16_out, not_17_out, nread_iod_mar, nSelReadLRH, nSelReadLRL, nSelReadPCH, nSelReadPCL,
       nSelWriteLRH, nSelWriteLRL, nSelWritePCH, nSelWritePCL, nwrite_iod_mar, pc_at_0, pc_at_1, pc_at_2,
       pc_inc, write;

  not not_1 (not_1_out, naddr_read_sp);
  not not_2 (not_2_out, naddr_write_sp);
  _74138 u_74138_1 (
    .pin1(WRITE_ADDR[0]), .pin2(WRITE_ADDR[1]), .pin3(WRITE_ADDR[2]), .pin4(n74138_1_pin4),
    .pin5(n74138_1_pin5), .pin6(write), .pin7(nSelWriteLRH), .pin15(nSelWritePCL), .pin14(nSelWritePCH),
    .pin13(nSelWriteSPL), .pin12(nSelWriteSPH), .pin11(nSelWriteMARL), .pin10(nSelWriteMARH),
    .pin9(nSelWriteLRL));
  not not_3 (n74138_1_pin4, WRITE_ADDR[3]);
  not not_4 (n74138_1_pin5, WRITE_ADDR[4]);
  _74138 u_74138_2 (
    .pin1(WRITE_ADDR[0]), .pin2(WRITE_ADDR[1]), .pin3(WRITE_ADDR[2]), .pin4(n74138_2_pin4),
    .pin5(WRITE_ADDR[4]), .pin6(WR_ENABLE), .pin15(n74138_2_pin15), .pin14(n74138_2_pin14),
    .pin13(n74138_2_pin13), .pin12(n74138_2_pin12), .pin11(n74138_2_pin11), .pin10(n74138_2_pin10));  // open: pin7, pin9
  not not_5 (n74138_2_pin4, WRITE_ADDR[3]);
  and and_1 (naddr_pc, naddr_write_pc, naddr_read_pc);
  not not_6 (not_6_out, naddr_pc);
  and and_2 (and_2_out, naddr_write_mar, naddr_read_mar);
  not not_7 (not_7_out, and_2_out);
  and and_3 (nADDR_SP, naddr_read_sp, naddr_write_sp);
  nand nand_1 (SP_DEC, not_2_out, CLOCK);
  nand nand_2 (SP_INC, not_1_out, CLOCK);
  nor nor_1 (MEMORY_WRITE, WRITE_ADDR[4], n74138_2_pin4);
  nand nand_3 (pc_inc, not_6_out, CLOCK);
  and and_4 (nADDR_MAR, nwrite_iod_mar, nread_iod_mar, and_2_out);
  nand nand_4 (MAR_INC, not_7_out, CLOCK);
  and and_5 (naddr_write_pc, n74138_2_pin15, n74138_2_pin14);
  and and_6 (naddr_write_sp, n74138_2_pin13, n74138_2_pin12);
  and and_7 (naddr_write_mar, n74138_2_pin11, n74138_2_pin10);
  and and_8 (write, WR_ENABLE, CLOCK);
  _74138 u_74138_3 (
    .pin1(READ_ADDR[0]), .pin2(READ_ADDR[1]), .pin3(READ_ADDR[2]), .pin4(n74138_3_pin4),
    .pin5(n74138_3_pin4), .pin6(READ_ADDR[4]), .pin7(nSelReadLRH), .pin15(nSelReadPCL), .pin14(nSelReadPCH),
    .pin13(nSelReadSPL), .pin12(nSelReadSPH), .pin11(nSelReadMARL), .pin10(nSelReadMARH), .pin9(nSelReadLRL));
  not not_8 (n74138_3_pin4, READ_ADDR[3]);
  _74138 u_74138_4 (
    .pin1(READ_ADDR[0]), .pin2(READ_ADDR[1]), .pin3(READ_ADDR[2]), .pin4(n74138_4_pin4), .pin5(READ_ADDR[4]),
    .pin6(n74138_4_pin6), .pin15(n74138_4_pin15), .pin14(n74138_4_pin14), .pin13(n74138_4_pin13),
    .pin12(n74138_4_pin12), .pin11(n74138_4_pin11), .pin10(n74138_4_pin10));  // open: pin7, pin9
  not not_9 (n74138_4_pin4, READ_ADDR[3]);
  _74138 u_74138_5 (
    .pin1(WRITE_ADDR[0]), .pin2(WRITE_ADDR[1]), .pin3(WRITE_ADDR[2]), .pin4(WRITE_ADDR[3]),
    .pin5(WRITE_ADDR[3]), .pin6(WRITE_ADDR[4]), .pin15(nwrite_iod_mar));  // open: pin7, pin14, pin13, pin12, pin11, pin10, pin9
  _74138 u_74138_6 (
    .pin1(READ_ADDR[0]), .pin2(READ_ADDR[1]), .pin3(READ_ADDR[2]), .pin4(READ_ADDR[3]), .pin5(READ_ADDR[3]),
    .pin6(READ_ADDR[4]), .pin15(nread_iod_mar));  // open: pin7, pin14, pin13, pin12, pin11, pin10, pin9
  nor nor_2 (MEMORY_READ, READ_ADDR[4], n74138_4_pin4);
  and and_9 (naddr_read_pc, n74138_4_pin15, n74138_4_pin14);
  and and_10 (naddr_read_sp, n74138_4_pin13, n74138_4_pin12);
  and and_11 (naddr_read_mar, n74138_4_pin11, n74138_4_pin10);
  Pull_Resistor #(.pull(1)) pull_resistor_1 (.node(nSelWrite0L));
  Pull_Resistor #(.pull(1)) pull_resistor_2 (.node(nSelWrite0H));
  Pull_Resistor #(.pull(1)) pull_resistor_3 (.node(nSelRead0L));
  Pull_Resistor #(.pull(1)) pull_resistor_4 (.node(nSelRead0H));
  Pull_Resistor #(.pull(1)) pull_resistor_5 (.node(nADDR_0));
  Pull_Resistor #(.pull(1)) pull_resistor_6 (.node(INC_0));
  _74125 u_74125_1 (
    .pin1(n74125_1_pin1), .pin2(PCIA_SWAP), .pin3(n74125_1_pin3), .pin4(n74125_1_pin4), .pin5(PCIA_SWAP),
    .pin6(n74125_1_pin6), .pin13(n74125_1_pin4), .pin12(PCLR_SWAP), .pin11(n74125_1_pin3),
    .pin10(n74125_1_pin1), .pin9(PCLR_SWAP), .pin8(n74125_1_pin6));
  _74244 u_74244_1 (
    .pin1(pc_at_0), .pin2(nSelWritePCL), .pin4(nSelWritePCH), .pin6(nSelReadPCL), .pin7(INC_0),
    .pin8(nSelReadPCH), .pin9(nADDR_0), .pin19(pc_at_0), .pin18(nSelWrite0L), .pin16(nSelWrite0H),
    .pin14(nSelRead0L), .pin13(pc_inc), .pin12(nSelRead0H), .pin11(naddr_pc));  // open: pin3, pin5, pin17, pin15
  _74244 u_74244_2 (
    .pin1(lr_at_0), .pin2(nSelWriteLRL), .pin3(nSelWrite1L), .pin4(nSelWriteLRH), .pin5(nSelWrite1H),
    .pin6(nSelReadLRL), .pin7(nSelRead1L), .pin8(nSelReadLRH), .pin9(nSelRead1H), .pin19(lr_at_1),
    .pin18(nSelWrite0L), .pin17(nSelWriteLRL), .pin16(nSelWrite0H), .pin15(nSelWriteLRH), .pin14(nSelRead0L),
    .pin13(nSelReadLRL), .pin12(nSelRead0H), .pin11(nSelReadLRH));
  not not_10 (n74125_1_pin1, n74125_1_pin4);
  Pull_Resistor #(.pull(1)) pull_resistor_7 (.node(nSelWrite1L));
  Pull_Resistor #(.pull(1)) pull_resistor_8 (.node(nSelWrite1H));
  Pull_Resistor #(.pull(1)) pull_resistor_9 (.node(nSelRead1L));
  Pull_Resistor #(.pull(1)) pull_resistor_10 (.node(nSelRead1H));
  Pull_Resistor #(.pull(1)) pull_resistor_11 (.node(nADDR_1));
  Pull_Resistor #(.pull(1)) pull_resistor_12 (.node(INC_1));
  _74193 u_74193_1 (
    .pin1(n74193_1_pin1), .pin2(n74193_1_pin2), .pin3(n74125_1_pin4), .pin4(n74125_1_pin6),
    .pin5(n74125_1_pin3), .pin6(n74193_1_pin6), .pin15(n74193_1_pin15), .pin14(n74193_1_pin14),
    .pin11(n74193_1_pin11), .pin10(n74193_1_pin10), .pin9(n74193_1_pin9));  // open: pin7, pin13, pin12
  not not_11 (n74193_1_pin14, n74138_7_pin9);
  _74138 u_74138_7 (
    .pin1(n74125_1_pin4), .pin2(n74193_1_pin2), .pin3(n74193_1_pin6), .pin4(n74138_7_pin4),
    .pin5(n74138_7_pin4), .pin6(n74138_7_pin6), .pin7(n74193_1_pin11), .pin15(n74138_7_pin15),
    .pin14(n74138_7_pin14), .pin13(n74138_7_pin13), .pin12(n74138_7_pin12), .pin11(n74138_7_pin11),
    .pin10(n74138_7_pin10), .pin9(n74138_7_pin9));
  not not_12 (not_12_out, n74138_7_pin15);
  not not_13 (not_13_out, n74138_7_pin14);
  not not_14 (not_14_out, n74138_7_pin13);
  not not_15 (not_15_out, n74138_7_pin12);
  not not_16 (not_16_out, n74138_7_pin11);
  not not_17 (not_17_out, n74138_7_pin10);
  Pull_Resistor #(.pull(1)) pull_resistor_13 (.node(nSelWrite2L));
  Pull_Resistor #(.pull(1)) pull_resistor_14 (.node(nSelWrite2H));
  Pull_Resistor #(.pull(1)) pull_resistor_15 (.node(nSelRead2L));
  Pull_Resistor #(.pull(1)) pull_resistor_16 (.node(nSelRead2H));
  Pull_Resistor #(.pull(1)) pull_resistor_17 (.node(nADDR_2));
  Pull_Resistor #(.pull(1)) pull_resistor_18 (.node(INC_2));
  nor nor_3 (pc_at_0, not_12_out, not_15_out);
  nor nor_4 (pc_at_1, not_13_out, not_16_out);
  nor nor_5 (pc_at_2, not_14_out, not_17_out);
  _74244 u_74244_3 (
    .pin1(pc_at_1), .pin2(nSelWritePCL), .pin4(nSelWritePCH), .pin6(nSelReadPCL), .pin7(INC_1),
    .pin8(nSelReadPCH), .pin9(nADDR_1), .pin19(pc_at_1), .pin18(nSelWrite1L), .pin16(nSelWrite1H),
    .pin14(nSelRead1L), .pin13(pc_inc), .pin12(nSelRead1H), .pin11(naddr_pc));  // open: pin3, pin5, pin17, pin15
  _74244 u_74244_4 (
    .pin1(lr_at_2), .pin2(nSelWriteLRL), .pin4(nSelWriteLRH), .pin6(nSelReadLRL), .pin8(nSelReadLRH),
    .pin18(nSelWrite2L), .pin16(nSelWrite2H), .pin14(nSelRead2L), .pin12(nSelRead2H));  // open: pin3, pin5, pin7, pin9, pin19, pin17, pin15, pin13, pin11
  nor nor_6 (lr_at_0, not_13_out, not_14_out);
  nor nor_7 (lr_at_1, not_12_out, not_17_out);
  nor nor_8 (lr_at_2, not_15_out, not_16_out);
  _74244 u_74244_5 (
    .pin1(pc_at_2), .pin2(nSelWritePCL), .pin4(nSelWritePCH), .pin6(nSelReadPCL), .pin7(INC_2),
    .pin8(nSelReadPCH), .pin9(nADDR_2), .pin19(pc_at_2), .pin18(nSelWrite2L), .pin16(nSelWrite2H),
    .pin14(nSelRead2L), .pin13(pc_inc), .pin12(nSelRead2H), .pin11(naddr_pc));  // open: pin3, pin5, pin17, pin15
  // also tied to GND on the sheet: {n74193_1_pin1, n74193_1_pin9, n74138_7_pin4}
  // also tied to VCC on the sheet: {n74138_4_pin6, n74193_1_pin15, n74193_1_pin10, n74138_7_pin6}
endmodule

module reg16 (
  input  [7:0] DATA_IN,
  input  nLOAD_HIGH,
  input  nLOAD_LOW,
  input  nINC,
  input  nDEC,
  input  nREAD_HIGH,
  input  nREAD_LOW,
  input  nADDR_SEL,
  output [7:0] DATA_OUT,
  output [15:0] ADDR
);

  wire count_0, count_1, count_2, count_3, count_4, count_5, count_6, count_7, count_8, count_9, count_10,
       count_11, count_12, count_13, count_14, count_15, n74193_1_pin4, n74193_1_pin5, n74193_2_pin4,
       n74193_2_pin5, n74193_3_pin4, n74193_3_pin5, n74244_5_pin3, n74244_5_pin5, n74244_5_pin7,
       n74244_5_pin9, n74244_5_pin12, n74244_5_pin14, n74244_5_pin16, n74244_5_pin18;

  _74193 u_74193_1 (
    .pin1(DATA_IN[5]), .pin2(count_13), .pin3(count_12), .pin4(n74193_1_pin4), .pin5(n74193_1_pin5),
    .pin6(count_14), .pin7(count_15), .pin15(DATA_IN[4]), .pin11(nLOAD_HIGH), .pin10(DATA_IN[6]),
    .pin9(DATA_IN[7]));  // open: pin14, pin13, pin12
  _74244 u_74244_1 (
    .pin1(nREAD_HIGH), .pin2(count_8), .pin3(DATA_OUT[6]), .pin4(count_9), .pin5(DATA_OUT[7]),
    .pin6(count_10), .pin7(DATA_OUT[5]), .pin8(count_11), .pin9(DATA_OUT[4]), .pin19(nREAD_HIGH),
    .pin18(DATA_OUT[0]), .pin17(count_15), .pin16(DATA_OUT[1]), .pin15(count_14), .pin14(DATA_OUT[2]),
    .pin13(count_13), .pin12(DATA_OUT[3]), .pin11(count_12));
  _74193 u_74193_2 (
    .pin1(DATA_IN[1]), .pin2(count_9), .pin3(count_8), .pin4(n74193_2_pin4), .pin5(n74193_2_pin5),
    .pin6(count_10), .pin7(count_11), .pin15(DATA_IN[0]), .pin13(n74193_1_pin4), .pin12(n74193_1_pin5),
    .pin11(nLOAD_HIGH), .pin10(DATA_IN[2]), .pin9(DATA_IN[3]));  // open: pin14
  _74244 u_74244_2 (
    .pin1(nADDR_SEL), .pin2(count_8), .pin3(ADDR[15]), .pin4(count_9), .pin5(ADDR[14]), .pin6(count_10),
    .pin7(ADDR[13]), .pin8(count_11), .pin9(ADDR[12]), .pin19(nADDR_SEL), .pin18(ADDR[8]), .pin17(count_15),
    .pin16(ADDR[9]), .pin15(count_14), .pin14(ADDR[10]), .pin13(count_13), .pin12(ADDR[11]), .pin11(count_12));
  _74193 u_74193_3 (
    .pin1(DATA_IN[5]), .pin2(count_5), .pin3(count_4), .pin4(n74193_3_pin4), .pin5(n74193_3_pin5),
    .pin6(count_6), .pin7(count_7), .pin15(DATA_IN[4]), .pin13(n74193_2_pin4), .pin12(n74193_2_pin5),
    .pin11(nLOAD_LOW), .pin10(DATA_IN[6]), .pin9(DATA_IN[7]));  // open: pin14
  _74244 u_74244_3 (
    .pin1(nREAD_LOW), .pin2(count_0), .pin3(DATA_OUT[6]), .pin4(count_1), .pin5(DATA_OUT[7]), .pin6(count_2),
    .pin7(DATA_OUT[5]), .pin8(count_3), .pin9(DATA_OUT[4]), .pin19(nREAD_LOW), .pin18(DATA_OUT[0]),
    .pin17(count_7), .pin16(DATA_OUT[1]), .pin15(count_6), .pin14(DATA_OUT[2]), .pin13(count_5),
    .pin12(DATA_OUT[3]), .pin11(count_4));
  _74244 u_74244_4 (
    .pin1(nADDR_SEL), .pin2(count_0), .pin3(ADDR[7]), .pin4(count_1), .pin5(ADDR[6]), .pin6(count_2),
    .pin7(ADDR[5]), .pin8(count_3), .pin9(ADDR[4]), .pin19(nADDR_SEL), .pin18(ADDR[0]), .pin17(count_7),
    .pin16(ADDR[1]), .pin15(count_6), .pin14(ADDR[2]), .pin13(count_5), .pin12(ADDR[3]), .pin11(count_4));
  _74193 u_74193_4 (
    .pin1(DATA_IN[1]), .pin2(count_1), .pin3(count_0), .pin4(nDEC), .pin5(nINC), .pin6(count_2),
    .pin7(count_3), .pin15(DATA_IN[0]), .pin13(n74193_3_pin4), .pin12(n74193_3_pin5), .pin11(nLOAD_LOW),
    .pin10(DATA_IN[2]), .pin9(DATA_IN[3]));  // open: pin14
  _74244 u_74244_5 (
    .pin2(count_0), .pin3(n74244_5_pin3), .pin4(count_1), .pin5(n74244_5_pin5), .pin6(count_2),
    .pin7(n74244_5_pin7), .pin8(count_3), .pin9(n74244_5_pin9), .pin18(n74244_5_pin18), .pin17(count_7),
    .pin16(n74244_5_pin16), .pin15(count_6), .pin14(n74244_5_pin14), .pin13(count_5), .pin12(n74244_5_pin12),
    .pin11(count_4));  // open: pin1, pin19
  _74283 u_74283_1 (
    .pin2(n74244_5_pin16), .pin3(DATA_IN[5]), .pin5(DATA_IN[4]), .pin6(n74244_5_pin18),
    .pin15(n74244_5_pin14), .pin14(DATA_IN[6]), .pin12(DATA_IN[7]), .pin11(n74244_5_pin12));  // open: pin1, pin4, pin7, pin13, pin10, pin9
  _74244 u_74244_6 (
    .pin2(count_8), .pin3(n74244_5_pin3), .pin4(count_9), .pin5(n74244_5_pin5), .pin6(count_10),
    .pin7(n74244_5_pin7), .pin8(count_11), .pin9(n74244_5_pin9), .pin18(n74244_5_pin18), .pin17(count_15),
    .pin16(n74244_5_pin16), .pin15(count_14), .pin14(n74244_5_pin14), .pin13(count_13),
    .pin12(n74244_5_pin12), .pin11(count_12));  // open: pin1, pin19
  _74283 u_74283_2 (
    .pin2(n74244_5_pin7), .pin3(DATA_IN[1]), .pin5(DATA_IN[0]), .pin6(n74244_5_pin9), .pin15(n74244_5_pin5),
    .pin14(DATA_IN[2]), .pin12(DATA_IN[3]), .pin11(n74244_5_pin3));  // open: pin1, pin4, pin7, pin13, pin10, pin9

  // Other names for the same wires on the sheet: addr_0 = ADDR[0]; addr_1 = ADDR[1]; addr_2 = ADDR[2];
  //   addr_3 = ADDR[3]; addr_4 = ADDR[4]; addr_5 = ADDR[5]; addr_6 = ADDR[6]; addr_7 = ADDR[7]; addr_8 = ADDR[8];
  //   addr_9 = ADDR[9]; addr_10 = ADDR[10]; addr_11 = ADDR[11]; addr_12 = ADDR[12]; addr_13 = ADDR[13];
  //   addr_14 = ADDR[14]; addr_15 = ADDR[15]; data_in_0 = DATA_IN[0]; data_in_1 = DATA_IN[1]; data_in_2 = DATA_IN[2];
  //   data_in_3 = DATA_IN[3]; data_in_4 = DATA_IN[4]; data_in_5 = DATA_IN[5]; data_in_6 = DATA_IN[6];
  //   data_in_7 = DATA_IN[7]; data_out_0 = DATA_OUT[0]; data_out_1 = DATA_OUT[1]; data_out_2 = DATA_OUT[2];
  //   data_out_3 = DATA_OUT[3]; data_out_4 = DATA_OUT[4]; data_out_5 = DATA_OUT[5]; data_out_6 = DATA_OUT[6];
  //   data_out_7 = DATA_OUT[7]

  // Notes on the sheet:
  //   nLOAD_HIGH: initial=0x1
  //   nADDR_SEL: initial=0x1
  //   nREAD_HIGH: initial=0x1
  //   nREAD_LOW: initial=0x1
  //   nLOAD_LOW: initial=0x1
endmodule
