// Logisim project selecao_registradores.circ as structural Verilog: 1 circuit, main circuit main
module main (
  input  SWAP_PC_LR,
  input  SWAP_PC_IA,
  input  PC,
  input  LR,
  input  IA,
  input  RESET,
  input  CLOCK
);

  wire and_1_out, and_2_out, and_3_out, and_4_out, and_5_out, and_6_out, and_7_out, and_8_out, and_9_out,
       n74125_1_pin1, n74125_1_pin3, n74125_1_pin4, n74125_1_pin6, n74138_1_pin4, n74138_1_pin6,
       n74138_1_pin9, n74138_1_pin10, n74138_1_pin11, n74138_1_pin12, n74138_1_pin13, n74138_1_pin14,
       n74138_1_pin15, n74193_1_pin1, n74193_1_pin2, n74193_1_pin6, n74193_1_pin9, n74193_1_pin10,
       n74193_1_pin11, n74193_1_pin14, n74193_1_pin15, not_3_out, not_4_out, not_5_out, not_6_out, not_7_out,
       not_8_out, or_1_out, or_2_out, or_3_out, or_4_out, or_5_out, or_6_out, or_7_out, or_8_out, or_9_out;

  _74125 u_74125_1 (
    .pin1(n74125_1_pin1), .pin2(SWAP_PC_IA), .pin3(n74125_1_pin3), .pin4(n74125_1_pin4), .pin5(SWAP_PC_IA),
    .pin6(n74125_1_pin6), .pin13(n74125_1_pin4), .pin12(SWAP_PC_LR), .pin11(n74125_1_pin3),
    .pin10(n74125_1_pin1), .pin9(SWAP_PC_LR), .pin8(n74125_1_pin6));
  not not_1 (n74125_1_pin1, n74125_1_pin4);
  _74193 u_74193_1 (
    .pin1(n74193_1_pin1), .pin2(n74193_1_pin2), .pin3(n74125_1_pin4), .pin4(n74125_1_pin6),
    .pin5(n74125_1_pin3), .pin6(n74193_1_pin6), .pin15(n74193_1_pin15), .pin14(n74193_1_pin14),
    .pin11(n74193_1_pin11), .pin10(n74193_1_pin10), .pin9(n74193_1_pin9));  // open: pin7, pin13, pin12
  _74138 u_74138_1 (
    .pin1(n74125_1_pin4), .pin2(n74193_1_pin2), .pin3(n74193_1_pin6), .pin4(n74138_1_pin4),
    .pin5(n74138_1_pin4), .pin6(n74138_1_pin6), .pin7(n74193_1_pin11), .pin15(n74138_1_pin15),
    .pin14(n74138_1_pin14), .pin13(n74138_1_pin13), .pin12(n74138_1_pin12), .pin11(n74138_1_pin11),
    .pin10(n74138_1_pin10), .pin9(n74138_1_pin9));
  not not_2 (n74193_1_pin14, n74138_1_pin9);
  not not_3 (not_3_out, n74138_1_pin15);
  not not_4 (not_4_out, n74138_1_pin14);
  not not_5 (not_5_out, n74138_1_pin13);
  not not_6 (not_6_out, n74138_1_pin12);
  not not_7 (not_7_out, n74138_1_pin11);
  not not_8 (not_8_out, n74138_1_pin10);
  or or_1 (or_1_out, not_3_out, not_6_out);
  or or_2 (or_2_out, not_4_out, not_7_out);
  or or_3 (or_3_out, not_5_out, not_8_out);
  and and_1 (and_1_out, or_1_out, PC);
  LED led_1 (.in(and_1_out));
  and and_2 (and_2_out, or_2_out, PC);
  LED led_2 (.in(and_2_out));
  and and_3 (and_3_out, or_3_out, PC);
  LED led_3 (.in(and_3_out));
  or or_4 (or_4_out, not_4_out, not_5_out);
  and and_4 (and_4_out, or_4_out, LR);
  or or_5 (or_5_out, not_3_out, not_8_out);
  and and_5 (and_5_out, or_5_out, LR);
  or or_6 (or_6_out, not_6_out, not_7_out);
  and and_6 (and_6_out, or_6_out, LR);
  LED led_4 (.in(and_4_out));
  LED led_5 (.in(and_5_out));
  LED led_6 (.in(and_6_out));
  or or_7 (or_7_out, not_7_out, not_8_out);
  or or_8 (or_8_out, not_5_out, not_6_out);
  or or_9 (or_9_out, not_3_out, not_4_out);
  and and_7 (and_7_out, or_7_out, IA);
  LED led_7 (.in(and_7_out));
  and and_8 (and_8_out, or_8_out, IA);
  LED led_8 (.in(and_8_out));
  and and_9 (and_9_out, or_9_out, IA);
  LED led_9 (.in(and_9_out));
  // also tied to GND on the sheet: {n74193_1_pin1, n74193_1_pin9, n74138_1_pin4}
  // also tied to VCC on the sheet: {n74193_1_pin15, n74193_1_pin10, n74138_1_pin6}
endmodule
