// Logisim project serial.circ as structural Verilog: 1 circuit, main circuit main
module main (
  input  in_1,
  input  [7:0] DATA,
  input  WRITE
);

  wire and_1_out, and_2_out, and_3_out, c_lock, clock_1_out, data_bit, digital_oscilloscope_1_p4,
       n7404_1_pin2, n7474_1_pin6, n74138_1_pin1, n74138_1_pin2, n74138_1_pin3, n74138_1_pin4, n74138_1_pin6,
       n74138_2_pin4, n74138_2_pin12, n74165_1_pin9, n74165_1_pin10, n74193_1_pin4, n74193_1_pin14,
       n74377_1_pin1, n74377_1_pin2, n74377_1_pin5, n74377_1_pin6, n74377_1_pin9, n74377_1_pin12,
       n74377_1_pin15, n74377_1_pin16, n74377_1_pin19, start_bit, stop_bit, TX;

  // Digital_Oscilloscope #(.nState(12)) digital_oscilloscope_1: pin names not known; wires that end beside it: c_lock, TX, in_1, digital_oscilloscope_1_p4
  Button button_1 (.out(digital_oscilloscope_1_p4));
  nand nand_1 (data_bit, stop_bit, start_bit);
  _74138 u_74138_1 (
    .pin1(n74138_1_pin1), .pin2(n74138_1_pin2), .pin3(n74138_1_pin3), .pin4(n74138_1_pin4),
    .pin5(n74138_1_pin4), .pin6(n74138_1_pin6), .pin14(start_bit));  // open: pin7, pin15, pin13, pin12, pin11, pin10, pin9
  or or_1 (c_lock, n7474_1_pin6, clock_1_out);
  Clock clock_1 (.out(clock_1_out));
  _74377 u_74377_1 (
    .pin1(n74377_1_pin1), .pin2(n74377_1_pin2), .pin3(DATA[0]), .pin4(DATA[1]), .pin5(n74377_1_pin5),
    .pin6(n74377_1_pin6), .pin7(DATA[2]), .pin8(DATA[3]), .pin9(n74377_1_pin9), .pin19(n74377_1_pin19),
    .pin18(DATA[7]), .pin17(DATA[6]), .pin16(n74377_1_pin16), .pin15(n74377_1_pin15), .pin14(DATA[5]),
    .pin13(DATA[4]), .pin12(n74377_1_pin12), .pin11(WRITE));
  _74138 u_74138_2 (
    .pin1(n74138_1_pin1), .pin2(n74138_1_pin2), .pin3(n74138_1_pin3), .pin4(n74138_2_pin4),
    .pin5(n74138_2_pin4), .pin6(n74138_1_pin6), .pin13(stop_bit), .pin12(n74138_2_pin12));  // open: pin7, pin15, pin14, pin11, pin10, pin9
  _74193 u_74193_1 (
    .pin2(n74138_1_pin2), .pin3(n74138_1_pin1), .pin4(n74193_1_pin4), .pin5(c_lock), .pin6(n74138_1_pin3),
    .pin7(n74138_1_pin4), .pin14(n74193_1_pin14));  // open: pin1, pin15, pin13, pin12, pin11, pin10, pin9
  _74165 u_74165_1 (
    .pin1(start_bit), .pin2(c_lock), .pin3(n74377_1_pin12), .pin4(n74377_1_pin15), .pin5(n74377_1_pin16),
    .pin6(n74377_1_pin19), .pin15(data_bit), .pin14(n74377_1_pin9), .pin13(n74377_1_pin6),
    .pin12(n74377_1_pin5), .pin11(n74377_1_pin2), .pin10(n74165_1_pin10), .pin9(n74165_1_pin9));  // open: pin7
  _7404 u_7404_1 (
    .pin1(WRITE), .pin2(n7404_1_pin2), .pin5(n74138_1_pin4), .pin6(n74138_2_pin4), .pin9(n74138_2_pin12),
    .pin8(n74193_1_pin14));  // open: pin3, pin4, pin13, pin12, pin11, pin10
  _7474 u_7474_1 (
    .pin1(n74138_2_pin12), .pin4(n7404_1_pin2), .pin5(n74138_1_pin6), .pin6(n7474_1_pin6));  // open: pin2, pin3, pin13, pin12, pin11, pin10, pin9, pin8
  and and_1 (and_1_out, n74165_1_pin9, ~data_bit);  // AND_Gate
  and and_2 (and_2_out, ~stop_bit, 1'b1);  // AND_Gate
  and and_3 (and_3_out, ~start_bit, 1'b0);  // AND_Gate
  or or_2 (TX, and_1_out, and_2_out, and_3_out, n7474_1_pin6);
  // also tied to GND on the sheet: {n74377_1_pin1, n74165_1_pin10}
  // also tied to VCC on the sheet: n74193_1_pin4
endmodule
