// Logisim project serial_v2.circ as structural Verilog: 1 circuit, main circuit main
module main (
  input  [7:0] DATA_IN,
  input  SEND,
  output SERIAL_TX
);

  wire and_2_out, baud_rate, data_bit, finish, n7474_1_pin1, n7474_1_pin2, n74138_1_pin6, n74138_1_pin7,
       n74138_1_pin9, n74138_1_pin10, n74138_1_pin11, n74138_1_pin12, n74138_1_pin13, n74138_2_pin4,
       n74138_2_pin12, n74138_2_pin13, n74138_2_pin14, n74138_2_pin15, n74193_1_pin2, n74193_1_pin3,
       n74193_1_pin4, n74193_1_pin5, n74193_1_pin6, n74193_1_pin7, n74193_1_pin11, n74377_1_pin1,
       n74377_1_pin11, n_idle, n_start_bit, not_1_out, not_2_out, not_3_out, not_4_out, not_5_out, not_6_out,
       not_7_out, not_8_out, not_9_out, not_12_out, pull_resistor_1_node, send_byte, stop_bit;
  wire [7:0] after_shift, before_shift;

  _74193 u_74193_1 (
    .pin2(n74193_1_pin2), .pin3(n74193_1_pin3), .pin4(n74193_1_pin4), .pin5(n74193_1_pin5),
    .pin6(n74193_1_pin6), .pin7(n74193_1_pin7), .pin14(finish), .pin11(n74193_1_pin11));  // open: pin1, pin15, pin13, pin12, pin10, pin9
  and and_1 (n74193_1_pin5, send_byte, baud_rate);
  _74377 u_74377_1 (
    .pin1(n74377_1_pin1), .pin2(after_shift[0]), .pin3(before_shift[0]), .pin4(before_shift[1]),
    .pin5(after_shift[1]), .pin6(after_shift[2]), .pin7(before_shift[2]), .pin8(before_shift[3]),
    .pin9(after_shift[3]), .pin19(after_shift[7]), .pin18(before_shift[7]), .pin17(before_shift[6]),
    .pin16(after_shift[6]), .pin15(after_shift[5]), .pin14(before_shift[5]), .pin13(before_shift[4]),
    .pin12(after_shift[4]), .pin11(n74377_1_pin11));
  or or_1 (data_bit, not_9_out, not_8_out, not_7_out, not_6_out, not_5_out, not_4_out, not_2_out, not_1_out);
  _74138 u_74138_1 (
    .pin1(n74193_1_pin3), .pin2(n74193_1_pin2), .pin3(n74193_1_pin6), .pin4(n74193_1_pin7),
    .pin5(n74193_1_pin7), .pin6(n74138_1_pin6), .pin7(n74138_1_pin7), .pin15(n_idle), .pin14(n_start_bit),
    .pin13(n74138_1_pin13), .pin12(n74138_1_pin12), .pin11(n74138_1_pin11), .pin10(n74138_1_pin10),
    .pin9(n74138_1_pin9));
  _74244 u_74244_1 (
    .pin1(n_idle), .pin2(DATA_IN[0]), .pin3(before_shift[7]), .pin4(DATA_IN[1]), .pin5(before_shift[6]),
    .pin6(DATA_IN[2]), .pin7(before_shift[5]), .pin8(DATA_IN[3]), .pin9(before_shift[4]), .pin19(n_idle),
    .pin18(before_shift[0]), .pin17(DATA_IN[7]), .pin16(before_shift[1]), .pin15(DATA_IN[6]),
    .pin14(before_shift[2]), .pin13(DATA_IN[5]), .pin12(before_shift[3]), .pin11(DATA_IN[4]));
  or or_2 (n74377_1_pin11, and_2_out, SEND);
  not not_1 (not_1_out, n74138_1_pin13);
  not not_2 (not_2_out, n74138_1_pin12);
  not not_3 (not_3_out, baud_rate);
  and and_2 (and_2_out, not_3_out, data_bit);
  not not_4 (not_4_out, n74138_1_pin11);
  not not_5 (not_5_out, n74138_1_pin10);
  not not_6 (not_6_out, n74138_1_pin9);
  not not_7 (not_7_out, n74138_1_pin7);
  not not_8 (not_8_out, n74138_2_pin15);
  _74138 u_74138_2 (
    .pin1(n74193_1_pin3), .pin2(n74193_1_pin2), .pin3(n74193_1_pin6), .pin4(n74138_2_pin4),
    .pin5(n74138_2_pin4), .pin6(n74193_1_pin7), .pin15(n74138_2_pin15), .pin14(n74138_2_pin14),
    .pin13(n74138_2_pin13), .pin12(n74138_2_pin12));  // open: pin7, pin11, pin10, pin9
  not not_9 (not_9_out, n74138_2_pin14);
  not not_10 (stop_bit, n74138_2_pin13);
  not not_11 (finish, n74138_2_pin12);
  Clock clock_1 (.out(baud_rate));
  not not_12 (not_12_out, data_bit);
  Pull_Resistor #(.pull(1)) pull_resistor_1 (.node(pull_resistor_1_node));
  _74244 u_74244_2 (
    .pin1(not_12_out), .pin2(after_shift[0]), .pin3(before_shift[6]), .pin4(after_shift[1]),
    .pin5(before_shift[5]), .pin6(after_shift[2]), .pin7(before_shift[4]), .pin8(after_shift[3]),
    .pin9(before_shift[3]), .pin19(not_12_out), .pin18(pull_resistor_1_node), .pin17(after_shift[7]),
    .pin16(before_shift[0]), .pin15(after_shift[6]), .pin14(before_shift[1]), .pin13(after_shift[5]),
    .pin12(before_shift[2]), .pin11(after_shift[4]));
  _7474 u_7474_1 (
    .pin1(n7474_1_pin1), .pin2(n7474_1_pin2), .pin3(SEND), .pin5(send_byte));  // open: pin4, pin6, pin13, pin12, pin11, pin10, pin9, pin8
  not not_13 (n7474_1_pin1, finish);
  and and_3 (SERIAL_TX, pull_resistor_1_node, n_start_bit);
  // also tied to GND on the sheet: {n74377_1_pin1, n74138_2_pin4}
  // also tied to VCC on the sheet: {n74193_1_pin4, n74193_1_pin11, n74138_1_pin6, n7474_1_pin2}
endmodule
