// Logisim project testbench.circ as structural Verilog: 1 circuit, main circuit main
module main (
  input  write_data,
  input  write_dir,
  input  n_read_enable,
  input  in_4,
  input  in_5,
  input  in_6,
  input  in_7,
  input  in_8,
  input  in_9,
  input  in_10,
  input  in_11,
  input  in_12,
  input  in_13,
  input  in_14,
  input  in_15,
  input  in_16,
  input  in_17,
  input  in_18,
  input  in_19
);

  wire dir_0, dir_1, dir_2, dir_3, dir_4, dir_5, dir_6, dir_7, dir_r0, dir_r1, dir_r2, dir_r3, dir_r4,
       dir_r5, dir_r6, dir_r7, latch_0, latch_1, latch_2, latch_3, latch_4, latch_5, latch_6, latch_7,
       n74377_1_pin1, n74377_2_pin1;

  LED led_1 (.in(in_4));
  LED led_2 (.in(in_5));
  LED led_3 (.in(in_6));
  LED led_4 (.in(in_7));
  LED led_5 (.in(in_8));
  LED led_6 (.in(in_9));
  LED led_7 (.in(in_10));
  LED led_8 (.in(in_11));
  LED led_9 (.in(in_12));
  LED led_10 (.in(in_13));
  LED led_11 (.in(in_14));
  LED led_12 (.in(in_15));
  LED led_13 (.in(in_16));
  LED led_14 (.in(in_17));
  LED led_15 (.in(in_18));
  LED led_16 (.in(in_19));
  _74377 u_74377_1 (
    .pin1(n74377_1_pin1), .pin2(latch_0), .pin3(in_4), .pin4(in_5), .pin5(latch_1), .pin6(latch_2),
    .pin7(in_6), .pin8(in_7), .pin9(latch_3), .pin19(latch_7), .pin18(in_11), .pin17(in_10), .pin16(latch_6),
    .pin15(latch_5), .pin14(in_9), .pin13(in_8), .pin12(latch_4), .pin11(write_data));
  _74377 u_74377_2 (
    .pin1(n74377_2_pin1), .pin2(dir_0), .pin3(in_4), .pin4(in_5), .pin5(dir_1), .pin6(dir_2), .pin7(in_6),
    .pin8(in_7), .pin9(dir_3), .pin19(dir_7), .pin18(in_11), .pin17(in_10), .pin16(dir_6), .pin15(dir_5),
    .pin14(in_9), .pin13(in_8), .pin12(dir_4), .pin11(write_dir));
  Pull_Resistor #(.pull(1)) pull_resistor_1 (.node(dir_r7));
  Pull_Resistor #(.pull(1)) pull_resistor_2 (.node(dir_r6));
  Pull_Resistor #(.pull(1)) pull_resistor_3 (.node(dir_r5));
  Pull_Resistor #(.pull(1)) pull_resistor_4 (.node(dir_r4));
  _74240 u_74240_1 (
    .pin1(n_read_enable), .pin2(dir_0), .pin3(dir_r7), .pin4(dir_1), .pin5(dir_r6), .pin6(dir_2),
    .pin7(dir_r5), .pin8(dir_3), .pin9(dir_r4), .pin19(n_read_enable), .pin18(dir_r0), .pin17(dir_7),
    .pin16(dir_r1), .pin15(dir_6), .pin14(dir_r2), .pin13(dir_5), .pin12(dir_r3), .pin11(dir_4));
  Pull_Resistor #(.pull(1)) pull_resistor_5 (.node(dir_r0));
  Pull_Resistor #(.pull(1)) pull_resistor_6 (.node(dir_r1));
  Pull_Resistor #(.pull(1)) pull_resistor_7 (.node(dir_r2));
  Pull_Resistor #(.pull(1)) pull_resistor_8 (.node(dir_r3));
  _74125 u_74125_1 (
    .pin1(dir_0), .pin2(latch_0), .pin3(in_12), .pin4(dir_1), .pin5(latch_1), .pin6(in_13), .pin13(dir_3),
    .pin12(latch_3), .pin11(in_15), .pin10(dir_2), .pin9(latch_2), .pin8(in_14));
  _74125 u_74125_2 (
    .pin1(dir_4), .pin2(latch_4), .pin3(in_16), .pin4(dir_5), .pin5(latch_5), .pin6(in_17), .pin13(dir_7),
    .pin12(latch_7), .pin11(in_19), .pin10(dir_6), .pin9(latch_6), .pin8(in_18));
  _74125 u_74125_3 (
    .pin1(dir_r0), .pin2(in_12), .pin3(in_4), .pin4(dir_r1), .pin5(in_13), .pin6(in_5), .pin13(dir_r3),
    .pin12(in_15), .pin11(in_7), .pin10(dir_r2), .pin9(in_14), .pin8(in_6));
  _74125 u_74125_4 (
    .pin1(dir_4), .pin2(in_16), .pin3(in_8), .pin4(dir_5), .pin5(in_17), .pin6(in_9), .pin13(dir_r7),
    .pin12(in_19), .pin11(in_11), .pin10(dir_r6), .pin9(in_18), .pin8(in_10));
  // also tied to GND on the sheet: {n74377_2_pin1, n74377_1_pin1}

  // Other names for the same wires on the sheet: data_in_0 = in_4; data_out_0 = in_4; data_in_1 = in_5;
  //   data_out_1 = in_5; data_in_2 = in_6; data_out_2 = in_6; data_in_3 = in_7; data_out_3 = in_7; data_in_4 = in_8;
  //   data_out_4 = in_8; data_in_5 = in_9; data_out_5 = in_9; data_in_6 = in_10; data_out_6 = in_10;
  //   data_in_7 = in_11; data_out_7 = in_11; test_in_0 = in_12; test_out_0 = in_12; test_in_1 = in_13;
  //   test_out_1 = in_13; test_in_2 = in_14; test_out_2 = in_14; test_in_3 = in_15; test_out_3 = in_15;
  //   test_in_4 = in_16; test_out_4 = in_16; test_in_5 = in_17; test_out_5 = in_17; test_in_6 = in_18;
  //   test_out_6 = in_18; test_in_7 = in_19; test_out_7 = in_19
endmodule
