// Logisim project ula_control.circ as structural Verilog
module ulacontrol (
  input  [3:0] in_1
);

  wire clr_cf, clr_if, execute_shift, invert_lower_bus, n7404_1_pin2, n7404_1_pin4, n7404_1_pin6,
       n7404_1_pin8, n7404_1_pin10, n7404_1_pin12, n7404_2_pin2, n7404_2_pin4, n7404_2_pin6, n7404_2_pin8,
       n7404_2_pin10, n7404_2_pin12, n74138_1_pin6, n74138_1_pin7, n74138_1_pin10, n74138_1_pin11,
       n74138_1_pin12, n74138_1_pin13, n74138_1_pin14, n74138_1_pin15, n74138_2_pin4, n74138_2_pin13,
       n74138_2_pin14, n74138_2_pin15, or_1_out, or_2_out, or_3_out, or_4_out, save_acc, select_adder,
       select_left_shifter, select_logic, select_right_shifter, select_sx, select_xor, set_cf, set_if;

  _74138 u_74138_1 (
    .pin1(in_1[0]), .pin2(in_1[1]), .pin3(in_1[2]), .pin4(in_1[3]), .pin5(in_1[3]), .pin6(n74138_1_pin6),
    .pin7(n74138_1_pin7), .pin15(n74138_1_pin15), .pin14(n74138_1_pin14), .pin13(n74138_1_pin13),
    .pin12(n74138_1_pin12), .pin11(n74138_1_pin11), .pin10(n74138_1_pin10), .pin9(select_xor));
  _74138 u_74138_2 (
    .pin1(in_1[0]), .pin2(in_1[1]), .pin3(in_1[2]), .pin4(n74138_2_pin4), .pin5(n74138_2_pin4),
    .pin6(in_1[3]), .pin7(select_sx), .pin15(n74138_2_pin15), .pin14(n74138_2_pin14), .pin13(n74138_2_pin13),
    .pin12(set_cf), .pin11(clr_cf), .pin10(set_if), .pin9(clr_if));
  _7404 u_7404_1 (
    .pin1(n74138_1_pin15), .pin2(n7404_1_pin2), .pin3(n74138_1_pin14), .pin4(n7404_1_pin4),
    .pin5(n74138_1_pin13), .pin6(n7404_1_pin6), .pin13(n74138_1_pin10), .pin12(n7404_1_pin12),
    .pin11(n74138_1_pin11), .pin10(n7404_1_pin10), .pin9(n74138_1_pin12), .pin8(n7404_1_pin8));
  _7404 #(.ShowInternalStructure("true")) u_7404_2 (
    .pin1(select_xor), .pin2(n7404_2_pin2), .pin3(n74138_1_pin7), .pin4(n7404_2_pin4), .pin5(n74138_2_pin15),
    .pin6(n7404_2_pin6), .pin13(select_sx), .pin12(n7404_2_pin12), .pin11(n74138_2_pin13),
    .pin10(n7404_2_pin10), .pin9(n74138_2_pin14), .pin8(n7404_2_pin8));
  or or_1 (or_1_out, n7404_1_pin2, n7404_1_pin4, n7404_1_pin6);
  or or_2 (or_2_out, n7404_1_pin8, n7404_1_pin10, n7404_1_pin12);
  or or_3 (or_3_out, n7404_2_pin4, n7404_2_pin6);
  or or_4 (or_4_out, n7404_2_pin8, n7404_2_pin10);
  _7404 #(.ShowInternalStructure("true")) u_7404_3 (
    .pin1(or_1_out), .pin2(select_adder), .pin3(or_2_out), .pin4(select_logic), .pin5(or_3_out),
    .pin6(select_left_shifter), .pin9(or_4_out), .pin8(select_right_shifter));  // open: pin13, pin12, pin11, pin10
  or or_5 (save_acc, n7404_2_pin10, n7404_2_pin8, n7404_2_pin6, n7404_2_pin4, n7404_2_pin2, n7404_1_pin12, n7404_1_pin10, n7404_1_pin8, n7404_1_pin4, n7404_1_pin2, n7404_2_pin12);
  or or_6 (invert_lower_bus, n7404_2_pin8, n7404_2_pin4, n7404_1_pin12, n7404_1_pin10, n7404_1_pin6, n7404_1_pin4);
  or or_7 (execute_shift, n7404_1_pin10, n7404_2_pin6, n7404_2_pin10);
  // also tied to GND on the sheet: n74138_2_pin4
  // also tied to VCC on the sheet: n74138_1_pin6

  // Other names for the same wires on the sheet: invert_output = execute_shift
endmodule
